// Logisim project my_target.circ as structural Verilog: 27 circuits, main circuit ◇单周期RISC-V
module \单周期RISC_V  (
  input  IR1,
  input  IR2,
  input  IR3,
  output RegWrite,
  output MemWrite,
  output [31:0] PC,
  output [31:0] IR,
  output [31:0] RDin,
  output [31:0] MDin,
  output [31:0] LedData
);

  wire alu_1_equal, alu_1_out_6, and_1_out, and_2_out, and_3_out, and_4_out, and_5_out, and_6_out, branch,
       CLK, clock_1_out, comparator_1_eq, comparator_2_eq, comparator_2_lt, d_ff_1_q, DASB, ecall, Go, halt,
       IR1_t, IR2_t, IR3_t, IRA, IRB, IRC, MemToReg, nand_1_out, NextPC2Reg, not_1_out, not_2_out, not_3_out,
       not_4_out, not_5_out, riscv_probe_1_p2, riscv_probe_1_p3, RST, undriven, W1, W2, W3,
       \单周期硬布线控制器_1_alu_src , \单周期硬布线控制器_1_beq , \单周期硬布线控制器_1_blt , \单周期硬布线控制器_1_bne , \单周期硬布线控制器_1_jal ,
       \单周期硬布线控制器_1_jalr , \单周期硬布线控制器_1_s_type ;
  wire [1:0] priority_encoder_1_out;
  wire [3:0] \单周期硬布线控制器_1_alu_op ;
  wire [4:0] multiplexer_2_out, multiplexer_3_out;
  wire [11:0] multiplexer_4_out;
  wire [12:0] CNT_num;
  wire [15:0] multiplexer_10_out, \总周期数 ;
  wire [31:0] adder_2_out, adder_3_out, bit_extender_1_out, bit_extender_2_out, bit_extender_3_out,
       bit_extender_4_out, bit_extender_5_out, calc, LH_DIN, LH_DOUT, multiplexer_1_out, multiplexer_5_out,
       multiplexer_8_out, PC_4, R1, R2, SB, shifter_1_out, shifter_2_out, shifter_3_out, shifter_4_out,
       shifter_5_out;

  Button \u_继续运行  (.out(Go));
  Button _1 (.out(IRA));
  Button _2 (.out(IRB));
  Button _3 (.out(IRC));
  LED #(.active("true")) led_1 (.in(W1));
  LED #(.active("true")) led_2 (.in(W2));
  LED #(.active("true")) led_3 (.in(W3));
  Multiplexer #(.select(2), .width(32), .disabled("Z"), .enable("false")) multiplexer_1 (
    .in0(PC_4), .in1(calc), .in2(adder_3_out), .in3(adder_2_out), .out(multiplexer_1_out),
    .sel(priority_encoder_1_out));
  Hex_Digit_Display hex_digit_display_1 (.value(LedData[31:28]));  // open: dp
  Priority_Encoder #(.select(2), .disabled("Z")) priority_encoder_1 (
    .in0(1'b1), .in1(\单周期硬布线控制器_1_jalr ), .in2(\单周期硬布线控制器_1_jal ), .in3(branch), .out(priority_encoder_1_out));  // open: gs, en_out, en_in
  Register #(.width(32), .trigger("rising"), .Select("low")) u_PC (
    .D(multiplexer_1_out), .en(not_1_out), .Q(PC), .clk(CLK), .clr(RST));
  not not_1 (not_1_out, halt);
  not not_2 (not_2_out, halt);
  Hex_Digit_Display hex_digit_display_2 (.value(LedData[27:24]));  // open: dp
  Hex_Digit_Display hex_digit_display_3 (.value(LedData[23:20]));  // open: dp
  Adder #(.width(32)) adder_1 (.a(32'h4), .b(PC), .out(PC_4));  // open: cin, cout
  Counter #(.width(16), .max('hffff), .ongoal("wrap"), .trigger("rising"), .behavior("new")) counter_1 (
    .count(not_2_out), .Q(\总周期数 ), .clk(CLK));  // open: load, D, carry, clr, preset, down
  Hex_Digit_Display hex_digit_display_4 (.value(LedData[19:16]));  // open: dp
  Hex_Digit_Display hex_digit_display_5 (.value(LedData[15:12]));  // open: dp
  // RiscV_Probe riscv_probe_1: pin names not known; wires that end beside it: IR, riscv_probe_1_p2, riscv_probe_1_p3
  Hex_Digit_Display hex_digit_display_6 (.value(LedData[11:8]));  // open: dp
  Hex_Digit_Display hex_digit_display_7 (.value(LedData[7:4]));  // open: dp
  // Probe on \总周期数 
  or or_1 (NextPC2Reg, \单周期硬布线控制器_1_jal , \单周期硬布线控制器_1_jalr );
  ROM #(.addrWidth(10), .dataWidth(32), .Select("high")) rom_1 (.addr(PC[11:2]), .data(IR));
  Hex_Digit_Display hex_digit_display_8 (.value(LedData[3:0]));  // open: dp
  \单周期硬布线控制器  \u_单周期硬布线控制器_1  (
    .OP(IR[6:2]), .Funct({IR[30], IR[25], IR[14:12]}), .ALU_OP(\单周期硬布线控制器_1_alu_op ), .in_3(IR[21]),
    .uret(riscv_probe_1_p2), .MemToReg(MemToReg), .ecall(ecall), .MemWrite(MemWrite),
    .ALU_SRC(\单周期硬布线控制器_1_alu_src ), .RegWrite(RegWrite), .S_type(\单周期硬布线控制器_1_s_type ),
    .Beq(\单周期硬布线控制器_1_beq ), .Bne(\单周期硬布线控制器_1_bne ), .Jalr(\单周期硬布线控制器_1_jalr ), .JAL(\单周期硬布线控制器_1_jal ),
    .blt(\单周期硬布线控制器_1_blt ), .csrrsi(riscv_probe_1_p3), .dasb(DASB));  // open: U_type, csrrci
  Multiplexer #(.select(1), .width(5), .disabled("Z"), .enable("false")) multiplexer_2 (
    .in0(IR[19:15]), .in1(5'b10001), .out(multiplexer_2_out), .sel(ecall));
  or or_2 (IR1_t, IR1, IRA);
  Multiplexer #(.select(1), .width(5), .disabled("Z"), .enable("false")) multiplexer_3 (
    .in0(IR[24:20]), .in1(5'b01010), .out(multiplexer_3_out), .sel(ecall));
  Multiplexer #(.select(1), .width(12), .disabled("Z"), .enable("false")) multiplexer_4 (
    .in0(IR[31:20]), .in1({IR[31:25], IR[11:7]}), .out(multiplexer_4_out), .sel(\单周期硬布线控制器_1_s_type ));
  assign bit_extender_1_out = {{20{IR[31]}}, {IR[31], IR[7], IR[30:25], IR[11:8]}};  // Bit_Extender bit_extender_1
  assign bit_extender_2_out = {{12{IR[31]}}, {IR[31], IR[19:12], IR[20], IR[30:21]}};  // Bit_Extender bit_extender_2
  or or_3 (IR2_t, IR2, IRB);
  Regifile regifile_1 (
    .Din(RDin), .Clk(CLK), .R1(R1), .R2(R2), .WE(RegWrite), .W_num(IR[11:7]), .R1_num(multiplexer_2_out),
    .R2_num(multiplexer_3_out));
  assign bit_extender_3_out = {{20{multiplexer_4_out[11]}}, multiplexer_4_out};  // Bit_Extender bit_extender_3
  Shifter #(.width(32), .shift("ll")) shifter_1 (.in(bit_extender_1_out), .\dist (5'b00001), .out(shifter_1_out));
  Shifter #(.width(32), .shift("ll")) shifter_2 (.in(bit_extender_2_out), .\dist (5'b00001), .out(shifter_2_out));
  Multiplexer #(.select(1), .width(32), .disabled("Z"), .enable("false")) multiplexer_5 (
    .in0(R2), .in1(bit_extender_3_out), .out(multiplexer_5_out), .sel(\单周期硬布线控制器_1_alu_src ));
  or or_4 (IR3_t, IR3, IRC);
  Multiplexer #(.select(1), .width(32), .disabled("Z"), .enable("false")) multiplexer_6 (
    .in0(R2), .in1(SB), .out(MDin), .sel(DASB));
  Multiplexer #(.select(2), .width(32), .disabled("Z"), .enable("false")) multiplexer_7 (
    .in0(calc), .in1(LH_DOUT), .in2(PC_4), .in3(bit_extender_3_out), .out(RDin), .sel({NextPC2Reg, MemToReg}));
  Adder #(.width(32)) adder_2 (.a(shifter_1_out), .b(PC), .out(adder_2_out));  // open: cin, cout
  Adder #(.width(32)) adder_3 (.a(shifter_2_out), .b(PC), .out(adder_3_out));  // open: cin, cout
  not not_3 (not_3_out, alu_1_out_6);
  ALU alu_1 (
    .X(R1), .Y(multiplexer_5_out), .AluOP(\单周期硬布线控制器_1_alu_op ), .Equal(alu_1_equal), .Result(calc),
    .out_6(alu_1_out_6));  // open: Result_2, out_4
  and and_1 (and_1_out, \单周期硬布线控制器_1_blt , not_3_out);
  or or_5 (branch, and_1_out, and_2_out, and_3_out);
  and and_2 (and_2_out, \单周期硬布线控制器_1_beq , alu_1_equal);
  and and_3 (and_3_out, \单周期硬布线控制器_1_bne , ~alu_1_equal);  // AND_Gate
  RAM #(.addrWidth(10), .dataWidth(32), .bus("separate"), .Select("high")) ram_1 (
    .addr(calc[11:2]), .din(MDin), .data(LH_DIN), .str(MemWrite), .clk(CLK), .ld(undriven));  // open: sel, clr
  assign bit_extender_4_out = {{24{1'b0}}, R2[7:0]};  // Bit_Extender bit_extender_4
  Shifter #(.width(32), .shift("ll")) shifter_3 (.in(bit_extender_4_out), .\dist (5'b01000), .out(shifter_3_out));
  Shifter #(.width(32), .shift("ll")) shifter_4 (.in(bit_extender_4_out), .\dist (5'b10000), .out(shifter_4_out));
  Shifter #(.width(32), .shift("ll")) shifter_5 (.in(bit_extender_4_out), .\dist (5'b11000), .out(shifter_5_out));
  D_Flip_Flop #(.trigger("high"), .Pre_Clr_Positions("LEGACY"), .NegatePresetClear("false"), .enable("true"), .NewFFLayout("false")) d_ff_1 (.Q(d_ff_1_q));  // open: clk, D, Qn, preset, en, reset
  // Probe on 13'hc
  Comparator #(.width(32), .mode("twosComplement")) comparator_1 (
    .a(R1), .b(32'h22), .eq(comparator_1_eq));  // open: gt, lt
  Comparator #(.width(13), .mode("twosComplement")) comparator_2 (
    .a(CNT_num), .b(13'hc), .eq(comparator_2_eq), .lt(comparator_2_lt));  // open: gt
  Clock #(.highDuration(1), .lowDuration(1)) clock_1 (.out(clock_1_out));
  Multiplexer #(.select(2), .width(32), .disabled("Z"), .enable("false")) multiplexer_8 (
    .in0(bit_extender_4_out), .in1(shifter_3_out), .in2(shifter_4_out), .in3(shifter_5_out),
    .out(multiplexer_8_out), .sel(calc[1:0]));
  and and_4 (and_4_out, ecall, ~comparator_1_eq);  // AND_Gate
  and and_5 (and_5_out, comparator_1_eq, ecall);
  Counter #(.width(13), .max('h1fff), .ongoal("stay"), .trigger("rising"), .behavior("old")) counter_2 (
    .count(comparator_2_lt), .Q(CNT_num), .clk(clock_1_out));  // open: load, D, carry, clr, preset
  assign SB = multiplexer_8_out | LH_DIN;  // OR_Gate or_6, 32 bits wide
  Multiplexer #(.select(1), .width(1), .disabled("Z"), .enable("false")) multiplexer_9 (
    .in0(and_4_out), .in1(1'b0), .out(halt), .sel(Go));
  Register #(.width(32), .trigger("rising"), .Select("low")) register_1 (
    .D(R2), .en(and_5_out), .Q(LedData), .clk(CLK));  // open: clr
  nand nand_1 (nand_1_out, d_ff_1_q, comparator_2_eq);
  assign CLK = nand_1_out ? clock_1_out : 1'bz;  // Controlled_Buffer controlled_buffer_1
  Pull_Resistor #(.pull(1)) pull_resistor_1 (.node(CLK));
  not not_4 (not_4_out, IR[13]);
  not not_5 (not_5_out, IR[14]);
  and and_6 (and_6_out, IR[12], not_4_out, not_5_out, MemToReg);
  Multiplexer #(.select(1), .width(16), .disabled("Z"), .enable("false")) multiplexer_10 (
    .in0(LH_DIN[15:0]), .in1(LH_DIN[31:16]), .out(multiplexer_10_out), .sel(calc[1]));
  assign bit_extender_5_out = {{16{multiplexer_10_out[15]}}, multiplexer_10_out};  // Bit_Extender bit_extender_5
  Multiplexer #(.select(1), .width(32), .disabled("Z"), .enable("false")) multiplexer_11 (
    .in0(LH_DIN), .in1(bit_extender_5_out), .out(LH_DOUT), .sel(and_6_out));

  // Notes on the sheet:
  //   中断源
  //   中断等待指示
  //   数码管输出应该用寄存器锁存，否则显示数据只能一闪而过
  //   数码管输出
  //   指令探针
  //   指令存储器
  //   指令字
  //   contents of rom_1 (hex, n*v repeats v):
  //   100493 100006f 100493 200913 300993 100006f 100493 200913 300993 100006f 100493 200913 300993
  //   100006f 100493 200913 300993 3c8000ef 100413 100493 1f49493 900533 2200893 73 24d493 48463 fedff06f
  //   900533 2200893 73 100493 249493 900533 2200893 73 48463 fedff06f 100493 1f49493 900533 2200893 73
  //   4034d493 900533 2200893 73 4044d493 900533 2200893 73 4044d493 900533 2200893 73 4044d493 900533
  //   2200893 73 4044d493 900533 2200893 73 4044d493 900533 2200893 73 4044d493 900533 2200893 73 4044d493
  //   900533 2200893 73 100413 1f41993 41f9d993 433 c00913 300b13 140413 f47413 800293 100313 499993
  //   89e9b3 1300533 2200893 73 406282b3 fe0294e3 140413 f00f93 1f47433 1c41413 800293 100313 49d993
  //   89e9b3 1300533 2200893 73 406282b3 fe0294e3 1c45413 406b0b33 b0463 f95ff06f 2b3 fff2c293 829293
  //   ff2e293 500533 2200893 73 fff00413 493 84a023 140413 448493 84a023 140413 448493 84a023 140413
  //   448493 84a023 140413 448493 84a023 140413 448493 84a023 140413 448493 84a023 140413 448493 84a023
  //   140413 448493 84a023 140413 448493 84a023 140413 448493 84a023 140413 448493 84a023 140413 448493
  //   84a023 140413 448493 84a023 140413 448493 84a023 140413 448493 84a023 140413 448493 140413 433
  //   3c00493 42983 4aa03 149a2b3 28663 134a023 1442023 ffc48493 fe9412e3 800533 2200893 73 440413 3c00493
  //   fc9416e3 a00893 73 100293 300313 800493 849493 7648493 1449493 900533 2200893 73 800e13 4054d4b3
  //   4064d4b3 900533 2200893 73 fffe0e13 fe0e14e3 a00893 73 fff00293 7700493 849493 7748493 900533
  //   2200893 73 1000e13 54c4b3 900533 2200893 73 fffe0e13 fe0e16e3 a00893 73 313 1000e13 8400493 849493
  //   8348493 400913 891913 490913 849493 8248493 849493 8148493 891913 490913 891913 490913 932023
  //   12484b3 430313 fffe0e13 fe0e18e3 2000e13 313 31483 900533 2200893 73 230313 fffe0e13 fe0e14e3 a00893
  //   73 f00493 900533 2200893 73 fff48493 fe04d8e3 a00893 73 413 140413 800533 2200893 73 240413 800533
  //   2200893 73 340413 800533 2200893 73 440413 800533 2200893 73 540413 800533 2200893 73 640413 800533
  //   2200893 73 740413 800533 2200893 73 840413 800533 2200893 2200893 73 8067
  //   JAL
  //   JALR
  //   URET
  //   BLT
  //   CSR
  //   DASB
  //   Beq
  //   Bne
  //   MemToReg
  //   MemWrite
  //   AluOP
  //   AluSrcB
  //   RegWrite
  //   数据存储器
  //   为方便自动评测，需要输出PC，IR，寄存器堆写如数据RDin
  //   RAM写使能MemWrite、RAM写入数据MDin等信号
  //   控制位
  //   暂停节拍，不能为0
  //   戳工具置1进入计数暂停模式，ctrl+k时钟自动运行到对应节拍暂停
  //   ctrl+k关闭时钟连续运行，将控制位置零，进入单步调试模式调试
  //   用这个时钟源需要去掉电路中的其他时钟源
  //   可计数暂停的时钟源
endmodule

// 单周期硬布线控制器
module \单周期硬布线控制器  (
  input  [4:0] OP,
  input  [4:0] Funct,
  input  in_3,
  output [3:0] ALU_OP,
  output uret,
  output MemToReg,
  output ecall,
  output MemWrite,
  output ALU_SRC,
  output RegWrite,
  output S_type,
  output Beq,
  output Bne,
  output Jalr,
  output JAL,
  output blt,
  output csrrsi,
  output dasb,
  output U_type,
  output csrrci
);

  wire BGEU, \控制信号自动生成_1_ecall ;
  wire [3:0] \运算控制器自动生成_1_s0 ;

  and and_1 (BGEU, blt, Funct[1]);
  \运算控制器自动生成  \u_运算控制器自动生成_1  (
    .OP2(OP[0]), .OP3(OP[1]), .OP4(OP[2]), .OP5(OP[3]), .OP6(OP[4]), .F12(Funct[0]), .F13(Funct[1]),
    .F14(Funct[2]), .F25(Funct[3]), .F30(Funct[4]), .S0(\运算控制器自动生成_1_s0 [0]), .S1(\运算控制器自动生成_1_s0 [1]),
    .S2(\运算控制器自动生成_1_s0 [2]), .S3(\运算控制器自动生成_1_s0 [3]));
  \控制信号自动生成  \u_控制信号自动生成_1  (
    .OP2(OP[0]), .OP3(OP[1]), .MemToReg(MemToReg), .OP4(OP[2]), .OP5(OP[3]), .OP6(OP[4]), .F12(Funct[0]),
    .MemWrite(MemWrite), .F13(Funct[1]), .F14(Funct[2]), .F25(Funct[3]), .F30(Funct[4]), .ALU_SRC(ALU_SRC),
    .RegWrite(RegWrite), .ecall(\控制信号自动生成_1_ecall ), .S_Type(S_type), .BEQ(Beq), .BNE(Bne), .JALR(Jalr),
    .JAL(JAL), .blt(blt), .csrrsi(csrrsi), .dasb(dasb), .U_type(U_type), .csrrci(csrrci));
  Multiplexer #(.select(1), .width(4), .disabled("Z"), .enable("false")) multiplexer_1 (
    .in0(\运算控制器自动生成_1_s0 ), .in1(4'b1100), .out(ALU_OP), .sel(BGEU));
  and and_2 (uret, in_3, \控制信号自动生成_1_ecall );
  and and_3 (ecall, ~in_3, \控制信号自动生成_1_ecall );  // AND_Gate

  // Other names for the same wires on the sheet: BLT_ANY = blt; IR21 = in_3; OP_CODE[4:0] = OP

  // Notes on the sheet:
  //   运算器控制器，根据指令生成运算器功能选择信号
  //   控制信号生成，产生数据通路需要的其他控制信号
endmodule

// 运算器控制器
module \运算控制器自动生成  (
  input  OP2,
  input  OP3,
  input  OP4,
  input  OP5,
  input  OP6,
  input  F12,
  input  F13,
  input  F14,
  input  F25,
  input  F30,
  output S0,
  output S1,
  output S2,
  output S3
);

  wire and_1_out, and_2_out, and_3_out, and_4_out, and_5_out, and_6_out, and_7_out, and_8_out, and_9_out,
       and_10_out, and_11_out, and_12_out, and_13_out, and_14_out, and_15_out, and_16_out, and_17_out,
       and_18_out, and_19_out, and_20_out, and_21_out, and_22_out, and_23_out, and_24_out, and_25_out,
       and_26_out, and_27_out, and_28_out, and_29_out, and_30_out, and_31_out, and_32_out, and_33_out,
       and_34_out, and_35_out, and_36_out, and_37_out, and_38_out, and_39_out, and_40_out, and_41_out,
       and_42_out, and_43_out, and_44_out, BGE_TERM, LH_TERM, not_1_out, not_2_out, not_3_out, not_4_out,
       not_5_out, not_6_out, not_7_out, not_8_out, not_9_out, not_10_out, not_11_out, not_12_out, not_13_out,
       not_14_out, not_15_out, not_16_out, not_17_out, not_18_out, not_19_out, not_20_out, not_21_out,
       not_22_out, not_23_out, not_24_out, not_25_out, not_26_out, not_27_out, not_28_out, not_29_out,
       not_30_out, not_31_out, not_32_out, not_33_out, not_34_out, not_35_out, not_36_out, not_37_out,
       not_38_out, not_39_out, not_40_out, not_41_out, not_42_out, not_43_out, not_44_out, not_45_out,
       not_46_out, not_47_out, not_48_out, not_49_out, not_50_out, not_51_out, not_52_out, not_53_out,
       not_54_out, not_55_out, not_56_out, not_57_out, not_58_out, not_59_out, not_60_out, not_61_out,
       not_62_out, not_63_out, not_64_out, not_65_out, not_66_out, not_67_out, not_68_out, not_69_out,
       not_70_out, not_71_out, not_72_out, not_73_out, not_74_out, not_75_out, not_76_out, not_77_out,
       not_78_out, not_79_out, not_80_out, not_81_out, not_82_out, not_83_out, not_84_out, not_85_out,
       not_86_out, not_87_out, not_88_out, not_89_out, not_90_out, not_91_out, not_92_out, not_93_out,
       not_94_out, not_95_out, not_96_out, not_97_out, not_98_out, not_99_out, not_100_out, not_101_out,
       not_102_out, not_103_out, not_104_out, not_105_out, not_106_out, not_107_out, not_108_out,
       not_109_out, not_110_out, not_111_out, not_112_out, not_113_out, not_114_out, not_115_out,
       not_116_out, not_117_out, not_118_out, not_119_out, not_120_out, not_121_out, not_122_out,
       not_123_out, not_124_out, not_125_out, not_126_out, not_127_out, not_128_out, not_129_out,
       not_130_out, not_131_out, not_132_out, not_133_out, not_134_out, not_135_out, not_136_out,
       not_137_out, not_138_out, not_139_out, not_140_out, not_141_out, not_142_out, not_143_out,
       not_144_out, not_145_out, not_146_out, not_147_out, not_148_out, not_149_out, not_150_out,
       not_151_out, not_152_out, not_153_out, not_154_out, not_155_out, not_156_out, not_157_out,
       not_158_out, not_159_out, not_160_out, not_161_out, not_162_out, not_163_out, not_164_out,
       not_165_out, not_166_out, not_167_out, not_168_out, not_169_out, not_170_out, not_171_out,
       not_172_out, not_173_out, not_174_out, not_175_out, not_176_out, not_177_out, not_178_out,
       not_179_out, not_180_out, not_181_out, not_182_out, not_183_out, not_184_out, not_185_out,
       not_186_out, not_187_out, not_188_out, not_189_out, not_190_out, not_191_out, not_192_out,
       not_193_out, not_194_out, not_195_out, not_196_out, not_197_out, not_198_out, not_199_out,
       not_200_out, not_201_out, not_202_out, not_203_out, not_204_out, not_205_out, not_206_out,
       not_207_out, not_208_out, not_209_out, not_210_out, not_211_out, not_212_out, not_213_out,
       not_214_out, not_215_out, not_216_out, not_217_out, not_218_out, not_219_out, not_220_out,
       not_221_out, not_222_out, not_223_out, not_224_out, not_225_out, not_226_out, not_227_out,
       not_228_out, not_229_out, not_230_out, not_231_out, not_232_out, not_233_out, not_234_out,
       not_235_out, not_236_out, not_237_out, not_238_out, not_239_out, not_240_out, not_241_out,
       not_242_out, not_243_out, not_244_out, not_245_out, not_246_out, not_247_out, not_248_out,
       not_249_out, not_250_out, not_251_out, not_252_out, not_253_out, not_254_out, not_255_out,
       not_256_out, not_257_out, not_258_out, not_259_out, not_260_out, not_261_out, not_262_out,
       not_263_out, not_264_out, not_265_out, not_266_out, not_267_out, not_268_out, not_269_out,
       not_270_out, not_271_out, not_272_out, not_273_out, not_274_out;

  not not_1 (not_1_out, F30);
  not not_2 (not_2_out, F25);
  not not_3 (not_3_out, F14);
  not not_4 (not_4_out, F13);
  not not_5 (not_5_out, F12);
  not not_6 (not_6_out, OP6);
  not not_7 (not_7_out, OP3);
  not not_8 (not_8_out, OP2);
  not not_9 (not_9_out, F30);
  not not_10 (not_10_out, F25);
  not not_11 (not_11_out, OP6);
  not not_12 (not_12_out, OP3);
  not not_13 (not_13_out, OP2);
  not not_14 (not_14_out, F30);
  not not_15 (not_15_out, F25);
  not not_16 (not_16_out, F14);
  not not_17 (not_17_out, F12);
  not not_18 (not_18_out, OP6);
  not not_19 (not_19_out, OP3);
  not not_20 (not_20_out, OP2);
  not not_21 (not_21_out, F14);
  not not_22 (not_22_out, F13);
  not not_23 (not_23_out, F12);
  not not_24 (not_24_out, OP6);
  not not_25 (not_25_out, OP5);
  not not_26 (not_26_out, OP3);
  not not_27 (not_27_out, OP2);
  not not_28 (not_28_out, OP6);
  not not_29 (not_29_out, OP5);
  not not_30 (not_30_out, OP3);
  not not_31 (not_31_out, OP2);
  not not_32 (not_32_out, F13);
  not not_33 (not_33_out, F12);
  not not_34 (not_34_out, OP6);
  not not_35 (not_35_out, OP5);
  not not_36 (not_36_out, OP3);
  not not_37 (not_37_out, OP2);
  not not_38 (not_38_out, F14);
  not not_39 (not_39_out, F12);
  not not_40 (not_40_out, OP6);
  not not_41 (not_41_out, OP5);
  not not_42 (not_42_out, OP3);
  not not_43 (not_43_out, OP2);
  not not_44 (not_44_out, F25);
  not not_45 (not_45_out, F13);
  not not_46 (not_46_out, OP6);
  not not_47 (not_47_out, OP5);
  not not_48 (not_48_out, OP3);
  not not_49 (not_49_out, OP2);
  not not_50 (not_50_out, F14);
  not not_51 (not_51_out, F12);
  not not_52 (not_52_out, OP6);
  not not_53 (not_53_out, OP5);
  not not_54 (not_54_out, OP4);
  not not_55 (not_55_out, OP3);
  not not_56 (not_56_out, OP2);
  not not_57 (not_57_out, F14);
  not not_58 (not_58_out, F12);
  not not_59 (not_59_out, OP6);
  not not_60 (not_60_out, OP4);
  not not_61 (not_61_out, OP3);
  not not_62 (not_62_out, OP2);
  not not_63 (not_63_out, F14);
  not not_64 (not_64_out, F13);
  not not_65 (not_65_out, F12);
  not not_66 (not_66_out, OP6);
  not not_67 (not_67_out, OP4);
  not not_68 (not_68_out, OP3);
  not not_69 (not_69_out, OP2);
  not not_70 (not_70_out, F13);
  not not_71 (not_71_out, F12);
  not not_72 (not_72_out, OP4);
  not not_73 (not_73_out, OP3);
  not not_74 (not_74_out, OP2);
  not not_75 (not_75_out, F25);
  not not_76 (not_76_out, F14);
  not not_77 (not_77_out, F13);
  not not_78 (not_78_out, F12);
  not not_79 (not_79_out, OP6);
  not not_80 (not_80_out, OP3);
  not not_81 (not_81_out, OP2);
  not not_82 (not_82_out, F30);
  not not_83 (not_83_out, F25);
  not not_84 (not_84_out, OP6);
  not not_85 (not_85_out, OP3);
  not not_86 (not_86_out, OP2);
  not not_87 (not_87_out, F30);
  not not_88 (not_88_out, F25);
  not not_89 (not_89_out, F14);
  not not_90 (not_90_out, F12);
  not not_91 (not_91_out, OP6);
  not not_92 (not_92_out, OP3);
  not not_93 (not_93_out, OP2);
  not not_94 (not_94_out, OP6);
  not not_95 (not_95_out, OP5);
  not not_96 (not_96_out, OP3);
  not not_97 (not_97_out, OP2);
  not not_98 (not_98_out, F14);
  not not_99 (not_99_out, F12);
  not not_100 (not_100_out, OP6);
  not not_101 (not_101_out, OP5);
  not not_102 (not_102_out, OP3);
  not not_103 (not_103_out, OP2);
  not not_104 (not_104_out, F30);
  not not_105 (not_105_out, F25);
  not not_106 (not_106_out, F13);
  not not_107 (not_107_out, OP6);
  not not_108 (not_108_out, OP5);
  not not_109 (not_109_out, OP3);
  not not_110 (not_110_out, OP2);
  not not_111 (not_111_out, F14);
  not not_112 (not_112_out, F13);
  not not_113 (not_113_out, F12);
  not not_114 (not_114_out, OP4);
  not not_115 (not_115_out, OP3);
  not not_116 (not_116_out, OP2);
  not not_117 (not_117_out, F14);
  not not_118 (not_118_out, F13);
  not not_119 (not_119_out, OP4);
  not not_120 (not_120_out, OP3);
  not not_121 (not_121_out, OP2);
  not not_122 (not_122_out, F30);
  not not_123 (not_123_out, F25);
  not not_124 (not_124_out, F13);
  not not_125 (not_125_out, OP6);
  not not_126 (not_126_out, OP3);
  not not_127 (not_127_out, OP2);
  not not_128 (not_128_out, F13);
  not not_129 (not_129_out, F12);
  not not_130 (not_130_out, OP4);
  not not_131 (not_131_out, OP3);
  not not_132 (not_132_out, OP2);
  not not_133 (not_133_out, F30);
  not not_134 (not_134_out, F25);
  not not_135 (not_135_out, F14);
  not not_136 (not_136_out, F13);
  not not_137 (not_137_out, F12);
  not not_138 (not_138_out, OP6);
  not not_139 (not_139_out, OP3);
  not not_140 (not_140_out, OP2);
  not not_141 (not_141_out, F25);
  not not_142 (not_142_out, F14);
  not not_143 (not_143_out, F13);
  not not_144 (not_144_out, F12);
  not not_145 (not_145_out, OP6);
  not not_146 (not_146_out, OP3);
  not not_147 (not_147_out, OP2);
  not not_148 (not_148_out, F30);
  not not_149 (not_149_out, F25);
  not not_150 (not_150_out, OP6);
  not not_151 (not_151_out, OP3);
  not not_152 (not_152_out, OP2);
  not not_153 (not_153_out, F30);
  not not_154 (not_154_out, F25);
  not not_155 (not_155_out, F14);
  not not_156 (not_156_out, OP6);
  not not_157 (not_157_out, OP3);
  not not_158 (not_158_out, OP2);
  not not_159 (not_159_out, F14);
  not not_160 (not_160_out, F13);
  not not_161 (not_161_out, F12);
  not not_162 (not_162_out, OP6);
  not not_163 (not_163_out, OP5);
  not not_164 (not_164_out, OP3);
  not not_165 (not_165_out, OP2);
  not not_166 (not_166_out, OP6);
  not not_167 (not_167_out, OP5);
  not not_168 (not_168_out, OP3);
  not not_169 (not_169_out, OP2);
  not not_170 (not_170_out, F14);
  not not_171 (not_171_out, F12);
  not not_172 (not_172_out, OP6);
  not not_173 (not_173_out, OP5);
  not not_174 (not_174_out, OP4);
  not not_175 (not_175_out, OP3);
  not not_176 (not_176_out, OP2);
  not not_177 (not_177_out, F14);
  not not_178 (not_178_out, F12);
  not not_179 (not_179_out, OP6);
  not not_180 (not_180_out, OP4);
  not not_181 (not_181_out, OP3);
  not not_182 (not_182_out, OP2);
  not not_183 (not_183_out, F14);
  not not_184 (not_184_out, F13);
  not not_185 (not_185_out, F12);
  not not_186 (not_186_out, OP4);
  not not_187 (not_187_out, OP3);
  not not_188 (not_188_out, OP2);
  not not_189 (not_189_out, F14);
  not not_190 (not_190_out, F13);
  not not_191 (not_191_out, OP4);
  not not_192 (not_192_out, OP3);
  not not_193 (not_193_out, OP2);
  not not_194 (not_194_out, F14);
  not not_195 (not_195_out, OP6);
  not not_196 (not_196_out, OP5);
  not not_197 (not_197_out, OP3);
  not not_198 (not_198_out, OP2);
  not not_199 (not_199_out, F14);
  not not_200 (not_200_out, F13);
  not not_201 (not_201_out, F12);
  not not_202 (not_202_out, OP6);
  not not_203 (not_203_out, OP4);
  not not_204 (not_204_out, OP3);
  not not_205 (not_205_out, OP2);
  not not_206 (not_206_out, F30);
  not not_207 (not_207_out, F25);
  not not_208 (not_208_out, F12);
  not not_209 (not_209_out, OP6);
  not not_210 (not_210_out, OP3);
  not not_211 (not_211_out, OP2);
  not not_212 (not_212_out, F30);
  not not_213 (not_213_out, F25);
  not not_214 (not_214_out, F14);
  not not_215 (not_215_out, F12);
  not not_216 (not_216_out, OP6);
  not not_217 (not_217_out, OP3);
  not not_218 (not_218_out, OP2);
  not not_219 (not_219_out, F30);
  not not_220 (not_220_out, F25);
  not not_221 (not_221_out, F14);
  not not_222 (not_222_out, OP6);
  not not_223 (not_223_out, OP3);
  not not_224 (not_224_out, OP2);
  not not_225 (not_225_out, F12);
  not not_226 (not_226_out, OP6);
  not not_227 (not_227_out, OP5);
  not not_228 (not_228_out, OP3);
  not not_229 (not_229_out, OP2);
  not not_230 (not_230_out, F13);
  not not_231 (not_231_out, F12);
  not not_232 (not_232_out, OP6);
  not not_233 (not_233_out, OP5);
  not not_234 (not_234_out, OP3);
  not not_235 (not_235_out, OP2);
  not not_236 (not_236_out, F14);
  not not_237 (not_237_out, F12);
  not not_238 (not_238_out, OP6);
  not not_239 (not_239_out, OP5);
  not not_240 (not_240_out, OP3);
  not not_241 (not_241_out, OP2);
  not not_242 (not_242_out, F14);
  not not_243 (not_243_out, OP6);
  not not_244 (not_244_out, OP5);
  not not_245 (not_245_out, OP3);
  not not_246 (not_246_out, OP2);
  not not_247 (not_247_out, F13);
  not not_248 (not_248_out, F12);
  not not_249 (not_249_out, OP4);
  not not_250 (not_250_out, OP3);
  not not_251 (not_251_out, OP2);
  and and_1 (and_1_out, not_1_out, not_2_out, not_3_out, not_4_out, not_5_out, not_6_out, OP5, OP4, not_7_out, not_8_out);
  and and_2 (and_2_out, not_9_out, not_10_out, F14, F13, F12, not_11_out, OP5, OP4, not_12_out, not_13_out);
  and and_3 (and_3_out, not_14_out, not_15_out, not_16_out, F13, not_17_out, not_18_out, OP5, OP4, not_19_out, not_20_out);
  and and_4 (and_4_out, not_21_out, not_22_out, not_23_out, not_24_out, not_25_out, OP4, not_26_out, not_27_out);
  and and_5 (and_5_out, F14, F13, F12, not_28_out, not_29_out, OP4, not_30_out, not_31_out);
  and and_6 (and_6_out, F14, not_32_out, not_33_out, not_34_out, not_35_out, OP4, not_36_out, not_37_out);
  and and_7 (and_7_out, not_38_out, F13, not_39_out, not_40_out, not_41_out, OP4, not_42_out, not_43_out);
  and and_8 (and_8_out, F30, not_44_out, F14, not_45_out, F12, not_46_out, not_47_out, OP4, not_48_out, not_49_out);
  and and_9 (and_9_out, not_50_out, F13, not_51_out, not_52_out, not_53_out, not_54_out, not_55_out, not_56_out);
  and and_10 (and_10_out, not_57_out, F13, not_58_out, not_59_out, OP5, not_60_out, not_61_out, not_62_out);
  and and_11 (and_11_out, not_63_out, not_64_out, not_65_out, not_66_out, OP5, not_67_out, not_68_out, not_69_out);
  and and_12 (and_12_out, F14, not_70_out, not_71_out, OP6, OP5, not_72_out, not_73_out, not_74_out);
  and and_13 (and_13_out, F30, not_75_out, not_76_out, not_77_out, not_78_out, not_79_out, OP5, OP4, not_80_out, not_81_out);
  and and_14 (and_14_out, not_82_out, not_83_out, F14, F13, F12, not_84_out, OP5, OP4, not_85_out, not_86_out);
  and and_15 (and_15_out, not_87_out, not_88_out, not_89_out, F13, not_90_out, not_91_out, OP5, OP4, not_92_out, not_93_out);
  and and_16 (and_16_out, F14, F13, F12, not_94_out, not_95_out, OP4, not_96_out, not_97_out);
  and and_17 (and_17_out, not_98_out, F13, not_99_out, not_100_out, not_101_out, OP4, not_102_out, not_103_out);
  and and_18 (and_18_out, not_104_out, not_105_out, F14, not_106_out, F12, not_107_out, not_108_out, OP4, not_109_out, not_110_out);
  and and_19 (and_19_out, not_111_out, not_112_out, not_113_out, OP6, OP5, not_114_out, not_115_out, not_116_out);
  and and_20 (and_20_out, not_117_out, not_118_out, F12, OP6, OP5, not_119_out, not_120_out, not_121_out);
  and and_21 (and_21_out, not_122_out, not_123_out, F14, not_124_out, F12, not_125_out, OP5, OP4, not_126_out, not_127_out);
  and and_22 (and_22_out, F14, not_128_out, not_129_out, OP6, OP5, not_130_out, not_131_out, not_132_out);
  and and_23 (and_23_out, not_133_out, not_134_out, not_135_out, not_136_out, not_137_out, not_138_out, OP5, OP4, not_139_out, not_140_out);
  and and_24 (and_24_out, F30, not_141_out, not_142_out, not_143_out, not_144_out, not_145_out, OP5, OP4, not_146_out, not_147_out);
  and and_25 (and_25_out, not_148_out, not_149_out, F14, F13, F12, not_150_out, OP5, OP4, not_151_out, not_152_out);
  and and_26 (and_26_out, not_153_out, not_154_out, not_155_out, F13, F12, not_156_out, OP5, OP4, not_157_out, not_158_out);
  and and_27 (and_27_out, not_159_out, not_160_out, not_161_out, not_162_out, not_163_out, OP4, not_164_out, not_165_out);
  and and_28 (and_28_out, F14, F13, F12, not_166_out, not_167_out, OP4, not_168_out, not_169_out);
  and and_29 (and_29_out, not_170_out, F13, not_171_out, not_172_out, not_173_out, not_174_out, not_175_out, not_176_out);
  and and_30 (and_30_out, not_177_out, F13, not_178_out, not_179_out, OP5, not_180_out, not_181_out, not_182_out);
  and and_31 (and_31_out, not_183_out, not_184_out, not_185_out, OP6, OP5, not_186_out, not_187_out, not_188_out);
  and and_32 (and_32_out, not_189_out, not_190_out, F12, OP6, OP5, not_191_out, not_192_out, not_193_out);
  and and_33 (and_33_out, not_194_out, F13, F12, not_195_out, not_196_out, OP4, not_197_out, not_198_out);
  and and_34 (and_34_out, not_199_out, not_200_out, not_201_out, not_202_out, OP5, not_203_out, not_204_out, not_205_out);
  and and_35 (and_35_out, not_206_out, not_207_out, F14, F13, not_208_out, not_209_out, OP5, OP4, not_210_out, not_211_out);
  and and_36 (and_36_out, not_212_out, not_213_out, not_214_out, F13, not_215_out, not_216_out, OP5, OP4, not_217_out, not_218_out);
  and and_37 (and_37_out, not_219_out, not_220_out, not_221_out, F13, F12, not_222_out, OP5, OP4, not_223_out, not_224_out);
  and and_38 (and_38_out, F14, F13, not_225_out, not_226_out, not_227_out, OP4, not_228_out, not_229_out);
  and and_39 (and_39_out, F14, not_230_out, not_231_out, not_232_out, not_233_out, OP4, not_234_out, not_235_out);
  and and_40 (and_40_out, not_236_out, F13, not_237_out, not_238_out, not_239_out, OP4, not_240_out, not_241_out);
  and and_41 (and_41_out, not_242_out, F13, F12, not_243_out, not_244_out, OP4, not_245_out, not_246_out);
  and and_42 (and_42_out, F14, not_247_out, not_248_out, OP6, OP5, not_249_out, not_250_out, not_251_out);
  or or_1 (S0, BGE_TERM, and_44_out, and_1_out, and_2_out, and_3_out, and_4_out, and_5_out, and_6_out, LH_TERM, and_7_out, and_8_out, and_9_out, and_10_out, and_11_out, and_12_out, and_43_out, BGE_TERM);
  or or_2 (S1, and_13_out, and_14_out, and_15_out, and_16_out, and_17_out, BGE_TERM, and_18_out, and_19_out, and_20_out, and_21_out, and_22_out);
  or or_3 (S2, and_23_out, and_24_out, and_25_out, and_26_out, and_27_out, and_28_out, LH_TERM, and_29_out, and_30_out, and_31_out, and_32_out, and_33_out, and_34_out);
  or or_4 (S3, BGE_TERM, and_35_out, and_36_out, and_37_out, and_38_out, and_44_out, and_39_out, and_40_out, and_41_out, and_42_out, BGE_TERM);
  not not_252 (not_252_out, F25);
  not not_253 (not_253_out, F13);
  not not_254 (not_254_out, OP6);
  not not_255 (not_255_out, OP3);
  not not_256 (not_256_out, OP2);
  not not_257 (not_257_out, F30);
  not not_258 (not_258_out, F25);
  not not_259 (not_259_out, F13);
  not not_260 (not_260_out, F12);
  not not_261 (not_261_out, OP6);
  not not_262 (not_262_out, OP3);
  not not_263 (not_263_out, OP2);
  not not_264 (not_264_out, OP6);
  not not_265 (not_265_out, OP5);
  not not_266 (not_266_out, OP4);
  not not_267 (not_267_out, OP3);
  not not_268 (not_268_out, OP2);
  not not_269 (not_269_out, F14);
  not not_270 (not_270_out, F13);
  and and_43 (and_43_out, F30, not_252_out, F14, not_253_out, F12, OP5, not_254_out, OP4, not_255_out, not_256_out);
  and and_44 (and_44_out, not_257_out, not_258_out, F14, not_259_out, not_260_out, not_261_out, OP5, OP4, not_262_out, not_263_out);
  and and_45 (LH_TERM, not_269_out, not_270_out, F12, not_264_out, not_265_out, not_266_out, not_267_out, not_268_out);
  not not_271 (not_271_out, OP4);
  not not_272 (not_272_out, OP3);
  not not_273 (not_273_out, OP2);
  not not_274 (not_274_out, F13);
  and and_46 (BGE_TERM, not_271_out, not_272_out, not_273_out, not_274_out, OP6, OP5, F12, F14);
endmodule

// 控制信号生成
module \控制信号自动生成  (
  input  OP2,
  input  OP3,
  input  OP4,
  input  OP5,
  input  OP6,
  input  F12,
  input  F13,
  input  F14,
  input  F25,
  input  F30,
  output MemToReg,
  output MemWrite,
  output ALU_SRC,
  output RegWrite,
  output ecall,
  output S_Type,
  output BEQ,
  output BNE,
  output JALR,
  output JAL,
  output blt,
  output csrrsi,
  output dasb,
  output U_type,
  output csrrci
);

  wire and_1_out, and_3_out, and_4_out, and_5_out, and_6_out, and_7_out, and_8_out, and_9_out, and_10_out,
       and_11_out, and_12_out, and_13_out, and_14_out, and_15_out, and_16_out, and_17_out, and_18_out,
       and_25_out, and_30_out, and_31_out, BGE_TERM, LH_TERM, not_1_out, not_2_out, not_3_out, not_4_out,
       not_5_out, not_6_out, not_7_out, not_8_out, not_9_out, not_10_out, not_11_out, not_12_out, not_13_out,
       not_14_out, not_15_out, not_16_out, not_17_out, not_18_out, not_19_out, not_20_out, not_21_out,
       not_22_out, not_23_out, not_24_out, not_25_out, not_26_out, not_27_out, not_28_out, not_29_out,
       not_30_out, not_31_out, not_32_out, not_33_out, not_34_out, not_35_out, not_36_out, not_37_out,
       not_38_out, not_39_out, not_40_out, not_41_out, not_42_out, not_43_out, not_44_out, not_45_out,
       not_46_out, not_47_out, not_48_out, not_49_out, not_50_out, not_51_out, not_52_out, not_53_out,
       not_54_out, not_55_out, not_56_out, not_57_out, not_58_out, not_59_out, not_60_out, not_61_out,
       not_62_out, not_63_out, not_64_out, not_65_out, not_66_out, not_67_out, not_68_out, not_69_out,
       not_70_out, not_71_out, not_72_out, not_73_out, not_74_out, not_75_out, not_76_out, not_77_out,
       not_78_out, not_79_out, not_80_out, not_81_out, not_82_out, not_83_out, not_84_out, not_85_out,
       not_86_out, not_87_out, not_88_out, not_89_out, not_90_out, not_91_out, not_92_out, not_93_out,
       not_94_out, not_95_out, not_96_out, not_97_out, not_98_out, not_99_out, not_100_out, not_101_out,
       not_102_out, not_103_out, not_104_out, not_105_out, not_106_out, not_107_out, not_108_out,
       not_109_out, not_110_out, not_111_out, not_112_out, not_113_out, not_114_out, not_115_out,
       not_116_out, not_117_out, not_118_out, not_119_out, not_120_out, not_121_out, not_122_out,
       not_123_out, not_124_out, not_125_out, not_126_out, not_127_out, not_128_out, not_129_out,
       not_130_out, not_131_out, not_132_out, not_133_out, not_134_out, not_135_out, not_136_out,
       not_137_out, not_138_out, not_139_out, not_140_out, not_141_out, not_142_out, not_143_out,
       not_144_out, not_145_out, not_146_out, not_147_out, not_148_out, not_149_out, not_150_out,
       not_151_out, not_152_out, not_153_out, not_154_out, not_155_out, not_156_out, not_157_out,
       not_158_out, not_159_out, not_160_out, not_161_out, not_162_out, not_163_out, not_164_out, or_2_out;

  not not_1 (not_1_out, OP2);
  not not_2 (not_2_out, OP3);
  not not_3 (not_3_out, OP4);
  not not_4 (not_4_out, OP5);
  not not_5 (not_5_out, OP6);
  not not_6 (not_6_out, F12);
  not not_7 (not_7_out, F14);
  not not_8 (not_8_out, OP2);
  not not_9 (not_9_out, OP3);
  not not_10 (not_10_out, OP4);
  not not_11 (not_11_out, OP6);
  not not_12 (not_12_out, F12);
  not not_13 (not_13_out, F14);
  not not_14 (not_14_out, OP2);
  not not_15 (not_15_out, OP3);
  not not_16 (not_16_out, OP5);
  not not_17 (not_17_out, OP6);
  not not_18 (not_18_out, F12);
  not not_19 (not_19_out, F14);
  not not_20 (not_20_out, OP2);
  not not_21 (not_21_out, OP3);
  not not_22 (not_22_out, OP4);
  not not_23 (not_23_out, OP6);
  not not_24 (not_24_out, F12);
  not not_25 (not_25_out, F14);
  not not_26 (not_26_out, OP2);
  not not_27 (not_27_out, OP3);
  not not_28 (not_28_out, OP5);
  not not_29 (not_29_out, OP6);
  not not_30 (not_30_out, F12);
  not not_31 (not_31_out, OP2);
  not not_32 (not_32_out, OP3);
  not not_33 (not_33_out, OP5);
  not not_34 (not_34_out, OP6);
  not not_35 (not_35_out, F25);
  not not_36 (not_36_out, F30);
  not not_37 (not_37_out, OP2);
  not not_38 (not_38_out, OP3);
  not not_39 (not_39_out, OP5);
  not not_40 (not_40_out, OP6);
  not not_41 (not_41_out, F25);
  not not_42 (not_42_out, OP2);
  not not_43 (not_43_out, OP3);
  not not_44 (not_44_out, OP5);
  not not_45 (not_45_out, OP6);
  not not_46 (not_46_out, OP2);
  not not_47 (not_47_out, OP3);
  not not_48 (not_48_out, OP5);
  not not_49 (not_49_out, OP6);
  not not_50 (not_50_out, F12);
  not not_51 (not_51_out, F14);
  not not_52 (not_52_out, OP2);
  not not_53 (not_53_out, OP3);
  not not_54 (not_54_out, OP5);
  not not_55 (not_55_out, OP6);
  not not_56 (not_56_out, F12);
  not not_57 (not_57_out, OP2);
  not not_58 (not_58_out, OP3);
  not not_59 (not_59_out, OP5);
  not not_60 (not_60_out, OP6);
  not not_61 (not_61_out, F25);
  not not_62 (not_62_out, F30);
  not not_63 (not_63_out, OP2);
  not not_64 (not_64_out, OP3);
  not not_65 (not_65_out, OP6);
  not not_66 (not_66_out, F12);
  not not_67 (not_67_out, F13);
  not not_68 (not_68_out, F14);
  not not_69 (not_69_out, F25);
  not not_70 (not_70_out, OP2);
  not not_71 (not_71_out, OP3);
  not not_72 (not_72_out, OP5);
  not not_73 (not_73_out, OP6);
  not not_74 (not_74_out, F25);
  not not_75 (not_75_out, OP2);
  not not_76 (not_76_out, OP3);
  not not_77 (not_77_out, OP5);
  not not_78 (not_78_out, OP6);
  not not_79 (not_79_out, OP2);
  not not_80 (not_80_out, OP3);
  not not_81 (not_81_out, OP6);
  not not_82 (not_82_out, F25);
  not not_83 (not_83_out, F30);
  not not_84 (not_84_out, OP2);
  not not_85 (not_85_out, OP3);
  not not_86 (not_86_out, OP6);
  not not_87 (not_87_out, F25);
  not not_88 (not_88_out, F30);
  not not_89 (not_89_out, OP4);
  not not_90 (not_90_out, F12);
  not not_91 (not_91_out, F13);
  not not_92 (not_92_out, F14);
  not not_93 (not_93_out, OP4);
  not not_94 (not_94_out, OP2);
  not not_95 (not_95_out, OP3);
  not not_96 (not_96_out, F12);
  not not_97 (not_97_out, F13);
  not not_98 (not_98_out, F14);
  not not_99 (not_99_out, F25);
  not not_100 (not_100_out, F30);
  not not_101 (not_101_out, OP2);
  not not_102 (not_102_out, OP3);
  not not_103 (not_103_out, OP4);
  not not_104 (not_104_out, OP6);
  not not_105 (not_105_out, F12);
  not not_106 (not_106_out, F14);
  not not_107 (not_107_out, OP2);
  not not_108 (not_108_out, OP3);
  not not_109 (not_109_out, OP4);
  not not_110 (not_110_out, F12);
  not not_111 (not_111_out, F13);
  not not_112 (not_112_out, F14);
  not not_113 (not_113_out, OP2);
  not not_114 (not_114_out, OP3);
  not not_115 (not_115_out, OP4);
  not not_116 (not_116_out, F13);
  not not_117 (not_117_out, F14);
  not not_118 (not_118_out, OP3);
  not not_119 (not_119_out, OP4);
  not not_120 (not_120_out, F12);
  not not_121 (not_121_out, F13);
  not not_122 (not_122_out, F14);
  not not_123 (not_123_out, OP4);
  not not_124 (not_124_out, OP2);
  not not_125 (not_125_out, OP3);
  not not_126 (not_126_out, OP4);
  not not_127 (not_127_out, F12);
  not not_128 (not_128_out, OP3);
  not not_129 (not_129_out, OP2);
  not not_130 (not_130_out, OP2);
  not not_131 (not_131_out, OP3);
  not not_132 (not_132_out, OP4);
  not not_133 (not_133_out, OP6);
  not not_134 (not_134_out, F12);
  not not_135 (not_135_out, F13);
  not not_136 (not_136_out, F14);
  not not_137 (not_137_out, OP3);
  not not_138 (not_138_out, OP6);
  not not_139 (not_139_out, OP3);
  not not_140 (not_140_out, OP2);
  and and_1 (and_1_out, not_1_out, not_2_out, not_3_out, not_4_out, not_5_out, not_6_out, F13, not_7_out);
  and and_2 (MemWrite, not_8_out, not_9_out, not_10_out, OP5, not_11_out, not_12_out, not_13_out);
  and and_3 (and_3_out, not_14_out, not_15_out, not_16_out, not_17_out, not_18_out, F13, not_19_out);
  and and_4 (and_4_out, not_20_out, not_21_out, not_22_out, OP5, not_23_out, not_24_out, not_25_out);
  and and_5 (and_5_out, not_26_out, not_27_out, OP4, not_28_out, not_29_out, not_30_out);
  and and_6 (and_6_out, not_31_out, not_32_out, OP4, not_33_out, not_34_out, not_35_out, not_36_out);
  and and_7 (and_7_out, not_37_out, not_38_out, OP4, not_39_out, not_40_out, F14, not_41_out);
  and and_8 (and_8_out, not_42_out, not_43_out, OP4, not_44_out, not_45_out, F13);
  and and_9 (and_9_out, not_46_out, not_47_out, not_48_out, not_49_out, not_50_out, F13, not_51_out);
  and and_10 (and_10_out, not_52_out, not_53_out, OP4, not_54_out, not_55_out, not_56_out);
  and and_11 (and_11_out, not_57_out, not_58_out, OP4, not_59_out, not_60_out, not_61_out, not_62_out);
  and and_12 (and_12_out, not_63_out, not_64_out, OP4, not_65_out, not_66_out, not_67_out, not_68_out, not_69_out);
  and and_13 (and_13_out, not_70_out, not_71_out, OP4, not_72_out, not_73_out, F14, not_74_out);
  and and_14 (and_14_out, not_75_out, not_76_out, OP4, not_77_out, not_78_out, F13);
  and and_15 (and_15_out, not_79_out, not_80_out, OP4, not_81_out, F13, not_82_out, not_83_out);
  and and_16 (and_16_out, not_84_out, not_85_out, OP4, not_86_out, F12, not_141_out, not_87_out, not_88_out);
  not not_141 (not_141_out, F14);
  and and_17 (and_17_out, OP2, not_89_out, OP5, OP6, not_90_out, not_91_out, not_92_out);
  and and_18 (and_18_out, OP2, OP3, not_93_out, OP5, OP6);
  and and_19 (ecall, not_94_out, not_95_out, OP4, OP5, OP6, not_96_out, not_97_out, not_98_out, not_99_out, not_100_out);
  and and_20 (S_Type, not_101_out, not_102_out, not_103_out, OP5, not_104_out, not_105_out, not_106_out);
  and and_21 (BEQ, not_107_out, not_108_out, not_109_out, OP5, OP6, not_110_out, not_111_out, not_112_out);
  and and_22 (BNE, not_113_out, not_114_out, not_115_out, OP5, OP6, F12, not_116_out, not_117_out);
  and and_23 (JALR, OP2, not_118_out, not_119_out, OP5, OP6, not_120_out, not_121_out, not_122_out);
  and and_24 (JAL, OP2, OP3, not_123_out, OP5, OP6);
  and and_25 (and_25_out, not_124_out, not_125_out, not_126_out, OP5, OP6, F12, F13, F14);
  and and_26 (csrrsi, F14, F13, not_127_out, OP6, OP5, OP4, not_128_out, not_129_out);
  and and_27 (dasb, not_130_out, not_131_out, not_132_out, OP5, not_133_out, not_134_out, not_135_out, not_136_out);
  and and_28 (U_type, OP2, not_137_out, OP4, OP5, not_138_out);
  and and_29 (csrrci, F14, F13, F12, OP6, OP5, OP4, not_139_out, not_140_out);
  or or_1 (ALU_SRC, and_3_out, and_4_out, and_5_out, LH_TERM, and_6_out, and_7_out, and_8_out);
  or or_2 (or_2_out, and_9_out, and_10_out, and_11_out, and_12_out, and_13_out, and_30_out, and_14_out, and_15_out, and_16_out, and_17_out, and_18_out);
  or or_3 (MemToReg, and_1_out, LH_TERM);
  or or_4 (RegWrite, or_2_out, LH_TERM, and_31_out);
  not not_142 (not_142_out, F25);
  not not_143 (not_143_out, F13);
  not not_144 (not_144_out, OP6);
  not not_145 (not_145_out, OP3);
  not not_146 (not_146_out, OP2);
  not not_147 (not_147_out, F30);
  not not_148 (not_148_out, F25);
  not not_149 (not_149_out, F13);
  not not_150 (not_150_out, F12);
  not not_151 (not_151_out, OP6);
  not not_152 (not_152_out, OP3);
  not not_153 (not_153_out, OP2);
  not not_154 (not_154_out, OP6);
  not not_155 (not_155_out, OP5);
  not not_156 (not_156_out, OP4);
  not not_157 (not_157_out, OP3);
  not not_158 (not_158_out, OP2);
  not not_159 (not_159_out, F14);
  not not_160 (not_160_out, F13);
  or or_5 (blt, and_25_out, BGE_TERM);
  and and_30 (and_30_out, F30, not_142_out, F14, not_143_out, F12, OP5, not_144_out, OP4, not_145_out, not_146_out);
  and and_31 (and_31_out, not_147_out, not_148_out, F14, not_149_out, not_150_out, not_151_out, OP5, OP4, not_152_out, not_153_out);
  and and_32 (LH_TERM, not_159_out, not_160_out, F12, not_154_out, not_155_out, not_156_out, not_157_out, not_158_out);
  not not_161 (not_161_out, OP4);
  not not_162 (not_162_out, OP3);
  not not_163 (not_163_out, OP2);
  not not_164 (not_164_out, F13);
  and and_33 (BGE_TERM, not_161_out, not_162_out, not_163_out, not_164_out, OP6, OP5, F12, F14);
endmodule

// ALU
module ALU (
  input  [31:0] X,
  input  [31:0] Y,
  input  [3:0] AluOP,
  output out_4,
  output Equal,
  output out_6,
  output [31:0] Result,
  output [31:0] Result_2
);

  wire [0:0] comparator_1_lt, comparator_2_lt;
  wire [31:0] adder_1_out, AND_out, divider_1_out, divider_1_rem, multiplier_1_cout, multiplier_1_out,
       NOR_out, OR_out, shifter_1_out, shifter_2_out, shifter_3_out, subtractor_1_out, XOR_out;

  assign AND_out = X & Y;  // AND_Gate AND, 32 bits wide
  assign OR_out = X | Y;  // OR_Gate OR, 32 bits wide
  Shifter #(.width(32), .shift("ll")) shifter_1 (.in(X), .\dist (Y[4:0]), .out(shifter_1_out));
  Shifter #(.width(32), .shift("ar")) shifter_2 (.in(X), .\dist (Y[4:0]), .out(shifter_2_out));
  Shifter #(.width(32), .shift("lr")) shifter_3 (.in(X), .\dist (Y[4:0]), .out(shifter_3_out));
  Multiplier #(.width(32)) multiplier_1 (.a(X), .b(Y), .out(multiplier_1_out), .cout(multiplier_1_cout));  // open: cin
  Divider #(.width(32)) divider_1 (.a(X), .b(Y), .out(divider_1_out), .rem(divider_1_rem));  // open: upper
  Adder #(.width(32)) adder_1 (.a(X), .b(Y), .out(adder_1_out));  // open: cin, cout
  Subtractor #(.width(32)) subtractor_1 (.a(X), .b(Y), .out(subtractor_1_out));  // open: bin, bout
  assign XOR_out = X ^ Y;  // XOR_Gate XOR, 32 bits wide
  assign NOR_out = ~(X | Y);  // NOR_Gate NOR, 32 bits wide
  Comparator #(.width(32), .mode("twosComplement")) comparator_1 (
    .a(X), .b(Y), .eq(Equal), .lt(comparator_1_lt[0]));  // open: gt
  Comparator #(.width(32), .mode("unsigned")) comparator_2 (.a(X), .b(Y), .lt(comparator_2_lt[0]));  // open: gt, eq
  Multiplexer #(.select(4), .width(32), .disabled("Z"), .enable("false")) multiplexer_1 (
    .in0(shifter_1_out), .in1(shifter_2_out), .in2(shifter_3_out), .in3(multiplier_1_out),
    .in4(divider_1_out), .in5(adder_1_out), .in6(subtractor_1_out), .in7(AND_out), .in8(OR_out),
    .in9(XOR_out), .in10(NOR_out), .in11({{31{1'b0}}, comparator_1_lt[0]}),
    .in12({{31{1'b0}}, comparator_2_lt[0]}), .in13({32{1'b0}}), .in14({32{1'b0}}), .in15({32{1'b0}}),
    .out(Result), .sel(AluOP));
  Multiplexer #(.select(4), .width(32), .disabled("Z"), .enable("false")) multiplexer_2 (
    .in0({32{1'b0}}), .in1({32{1'b0}}), .in2({32{1'b0}}), .in3(multiplier_1_cout), .in4(divider_1_rem),
    .in5({32{1'b0}}), .in6({32{1'b0}}), .in7({32{1'b0}}), .in8({32{1'b0}}), .in9({32{1'b0}}),
    .in10({32{1'b0}}), .in11({32{1'b0}}), .in12({32{1'b0}}), .in13({32{1'b0}}), .in14({32{1'b0}}),
    .in15({32{1'b0}}), .out(Result_2), .sel(AluOP));
  Multiplexer #(.select(4), .width(1), .disabled("Z"), .enable("false")) multiplexer_3 (
    .in0(1'b0), .in1(1'b0), .in2(1'b0), .in3(1'b0), .in4(1'b0), .in5(1'b0), .in6(1'b0), .in7(1'b0),
    .in8(1'b0), .in9(1'b0), .in10(1'b0), .in11(comparator_1_lt[0]), .in12(comparator_2_lt[0]), .in13(1'b0),
    .in14(1'b0), .in15(1'b0), .out(out_6), .sel(AluOP));
  not not_1 (out_4, out_6);

  // Other names for the same wires on the sheet: Result2[31:0] = Result_2; S[3:0] = AluOP; tunnel = out_6;
  //   tunnel_t = out_4

  // Notes on the sheet:
  //   不要改变此引脚区域内容，也不要改变ALU封装形式
  //   输入引脚
  //   输出引脚
endmodule

module Regifile (
  input  [31:0] Din,
  input  Clk,
  input  WE,
  input  [4:0] R1_num,
  input  [4:0] W_num,
  input  [4:0] R2_num,
  output [31:0] R1,
  output [31:0] R2
);

  // RegisterFile registerfile_1: pin names not known; wires that end beside it: Din, Clk, WE, W_num, R1_num, R2_num, R1, R2
endmodule

module \气泡流水线  (
  output RegWrite,
  output MemWrite,
  output [31:0] IF_PC,
  output [31:0] ID_PC,
  output [31:0] EX_PC,
  output [31:0] M_PC,
  output [31:0] WB_PC,
  output [31:0] RDin,
  output [31:0] MDin,
  output [31:0] LedData
);

  wire alu_1_equal, alu_1_out_6, and_1_out, and_2_out, and_3_out, and_4_out, and_5_out, and_6_out, and_7_out,
       and_8_out, BGEU, branch, bubble, CLK, clock_1_out, comparator_1_eq, comparator_1_lt, comparator_2_eq,
       CSR, d_ff_1_q, DASB, DC, ecall, ex_mem_1_halt_2, ex_mem_1_memtoreg_2, ex_mem_1_regwrite_2, Go, halt,
       id_ex_1_alusrc_2, id_ex_1_memtoreg_2, id_ex_1_memwrite_2, id_ex_1_regwrite_2, IR1, IR2, IR3, JAL,
       JALR, jump, mem_wb_1_out_24, nand_1_out, not_1_out, not_2_out, not_3_out, not_4_out, or_1_out,
       or_2_out, or_5_out, RST, S_type, URET, W1, W2, W3, \单周期硬布线控制器_1_alu_src , \单周期硬布线控制器_1_memtoreg ,
       \单周期硬布线控制器_1_memwrite , \单周期硬布线控制器_1_regwrite , \寄存器使用情况_1_rs1_used , \寄存器使用情况_1_rs2_used ;
  wire [0:0] mem_wb_1_memtoreg_2;
  wire [1:0] priority_encoder_1_out;
  wire [3:0] id_ex_1_aluop_2, \单周期硬布线控制器_1_alu_op ;
  wire [4:0] ex_mem_1_writereg_num_2, id_ex_1_writereg_num_2, mem_wb_1_writereg_num_2, multiplexer_2_out,
       multiplexer_3_out;
  wire [8:0] \单周期硬布线控制器_1_beq ;
  wire [9:0] \ex_mem_1_指令译码信号_2 , \id_ex_1_指令译码信号_2 , \mem_wb_1_指令译码信号_2 ;
  wire [11:0] multiplexer_4_out;
  wire [12:0] CNT_num;
  wire [15:0] \LoadUse次数 , \总周期数 , \插入气泡数 , \无条件分支数 , \条件分支成功数 ;
  wire [31:0] adder_1_out, adder_2_out, adder_3_out, adder_4_out, alu_1_result, bit_extender_1_out,
       bit_extender_2_out, bit_extender_3_out, bit_extender_4_out, EX_IR, ex_mem_1_aluresult_2,
       ex_mem_1_reserved1_2, ex_mem_1_reserved2_2, ex_mem_1_writedata_2, id_ex_1_imm32_2, id_ex_1_immb_2,
       id_ex_1_immj_2, id_ex_1_rs1_2, id_ex_1_rs2_2, ID_IR, IF_IR, IR, MEM_IR, mem_wb_1_aluresult_2,
       mem_wb_1_memdata_2, multiplexer_1_out, multiplexer_5_out, multiplexer_7_out, R1, ram_1_data,
       regifile_1_r2, SB, shifter_1_out, shifter_2_out, shifter_3_out, shifter_4_out, shifter_5_out, WB_IR;

  Button \u_总复位  (.out(RST));
  Button _1 (.out(IR1));
  Button _2 (.out(IR2));
  Button _3 (.out(IR3));
  // Probe on \总周期数 
  // Probe on \总周期数 
  Button \u_继续运行  (.out(Go));
  LED #(.active("true")) led_1 (.in(W1));
  LED #(.active("true")) led_2 (.in(W2));
  LED #(.active("true")) led_3 (.in(W3));
  Multiplexer #(.select(2), .width(32), .disabled("Z"), .enable("false")) multiplexer_1 (
    .in0(adder_1_out), .in1(alu_1_result), .in2(adder_2_out), .in3(adder_3_out), .out(multiplexer_1_out),
    .sel(priority_encoder_1_out));
  not not_1 (not_1_out, or_1_out);
  or or_1 (or_1_out, DC, halt);
  Hex_Digit_Display hex_digit_display_1 (.value(LedData[31:28]));  // open: dp
  // Probe on IF_PC[19:0]
  // RiscV_Probe riscv_probe_1: pin names not known; wires that end beside it: IF_IR
  Register #(.width(32), .trigger("rising"), .Select("low")) PC (
    .D(multiplexer_1_out), .en(not_1_out), .Q(IF_PC), .clk(CLK), .clr(RST));
  Hex_Digit_Display hex_digit_display_2 (.value(LedData[23:20]));  // open: dp
  Hex_Digit_Display hex_digit_display_3 (.value(LedData[27:24]));  // open: dp
  // Probe on ID_PC[19:0]
  // RiscV_Probe riscv_probe_2: pin names not known; wires that end beside it: ID_IR
  Adder #(.width(32)) adder_1 (.a(IF_PC), .b(32'h4), .out(adder_1_out));  // open: cin, cout
  Hex_Digit_Display hex_digit_display_4 (.value(LedData[15:12]));  // open: dp
  Hex_Digit_Display hex_digit_display_5 (.value(LedData[19:16]));  // open: dp
  ROM #(.addrWidth(10), .dataWidth(32), .Select("low")) rom_1 (.addr(IF_PC[11:2]), .data(IF_IR));
  Hex_Digit_Display hex_digit_display_6 (.value(LedData[7:4]));  // open: dp
  Hex_Digit_Display hex_digit_display_7 (.value(LedData[11:8]));  // open: dp
  // Probe on EX_PC[19:0]
  // RiscV_Probe riscv_probe_3: pin names not known; wires that end beside it: EX_IR
  or or_2 (or_2_out, halt, DC);
  Hex_Digit_Display hex_digit_display_8 (.value(LedData[3:0]));  // open: dp
  IF_ID if_id_1 (
    .IR(IF_IR), .\气泡 (bubble), .IR_2(IR), .\EN_低电平有效 (or_2_out), .CLK(CLK), .PC_2(ID_PC), .PC(IF_PC),
    .IR_3(ID_IR));  // open: PredictJump, PredictJump_2
  // Probe on \总周期数 
  // Probe on M_PC[19:0]
  // RiscV_Probe riscv_probe_4: pin names not known; wires that end beside it: MEM_IR
  \数据相关监测  \u_数据相关监测_1  (
    .rs1_id(multiplexer_2_out), .rs2_id(multiplexer_3_out), .rs1_used(\寄存器使用情况_1_rs1_used ),
    .rs2_used(\寄存器使用情况_1_rs2_used ), .EX_RegWrite(id_ex_1_regwrite_2), .MEM_RegWrite(ex_mem_1_regwrite_2),
    .EX_MemToReg(id_ex_1_memtoreg_2), .EX_rd(id_ex_1_writereg_num_2), .MEM_rd(ex_mem_1_writereg_num_2),
    .DataCorrelate(DC));  // open: rs1Fwd, rs2Fwd, LoadUse
  \寄存器使用情况  \u_寄存器使用情况_1  (
    .OP(IR[6:2]), .Funct({IR[30], IR[25], IR[14:12]}), .rs1_used(\寄存器使用情况_1_rs1_used ),
    .rs2_used(\寄存器使用情况_1_rs2_used ));
  // Probe on \总周期数 
  // Probe on \无条件分支数 
  // Probe on \条件分支成功数 
  // Probe on \插入气泡数 
  // Probe on \LoadUse次数 
  // Probe on IF_PC[11:0]
  // Probe on WB_PC[19:0]
  // RiscV_Probe riscv_probe_5: pin names not known; wires that end beside it: WB_IR
  // Probe on ID_PC[11:0]
  // Probe on EX_PC[11:0]
  \单周期硬布线控制器  \u_单周期硬布线控制器_1  (
    .OP(IR[6:2]), .Funct({IR[30], IR[25], IR[14:12]}), .ALU_OP(\单周期硬布线控制器_1_alu_op ), .in_3(IR[21]),
    .uret(URET), .MemToReg(\单周期硬布线控制器_1_memtoreg ), .ecall(ecall), .MemWrite(\单周期硬布线控制器_1_memwrite ),
    .ALU_SRC(\单周期硬布线控制器_1_alu_src ), .RegWrite(\单周期硬布线控制器_1_regwrite ), .S_type(S_type),
    .Beq(\单周期硬布线控制器_1_beq [0]), .Bne(\单周期硬布线控制器_1_beq [1]), .Jalr(JALR), .JAL(JAL), .blt(BGEU), .csrrsi(CSR),
    .dasb(DASB));  // open: U_type, csrrci
  Multiplexer #(.select(1), .width(5), .disabled("Z"), .enable("false")) multiplexer_2 (
    .in0(IR[19:15]), .in1(5'b10001), .out(multiplexer_2_out), .sel(ecall));
  Multiplexer #(.select(1), .width(5), .disabled("Z"), .enable("false")) multiplexer_3 (
    .in0(IR[24:20]), .in1(5'b01010), .out(multiplexer_3_out), .sel(ecall));
  Multiplexer #(.select(1), .width(12), .disabled("Z"), .enable("false")) multiplexer_4 (
    .in0(IR[31:20]), .in1({IR[31:25], IR[11:7]}), .out(multiplexer_4_out), .sel(S_type));
  assign bit_extender_1_out = {{20{IR[31]}}, {IR[31], IR[7], IR[30:25], IR[11:8]}};  // Bit_Extender bit_extender_1
  assign bit_extender_2_out = {{12{IR[31]}}, {IR[31], IR[19:12], IR[20], IR[30:21]}};  // Bit_Extender bit_extender_2
  // Probe on M_PC[11:0]
  D_Flip_Flop #(.trigger("high"), .Pre_Clr_Positions("LEGACY"), .NegatePresetClear("false"), .enable("true"), .NewFFLayout("false")) d_ff_1 (.Q(d_ff_1_q));  // open: clk, D, Qn, preset, en, reset
  // Probe on 13'h5b4
  assign bit_extender_3_out = {{20{multiplexer_4_out[11]}}, multiplexer_4_out};  // Bit_Extender bit_extender_3
  // Probe on WB_PC[11:0]
  Comparator #(.width(13), .mode("twosComplement")) comparator_1 (
    .a(CNT_num), .b(13'h5b4), .eq(comparator_1_eq), .lt(comparator_1_lt));  // open: gt
  Clock #(.highDuration(1), .lowDuration(1)) clock_1 (.out(clock_1_out));
  not not_2 (not_2_out, CLK);
  Regifile regifile_1 (
    .Din(RDin), .Clk(not_2_out), .R1(R1), .R2(regifile_1_r2), .WE(RegWrite), .W_num(mem_wb_1_writereg_num_2),
    .R1_num(multiplexer_2_out), .R2_num(multiplexer_3_out));
  Shifter #(.width(32), .shift("ll")) shifter_1 (.in(bit_extender_1_out), .\dist (5'b00001), .out(shifter_1_out));
  Shifter #(.width(32), .shift("ll")) shifter_2 (.in(bit_extender_2_out), .\dist (5'b00001), .out(shifter_2_out));
  nand nand_1 (nand_1_out, d_ff_1_q, comparator_1_eq);
  Counter #(.width(13), .max('h1fff), .ongoal("stay"), .trigger("rising"), .behavior("old")) counter_1 (
    .count(comparator_1_lt), .Q(CNT_num), .clk(clock_1_out));  // open: load, D, carry, clr, preset
  Priority_Encoder #(.select(2), .disabled("Z")) priority_encoder_1 (
    .in0(1'b1), .in1(\id_ex_1_指令译码信号_2 [3]), .in2(branch), .in3(\id_ex_1_指令译码信号_2 [2]),
    .out(priority_encoder_1_out));  // open: gs, en_out, en_in
  assign CLK = nand_1_out ? clock_1_out : 1'bz;  // Controlled_Buffer controlled_buffer_1
  or or_3 (bubble, \id_ex_1_指令译码信号_2 [3], \id_ex_1_指令译码信号_2 [2], branch);
  Pull_Resistor #(.pull(1)) pull_resistor_1 (.node(CLK));
  or or_4 (branch, and_1_out, and_2_out, and_3_out);
  or or_5 (or_5_out, bubble, DC);
  ID_EX id_ex_1 (
    .PC(ID_PC), .RS1(R1), .RS2(regifile_1_r2), .IR(IR), .WriteReg_num(IR[11:7]),
    .ALUOP(\单周期硬布线控制器_1_alu_op ), .\气泡 (or_5_out), .PC_2(EX_PC), .RS1_2(id_ex_1_rs1_2),
    .RS2_2(id_ex_1_rs2_2), .IR_2(EX_IR), .RegWrite_2(id_ex_1_regwrite_2), .MemToReg_2(id_ex_1_memtoreg_2),
    .MemWrite_2(id_ex_1_memwrite_2), .ALuSrc_2(id_ex_1_alusrc_2), .WriteReg_num_2(id_ex_1_writereg_num_2),
    .RegWrite(\单周期硬布线控制器_1_regwrite ), .MemToReg(\单周期硬布线控制器_1_memtoreg ), .MemWrite(\单周期硬布线控制器_1_memwrite ),
    .ALuSrc(\单周期硬布线控制器_1_alu_src ), .ALUOP_2(id_ex_1_aluop_2), .CLK(CLK), .immb_2(id_ex_1_immb_2),
    .immb(shifter_1_out), .Imm32_2(id_ex_1_imm32_2), .Imm32(bit_extender_3_out),
    .\指令译码信号 ({ecall, \单周期硬布线控制器_1_beq [8], DASB, CSR, BGEU, URET, JALR, JAL, \单周期硬布线控制器_1_beq [1:0]}),
    .\指令译码信号_2 (\id_ex_1_指令译码信号_2 ), .immj(shifter_2_out), .immj_2(id_ex_1_immj_2), .\EN_低电平有效 (halt));  // open: rs2Fwd_2, rs1Fwd_2, PredictJump_2, rs2Fwd, rs1Fwd, PredictJump
  and and_1 (and_1_out, \id_ex_1_指令译码信号_2 [5], ~alu_1_out_6);  // AND_Gate
  and and_2 (and_2_out, \id_ex_1_指令译码信号_2 [0], alu_1_equal);
  and and_3 (and_3_out, \id_ex_1_指令译码信号_2 [1], ~alu_1_equal);  // AND_Gate
  Multiplexer #(.select(1), .width(32), .disabled("Z"), .enable("false")) multiplexer_5 (
    .in0(id_ex_1_rs2_2), .in1(id_ex_1_imm32_2), .out(multiplexer_5_out), .sel(id_ex_1_alusrc_2));
  not not_3 (not_3_out, comparator_2_eq);
  Adder #(.width(32)) adder_2 (.a(id_ex_1_immb_2), .b(EX_PC), .out(adder_2_out));  // open: cin, cout
  Adder #(.width(32)) adder_3 (.a(EX_PC), .b(id_ex_1_immj_2), .out(adder_3_out));  // open: cin, cout
  not not_4 (not_4_out, halt);
  ALU alu_1 (
    .X(id_ex_1_rs1_2), .Y(multiplexer_5_out), .AluOP(id_ex_1_aluop_2), .Equal(alu_1_equal),
    .Result(alu_1_result), .out_6(alu_1_out_6));  // open: Result_2, out_4
  and and_4 (and_4_out, not_3_out, \id_ex_1_指令译码信号_2 [9]);
  Register #(.width(32), .trigger("rising"), .Select("low")) register_1 (
    .D(id_ex_1_rs2_2), .en(and_5_out), .Q(LedData), .clk(CLK));  // open: clr
  and and_5 (and_5_out, comparator_2_eq, \id_ex_1_指令译码信号_2 [9]);
  Counter #(.width(16), .max('hffff), .ongoal("wrap"), .trigger("rising"), .behavior("old")) counter_2 (
    .count(not_4_out), .Q(\总周期数 ), .clk(CLK));  // open: load, D, carry, clr, preset
  Comparator #(.width(32), .mode("twosComplement")) comparator_2 (
    .a(id_ex_1_rs1_2), .b(32'h22), .eq(comparator_2_eq));  // open: gt, lt
  and and_6 (and_6_out, not_4_out, jump);
  Counter #(.width(16), .max('hffff), .ongoal("wrap"), .trigger("rising"), .behavior("old")) counter_3 (
    .count(and_6_out), .Q(\无条件分支数 ), .clk(CLK));  // open: load, D, carry, clr, preset
  EX_MEM ex_mem_1 (
    .PC(EX_PC), .IR(EX_IR), .WriteReg_num(id_ex_1_writereg_num_2), .\气泡 (1'b0), .PC_2(M_PC), .IR_2(MEM_IR),
    .RegWrite_2(ex_mem_1_regwrite_2), .MemToReg_2(ex_mem_1_memtoreg_2), .MemWrite_2(MemWrite),
    .WriteReg_num_2(ex_mem_1_writereg_num_2), .RegWrite(id_ex_1_regwrite_2), .MemToReg(id_ex_1_memtoreg_2),
    .MemWrite(id_ex_1_memwrite_2), .\EN_低电平有效 (halt), .CLK(CLK), .Reserved1_2(ex_mem_1_reserved1_2),
    .Reserved1(id_ex_1_immb_2), .\指令译码信号 (\id_ex_1_指令译码信号_2 ), .\指令译码信号_2 (\ex_mem_1_指令译码信号_2 ),
    .Reserved2(id_ex_1_immj_2), .Reserved2_2(ex_mem_1_reserved2_2), .WriteData(id_ex_1_rs2_2),
    .WriteData_2(ex_mem_1_writedata_2), .AluResult(alu_1_result), .AluResult_2(ex_mem_1_aluresult_2),
    .halt(and_4_out), .halt_2(ex_mem_1_halt_2));
  and and_7 (and_7_out, not_4_out, branch);
  assign bit_extender_4_out = {{24{1'b0}}, ex_mem_1_writedata_2[7:0]};  // Bit_Extender bit_extender_4
  Counter #(.width(16), .max('hffff), .ongoal("wrap"), .trigger("rising"), .behavior("old")) counter_4 (
    .count(and_7_out), .Q(\条件分支成功数 ), .clk(CLK));  // open: load, D, carry, clr, preset
  Multiplexer #(.select(1), .width(32), .disabled("Z"), .enable("false")) multiplexer_6 (
    .in0(ex_mem_1_writedata_2), .in1(SB), .out(MDin), .sel(\ex_mem_1_指令译码信号_2 [7]));
  Shifter #(.width(32), .shift("ll")) shifter_3 (.in(bit_extender_4_out), .\dist (5'b01000), .out(shifter_3_out));
  Shifter #(.width(32), .shift("ll")) shifter_4 (.in(bit_extender_4_out), .\dist (5'b10000), .out(shifter_4_out));
  Shifter #(.width(32), .shift("ll")) shifter_5 (.in(bit_extender_4_out), .\dist (5'b11000), .out(shifter_5_out));
  and and_8 (and_8_out, not_4_out, DC);
  RAM #(.addrWidth(10), .dataWidth(32), .bus("separate"), .Select("low")) ram_1 (
    .addr(ex_mem_1_aluresult_2[11:2]), .din(MDin), .data(ram_1_data), .str(MemWrite), .sel(1'b0), .clk(CLK),
    .ld(1'b1));  // open: clr
  Multiplexer #(.select(2), .width(32), .disabled("Z"), .enable("false")) multiplexer_7 (
    .in0(bit_extender_4_out), .in1(shifter_3_out), .in2(shifter_4_out), .in3(shifter_5_out),
    .out(multiplexer_7_out), .sel(ex_mem_1_aluresult_2[1:0]));
  Counter #(.width(16), .max('hffff), .ongoal("wrap"), .trigger("rising"), .behavior("old")) counter_5 (
    .count(and_8_out), .Q(\插入气泡数 ), .clk(CLK));  // open: load, D, carry, clr, preset
  MEM_WB mem_wb_1 (
    .PC(M_PC), .IR(MEM_IR), .WriteReg_num(ex_mem_1_writereg_num_2), .\气泡 (1'b0), .PC_2(WB_PC), .IR_2(WB_IR),
    .RegWrite_2(RegWrite), .MemToReg_2(mem_wb_1_memtoreg_2[0]), .WriteReg_num_2(mem_wb_1_writereg_num_2),
    .RegWrite(ex_mem_1_regwrite_2), .MemToReg(ex_mem_1_memtoreg_2), .\EN_低电平有效 (halt), .CLK(CLK),
    .Reserved1(ex_mem_1_reserved1_2), .\指令译码信号 (\ex_mem_1_指令译码信号_2 ), .\指令译码信号_2 (\mem_wb_1_指令译码信号_2 ),
    .Reserved2(ex_mem_1_reserved2_2), .MemData(ram_1_data), .MemData_2(mem_wb_1_memdata_2),
    .AluResult(ex_mem_1_aluresult_2), .AluResult_2(mem_wb_1_aluresult_2), .halt(ex_mem_1_halt_2),
    .out_24(mem_wb_1_out_24));  // open: Reserved1_2, Reserved2_2
  assign SB = multiplexer_7_out | ram_1_data;  // OR_Gate or_6, 32 bits wide
  Multiplexer #(.select(1), .width(1), .disabled("Z"), .enable("false")) multiplexer_8 (
    .in0(mem_wb_1_out_24), .in1(1'b0), .out(halt), .sel(Go));
  Adder #(.width(32)) adder_4 (.a(32'h4), .b(WB_PC), .out(adder_4_out));  // open: cin, cout
  or or_7 (jump, \mem_wb_1_指令译码信号_2 [2], \mem_wb_1_指令译码信号_2 [3]);
  Multiplexer #(.select(2), .width(32), .disabled("Z"), .enable("false")) multiplexer_9 (
    .in0(mem_wb_1_aluresult_2), .in1(mem_wb_1_memdata_2), .in2(adder_4_out), .out(RDin),
    .sel({jump, mem_wb_1_memtoreg_2[0]}));  // open: in3
  Multiplexer #(.select(1), .width(32), .disabled("Z"), .enable("false")) multiplexer_10 (
    .in0(mem_wb_1_aluresult_2), .in1(adder_4_out), .sel(\mem_wb_1_指令译码信号_2 [2]));  // open: out

  // Other names for the same wires on the sheet: rd[4:0] = IR[11:7]; MEM_PC[31:0] = M_PC

  // Notes on the sheet:
  //   中断源
  //   时空图监测，可删除
  //   中断等待指示
  //   数码管输出
  //   contents of rom_1 (hex, n*v repeats v):
  //   100493 100006f 100493 200913 300993 100006f 100493 200913 300993 100006f 100493 200913 300993
  //   100006f 100493 200913 300993 398000ef 100413 100493 1f49493 900533 2200893 73 24d493 48463 fedff06f
  //   900533 2200893 73 100493 249493 900533 2200893 73 48463 fedff06f 100493 1f49493 900533 2200893 73
  //   4034d493 900533 2200893 73 4044d493 900533 2200893 73 4044d493 900533 2200893 73 4044d493 900533
  //   2200893 73 4044d493 900533 2200893 73 4044d493 900533 2200893 73 4044d493 900533 2200893 73 4044d493
  //   900533 2200893 73 100413 1f41993 41f9d993 433 c00913 300b13 140413 f47413 800293 100313 499993
  //   89e9b3 1300533 2200893 73 406282b3 fe0294e3 140413 f00f93 1f47433 1c41413 800293 100313 49d993
  //   89e9b3 1300533 2200893 73 406282b3 fe0294e3 1c45413 406b0b33 b0463 f95ff06f 2b3 fff2c293 829293
  //   ff2e293 500533 2200893 73 fff00413 493 84a023 140413 448493 84a023 140413 448493 84a023 140413
  //   448493 84a023 140413 448493 84a023 140413 448493 84a023 140413 448493 84a023 140413 448493 84a023
  //   140413 448493 84a023 140413 448493 84a023 140413 448493 84a023 140413 448493 84a023 140413 448493
  //   84a023 140413 448493 84a023 140413 448493 84a023 140413 448493 84a023 140413 448493 140413 433
  //   3c00493 42983 4aa03 149a2b3 28663 134a023 1442023 ffc48493 fe9412e3 800533 2200893 73 440413 3c00493
  //   fc9416e3 a00893 73 100293 300313 800493 849493 7648493 1449493 900533 2200893 73 800e13 54d4b3
  //   64d4b3 900533 2200893 73 fffe0e13 fe0e14e3 a00893 73 fff00293 313 1900413 841413 9700493 940533
  //   2200893 73 5484b3 494b313 fe0306e3 a00893 73 313 2000e13 493 100913 930023 900533 2200893 73 12484b3
  //   130313 fffe0e13 fe0e12e3 800e13 313 32483 900533 2200893 73 430313 fffe0e13 fe0e14e3 a00893 73
  //   ff100493 900533 2200893 73 148493 fe04c8e3 a00893 73 413 140413 800533 2200893 73 240413 800533
  //   2200893 73 340413 800533 2200893 73 440413 800533 2200893 73 540413 800533 2200893 73 640413 800533
  //   2200893 73 740413 800533 2200893 73 840413 800533 2200893 2200893 73 8067
  //   指令字
  //   JALR
  //   URET
  //   b型
  //   j型
  //   控制位
  //   Beq
  //   Bne
  //   MemToReg
  //   MemWrite
  //   AluOP
  //   AluSrcB
  //   RegWrite
  //   流水调试日志用
  //   暂停节拍，不能为0
  //   戳工具置1进入计数暂停模式，ctrl+k时钟自动运行到对应节拍暂停
  //   ctrl+k关闭时钟连续运行，将控制位置零，进入单步调试模式调试
  //   可计数暂停的时钟源
  //   为方便自动评测，需要输出流水线各段保存的PC值，注意是PC不是PC+4，另外ID段寄存器写入信息，Mem段内存写入信息也要输出
endmodule

module \理想流水线  (
  output RegWrite,
  output MemWrite,
  output [31:0] IF_PC,
  output [31:0] ID_PC,
  output [31:0] EX_PC,
  output [31:0] M_PC,
  output [31:0] WB_PC,
  output [31:0] RDin,
  output [31:0] MDin,
  output [31:0] LedData
);

  wire alu_1_equal, alu_1_out_6, and_1_out, and_2_out, and_3_out, and_4_out, and_5_out, and_6_out, BGEU,
       branch, CLK, clock_1_out, comparator_1_eq, comparator_1_lt, comparator_3_eq, CSR, d_ff_1_q, DASB,
       ecall, ex_mem_1_memtoreg_2, ex_mem_1_regwrite_2, Exit_EX_q, Exit_MEM_Out, Go, halt, HaltNext,
       id_ex_1_alusrc_2, id_ex_1_memtoreg_2, id_ex_1_memwrite_2, id_ex_1_regwrite_2, ID_Exit, ID_Print, IR1,
       IR2, IR3, JAL, JALR, jump, nand_1_out, not_1_out, not_2_out, not_3_out, or_1_out, RST, S_type, URET,
       W1, W2, W3, \单周期硬布线控制器_1_alu_src , \单周期硬布线控制器_1_memtoreg , \单周期硬布线控制器_1_memwrite ,
       \单周期硬布线控制器_1_regwrite ;
  wire [0:0] mem_wb_1_memtoreg_2;
  wire [1:0] \单周期硬布线控制器_1_beq ;
  wire [3:0] id_ex_1_aluop_2, \单周期硬布线控制器_1_alu_op ;
  wire [4:0] ex_mem_1_writereg_num_2, id_ex_1_writereg_num_2, mem_wb_1_writereg_num_2, multiplexer_3_out,
       multiplexer_4_out;
  wire [9:0] \ex_mem_1_指令译码信号_2 , \id_ex_1_指令译码信号_2 , \mem_wb_1_指令译码信号_2 ;
  wire [11:0] multiplexer_5_out;
  wire [12:0] CNT_num;
  wire [15:0] \LoadUse次数 , \总周期数 , \插入气泡数 , \无条件分支数 , \条件分支成功数 ;
  wire [31:0] adder_1_out, adder_2_out, adder_3_out, adder_4_out, adder_5_out, alu_1_result,
       bit_extender_1_out, bit_extender_2_out, bit_extender_3_out, bit_extender_4_out, EX_IR,
       ex_mem_1_aluresult_2, ex_mem_1_reserved1_2, ex_mem_1_reserved2_2, ex_mem_1_writedata_2,
       id_ex_1_imm32_2, id_ex_1_immb_2, id_ex_1_immj_2, id_ex_1_rs1_2, id_ex_1_rs2_2, ID_IR, ID_R2, IF_IR,
       IR, MEM_IR, mem_wb_1_aluresult_2, mem_wb_1_memdata_2, multiplexer_1_out, multiplexer_2_out,
       multiplexer_6_out, multiplexer_8_out, multiplexer_10_out, R1, ram_1_data, SB, shifter_1_out,
       shifter_2_out, shifter_3_out, shifter_4_out, shifter_5_out, WB_IR;

  Button \u_总复位  (.out(RST));
  Button _1 (.out(IR1));
  Button _2 (.out(IR2));
  Button _3 (.out(IR3));
  // Probe on \总周期数 
  // Probe on \总周期数 
  Button \u_继续运行  (.out(Go));
  LED #(.active("true")) led_1 (.in(W1));
  LED #(.active("true")) led_2 (.in(W2));
  LED #(.active("true")) led_3 (.in(W3));
  not not_1 (not_1_out, halt);
  Hex_Digit_Display hex_digit_display_1 (.value(LedData[31:28]));  // open: dp
  // Probe on IF_PC[19:0]
  // RiscV_Probe riscv_probe_1: pin names not known; wires that end beside it: IF_IR
  Register #(.width(32), .trigger("rising"), .Select("low")) PC (
    .D(multiplexer_2_out), .en(not_1_out), .Q(IF_PC), .clk(CLK), .clr(RST));
  Hex_Digit_Display hex_digit_display_2 (.value(LedData[27:24]));  // open: dp
  Hex_Digit_Display hex_digit_display_3 (.value(LedData[23:20]));  // open: dp
  // Probe on ID_PC[19:0]
  // RiscV_Probe riscv_probe_2: pin names not known; wires that end beside it: ID_IR
  Adder #(.width(32)) adder_1 (.a(IF_PC), .b(32'h4), .out(adder_1_out));  // open: cin, cout
  Multiplexer #(.select(1), .width(32), .disabled("Z"), .enable("false")) multiplexer_1 (
    .in0(adder_4_out), .in1(multiplexer_10_out), .out(multiplexer_1_out), .sel(jump));
  Hex_Digit_Display hex_digit_display_4 (.value(LedData[19:16]));  // open: dp
  Hex_Digit_Display hex_digit_display_5 (.value(LedData[15:12]));  // open: dp
  Multiplexer #(.select(1), .width(32), .disabled("Z"), .enable("false")) multiplexer_2 (
    .in0(adder_1_out), .in1(multiplexer_1_out), .out(multiplexer_2_out), .sel(or_1_out));
  or or_1 (or_1_out, jump, branch);
  Hex_Digit_Display hex_digit_display_6 (.value(LedData[7:4]));  // open: dp
  Hex_Digit_Display hex_digit_display_7 (.value(LedData[11:8]));  // open: dp
  // Probe on EX_PC[19:0]
  // RiscV_Probe riscv_probe_3: pin names not known; wires that end beside it: EX_IR
  ROM #(.addrWidth(10), .dataWidth(32), .Select("low")) rom_1 (.addr(IF_PC[11:2]), .data(IF_IR));
  Hex_Digit_Display hex_digit_display_8 (.value(LedData[3:0]));  // open: dp
  IF_ID if_id_1 (
    .IR(IF_IR), .IR_2(IR), .\EN_低电平有效 (halt), .CLK(CLK), .PC_2(ID_PC), .PC(IF_PC), .IR_3(ID_IR));  // open: PredictJump, 气泡, PredictJump_2
  // Probe on \总周期数 
  // Probe on M_PC[19:0]
  // RiscV_Probe riscv_probe_4: pin names not known; wires that end beside it: MEM_IR
  // Probe on \总周期数 
  // Probe on \无条件分支数 
  // Probe on \条件分支成功数 
  // Probe on \插入气泡数 
  // Probe on \LoadUse次数 
  // Probe on IF_PC[11:0]
  // Probe on WB_PC[19:0]
  // RiscV_Probe riscv_probe_5: pin names not known; wires that end beside it: WB_IR
  // Probe on ID_PC[11:0]
  // Probe on EX_PC[11:0]
  \单周期硬布线控制器  \u_单周期硬布线控制器_1  (
    .OP(IR[6:2]), .Funct({IR[30], IR[25], IR[14:12]}), .ALU_OP(\单周期硬布线控制器_1_alu_op ), .in_3(IR[21]),
    .uret(URET), .MemToReg(\单周期硬布线控制器_1_memtoreg ), .ecall(ecall), .MemWrite(\单周期硬布线控制器_1_memwrite ),
    .ALU_SRC(\单周期硬布线控制器_1_alu_src ), .RegWrite(\单周期硬布线控制器_1_regwrite ), .S_type(S_type),
    .Beq(\单周期硬布线控制器_1_beq [0]), .Bne(\单周期硬布线控制器_1_beq [1]), .Jalr(JALR), .JAL(JAL), .blt(BGEU), .csrrsi(CSR),
    .dasb(DASB));  // open: U_type, csrrci
  Multiplexer #(.select(1), .width(5), .disabled("Z"), .enable("false")) multiplexer_3 (
    .in0(IR[19:15]), .in1(5'b10001), .out(multiplexer_3_out), .sel(ecall));
  Multiplexer #(.select(1), .width(5), .disabled("Z"), .enable("false")) multiplexer_4 (
    .in0(IR[24:20]), .in1(5'b01010), .out(multiplexer_4_out), .sel(ecall));
  Multiplexer #(.select(1), .width(12), .disabled("Z"), .enable("false")) multiplexer_5 (
    .in0(IR[31:20]), .in1({IR[31:25], IR[11:7]}), .out(multiplexer_5_out), .sel(S_type));
  assign bit_extender_1_out = {{20{IR[31]}}, {IR[31], IR[7], IR[30:25], IR[11:8]}};  // Bit_Extender bit_extender_1
  assign bit_extender_2_out = {{12{IR[31]}}, {IR[31], IR[19:12], IR[20], IR[30:21]}};  // Bit_Extender bit_extender_2
  // Probe on M_PC[11:0]
  D_Flip_Flop #(.trigger("high"), .Pre_Clr_Positions("LEGACY"), .NegatePresetClear("false"), .enable("true"), .NewFFLayout("false")) d_ff_1 (.Q(d_ff_1_q));  // open: clk, D, Qn, preset, en, reset
  // Probe on 13'hc
  // Probe on WB_PC[11:0]
  Comparator #(.width(13), .mode("twosComplement")) comparator_1 (
    .a(CNT_num), .b(13'hc), .eq(comparator_1_eq), .lt(comparator_1_lt));  // open: gt
  Clock #(.highDuration(1), .lowDuration(1)) clock_1 (.out(clock_1_out));
  Regifile regifile_1 (
    .Din(RDin), .Clk(CLK), .R1(R1), .R2(ID_R2), .WE(RegWrite), .W_num(mem_wb_1_writereg_num_2),
    .R1_num(multiplexer_3_out), .R2_num(multiplexer_4_out));
  assign bit_extender_3_out = {{20{multiplexer_5_out[11]}}, multiplexer_5_out};  // Bit_Extender bit_extender_3
  Shifter #(.width(32), .shift("ll")) shifter_1 (.in(bit_extender_1_out), .\dist (5'b00001), .out(shifter_1_out));
  Shifter #(.width(32), .shift("ll")) shifter_2 (.in(bit_extender_2_out), .\dist (5'b00001), .out(shifter_2_out));
  nand nand_1 (nand_1_out, d_ff_1_q, comparator_1_eq);
  Counter #(.width(13), .max('h1fff), .ongoal("stay"), .trigger("rising"), .behavior("old")) counter_1 (
    .count(comparator_1_lt), .Q(CNT_num), .clk(clock_1_out));  // open: load, D, carry, clr, preset
  Adder #(.width(32)) adder_2 (.a(shifter_1_out), .b(ID_PC), .out(adder_2_out));  // open: cin, cout
  Adder #(.width(32)) adder_3 (.a(shifter_2_out), .b(ID_PC), .out(adder_3_out));  // open: cin, cout
  assign CLK = nand_1_out ? clock_1_out : 1'bz;  // Controlled_Buffer controlled_buffer_1
  Pull_Resistor #(.pull(1)) pull_resistor_1 (.node(CLK));
  ID_EX id_ex_1 (
    .PC(ID_PC), .RS1(R1), .RS2(ID_R2), .IR(IR), .WriteReg_num(IR[11:7]), .ALUOP(\单周期硬布线控制器_1_alu_op ),
    .PC_2(EX_PC), .RS1_2(id_ex_1_rs1_2), .RS2_2(id_ex_1_rs2_2), .IR_2(EX_IR),
    .RegWrite_2(id_ex_1_regwrite_2), .MemToReg_2(id_ex_1_memtoreg_2), .MemWrite_2(id_ex_1_memwrite_2),
    .ALuSrc_2(id_ex_1_alusrc_2), .WriteReg_num_2(id_ex_1_writereg_num_2), .RegWrite(\单周期硬布线控制器_1_regwrite ),
    .MemToReg(\单周期硬布线控制器_1_memtoreg ), .MemWrite(\单周期硬布线控制器_1_memwrite ), .ALuSrc(\单周期硬布线控制器_1_alu_src ),
    .ALUOP_2(id_ex_1_aluop_2), .CLK(CLK), .immb_2(id_ex_1_immb_2), .immb(adder_2_out),
    .Imm32_2(id_ex_1_imm32_2), .Imm32(bit_extender_3_out),
    .\指令译码信号 ({ecall, 1'b0, DASB, CSR, BGEU, URET, JALR, JAL, \单周期硬布线控制器_1_beq }),
    .\指令译码信号_2 (\id_ex_1_指令译码信号_2 ), .immj(adder_3_out), .immj_2(id_ex_1_immj_2), .\EN_低电平有效 (halt));  // open: 气泡, rs2Fwd_2, rs1Fwd_2, PredictJump_2, rs2Fwd, rs1Fwd, PredictJump
  not not_2 (not_2_out, halt);
  Multiplexer #(.select(1), .width(32), .disabled("Z"), .enable("false")) multiplexer_6 (
    .in0(id_ex_1_rs2_2), .in1(id_ex_1_imm32_2), .out(multiplexer_6_out), .sel(id_ex_1_alusrc_2));
  Counter #(.width(16), .max('hffff), .ongoal("wrap"), .trigger("rising"), .behavior("old")) counter_2 (
    .count(not_2_out), .Q(\总周期数 ), .clk(CLK));  // open: load, D, carry, clr, preset
  and and_1 (and_1_out, \id_ex_1_指令译码信号_2 [0], alu_1_equal);
  and and_2 (and_2_out, \id_ex_1_指令译码信号_2 [5], ~alu_1_out_6);  // AND_Gate
  and and_3 (and_3_out, \id_ex_1_指令译码信号_2 [1], ~alu_1_equal);  // AND_Gate
  ALU alu_1 (
    .X(id_ex_1_rs1_2), .Y(multiplexer_6_out), .AluOP(id_ex_1_aluop_2), .Equal(alu_1_equal),
    .Result(alu_1_result), .out_6(alu_1_out_6));  // open: Result_2, out_4
  Adder #(.width(32)) adder_4 (.a(id_ex_1_immb_2), .b({32{1'b0}}), .out(adder_4_out));  // open: cin, cout
  and and_4 (and_4_out, not_2_out, jump);
  or or_2 (branch, and_1_out, and_2_out, and_3_out);
  Counter #(.width(16), .max('hffff), .ongoal("wrap"), .trigger("rising"), .behavior("old")) counter_3 (
    .count(and_4_out), .Q(\无条件分支数 ), .clk(CLK));  // open: load, D, carry, clr, preset
  Comparator #(.width(32), .mode("twosComplement")) comparator_2 (.a(id_ex_1_rs1_2), .b(32'h22));  // open: gt, eq, lt
  and and_5 (and_5_out, not_2_out, branch);
  EX_MEM ex_mem_1 (
    .PC(EX_PC), .IR(EX_IR), .WriteReg_num(id_ex_1_writereg_num_2), .PC_2(M_PC), .IR_2(MEM_IR),
    .RegWrite_2(ex_mem_1_regwrite_2), .MemToReg_2(ex_mem_1_memtoreg_2), .MemWrite_2(MemWrite),
    .WriteReg_num_2(ex_mem_1_writereg_num_2), .RegWrite(id_ex_1_regwrite_2), .MemToReg(id_ex_1_memtoreg_2),
    .MemWrite(id_ex_1_memwrite_2), .\EN_低电平有效 (halt), .CLK(CLK), .Reserved1_2(ex_mem_1_reserved1_2),
    .Reserved1(id_ex_1_immb_2), .\指令译码信号 (\id_ex_1_指令译码信号_2 ), .\指令译码信号_2 (\ex_mem_1_指令译码信号_2 ),
    .Reserved2(id_ex_1_immj_2), .Reserved2_2(ex_mem_1_reserved2_2), .WriteData(id_ex_1_rs2_2),
    .WriteData_2(ex_mem_1_writedata_2), .AluResult(alu_1_result), .AluResult_2(ex_mem_1_aluresult_2));  // open: 气泡, halt, halt_2
  Counter #(.width(16), .max('hffff), .ongoal("wrap"), .trigger("rising"), .behavior("old")) counter_4 (
    .count(and_5_out), .Q(\条件分支成功数 ), .clk(CLK));  // open: load, D, carry, clr, preset
  Multiplexer #(.select(1), .width(32), .disabled("Z"), .enable("false")) multiplexer_7 (
    .in0(ex_mem_1_writedata_2), .in1(SB), .out(MDin), .sel(\ex_mem_1_指令译码信号_2 [7]));
  assign bit_extender_4_out = {{24{1'b0}}, ex_mem_1_writedata_2[7:0]};  // Bit_Extender bit_extender_4
  RAM #(.addrWidth(10), .dataWidth(32), .bus("separate"), .Select("low")) ram_1 (
    .addr(ex_mem_1_aluresult_2[11:2]), .din(MDin), .data(ram_1_data), .str(MemWrite), .sel(1'b0), .clk(CLK),
    .ld(1'b1), .clr(RST));
  Shifter #(.width(32), .shift("ll")) shifter_3 (.in(bit_extender_4_out), .\dist (5'b01000), .out(shifter_3_out));
  Shifter #(.width(32), .shift("ll")) shifter_4 (.in(bit_extender_4_out), .\dist (5'b10000), .out(shifter_4_out));
  Shifter #(.width(32), .shift("ll")) shifter_5 (.in(bit_extender_4_out), .\dist (5'b11000), .out(shifter_5_out));
  Multiplexer #(.select(2), .width(32), .disabled("Z"), .enable("false")) multiplexer_8 (
    .in0(bit_extender_4_out), .in1(shifter_3_out), .in2(shifter_4_out), .in3(shifter_5_out),
    .out(multiplexer_8_out), .sel(ex_mem_1_aluresult_2[1:0]));
  MEM_WB mem_wb_1 (
    .PC(M_PC), .IR(MEM_IR), .WriteReg_num(ex_mem_1_writereg_num_2), .PC_2(WB_PC), .IR_2(WB_IR),
    .RegWrite_2(RegWrite), .MemToReg_2(mem_wb_1_memtoreg_2[0]), .WriteReg_num_2(mem_wb_1_writereg_num_2),
    .RegWrite(ex_mem_1_regwrite_2), .MemToReg(ex_mem_1_memtoreg_2), .\EN_低电平有效 (halt), .CLK(CLK),
    .Reserved1(ex_mem_1_reserved1_2), .\指令译码信号 (\ex_mem_1_指令译码信号_2 ), .\指令译码信号_2 (\mem_wb_1_指令译码信号_2 ),
    .Reserved2(ex_mem_1_reserved2_2), .MemData(ram_1_data), .MemData_2(mem_wb_1_memdata_2),
    .AluResult(ex_mem_1_aluresult_2), .AluResult_2(mem_wb_1_aluresult_2));  // open: 气泡, Reserved1_2, Reserved2_2, halt, out_24
  assign SB = multiplexer_8_out | ram_1_data;  // OR_Gate or_3, 32 bits wide
  or or_4 (jump, \mem_wb_1_指令译码信号_2 [2], \mem_wb_1_指令译码信号_2 [3]);
  Adder #(.width(32)) adder_5 (.a(32'h4), .b(WB_PC), .out(adder_5_out));  // open: cin, cout
  Multiplexer #(.select(2), .width(32), .disabled("Z"), .enable("false")) multiplexer_9 (
    .in0(mem_wb_1_aluresult_2), .in1(mem_wb_1_memdata_2), .in2(adder_5_out), .out(RDin),
    .sel({jump, mem_wb_1_memtoreg_2[0]}));  // open: in3
  Multiplexer #(.select(1), .width(32), .disabled("Z"), .enable("false")) multiplexer_10 (
    .in0(mem_wb_1_aluresult_2), .in1(adder_5_out), .out(multiplexer_10_out), .sel(\mem_wb_1_指令译码信号_2 [2]));
  not not_3 (not_3_out, \mem_wb_1_指令译码信号_2 [8]);
  and and_6 (and_6_out, not_3_out, \mem_wb_1_指令译码信号_2 [9]);
  Register #(.width(32), .trigger("rising"), .Select("low")) register_1 (
    .D(ID_R2), .en(ID_Print), .Q(LedData), .clk(CLK));  // open: clr
  // AND_Gate and_7 has open pins: in0=\mem_wb_1_指令译码信号_2 [8], in1=\mem_wb_1_指令译码信号_2 [9], out=open
  Multiplexer #(.select(1), .width(1), .disabled("Z"), .enable("false")) multiplexer_11 (
    .in0(and_6_out), .in1(1'b0), .sel(Go));  // open: out
  Comparator #(.width(32), .mode("unsigned")) comparator_3 (.a(R1), .b(32'h22), .eq(comparator_3_eq));  // open: gt, lt
  and and_8 (ID_Print, comparator_3_eq, ecall);
  and and_9 (ID_Exit, ~comparator_3_eq, ecall);  // AND_Gate
  Register #(.width(1), .trigger("rising"), .Select("low")) Exit_EX (
    .D(ID_Exit), .en(1'b1), .Q(Exit_EX_q), .clk(CLK), .clr(RST));
  Register #(.width(1), .trigger("rising"), .Select("low")) Exit_MEM (
    .D(Exit_EX_q), .en(1'b1), .Q(Exit_MEM_Out), .clk(CLK), .clr(RST));
  Register #(.width(1), .trigger("rising"), .Select("low")) Exit_WB (
    .D(HaltNext), .en(1'b1), .Q(halt), .clk(CLK), .clr(RST));
  or or_5 (HaltNext, Exit_MEM_Out, halt);

  // Other names for the same wires on the sheet: rd[4:0] = IR[11:7]; HaltHold = halt; MEM_PC[31:0] = M_PC

  // Notes on the sheet:
  //   中断源
  //   时空图监测，可删除
  //   中断等待指示
  //   数码管输出
  //   contents of rom_1 (hex, n*v repeats v):
  //   100493 100006f 100493 200913 300993 100006f 100493 200913 300993 100006f 100493 200913 300993
  //   100006f 100493 200913 300993 29c000ef 100413 100493 1f49493 900533 2200893 73 24d493 48463 fedff06f
  //   900533 2200893 73 100493 249493 900533 2200893 73 48463 fedff06f 100493 1f49493 900533 2200893 73
  //   4034d493 900533 2200893 73 4044d493 900533 2200893 73 4044d493 900533 2200893 73 4044d493 900533
  //   2200893 73 4044d493 900533 2200893 73 4044d493 900533 2200893 73 4044d493 900533 2200893 73 4044d493
  //   900533 2200893 73 100413 1f41993 41f9d993 433 c00913 300b13 140413 f47413 800293 100313 499993
  //   89e9b3 1300533 2200893 73 406282b3 fe0294e3 140413 f00f93 1f47433 1c41413 800293 100313 49d993
  //   89e9b3 1300533 2200893 73 406282b3 fe0294e3 1c45413 406b0b33 b0463 f95ff06f 2b3 fff2c293 829293
  //   ff2e293 500533 2200893 73 fff00413 493 84a023 140413 448493 84a023 140413 448493 84a023 140413
  //   448493 84a023 140413 448493 84a023 140413 448493 84a023 140413 448493 84a023 140413 448493 84a023
  //   140413 448493 84a023 140413 448493 84a023 140413 448493 84a023 140413 448493 84a023 140413 448493
  //   84a023 140413 448493 84a023 140413 448493 84a023 140413 448493 84a023 140413 448493 140413 433
  //   3c00493 42983 4aa03 149a2b3 28663 134a023 1442023 ffc48493 fe9412e3 800533 2200893 73 440413 3c00493
  //   fc9416e3 a00893 73 413 140413 800533 2200893 73 240413 800533 2200893 73 340413 800533 2200893 73
  //   440413 800533 2200893 73 540413 800533 2200893 73 640413 800533 2200893 73 740413 800533 2200893 73
  //   840413 800533 2200893 2200893 73 8067
  //   指令字
  //   JALR
  //   URET
  //   b型
  //   j型
  //   控制位
  //   Beq
  //   Bne
  //   MemToReg
  //   MemWrite
  //   AluOP
  //   AluSrcB
  //   RegWrite
  //   流水调试日志用
  //   暂停节拍，不能为0
  //   戳工具置1进入计数暂停模式，ctrl+k时钟自动运行到对应节拍暂停
  //   ctrl+k关闭时钟连续运行，将控制位置零，进入单步调试模式调试
  //   用这个时钟源需要去掉电路中的其他时钟源
  //   可计数暂停的时钟源
  //   为方便自动评测，需要输出流水线各段保存的PC值，注意是PC不是PC+4，另外ID段寄存器写入信息，Mem段内存写入信息也要输出
endmodule
module \重定向流水线  (
  output RegWrite,
  output MemWrite,
  output [31:0] IF_PC,
  output [31:0] ID_PC,
  output [31:0] EX_PC,
  output [31:0] M_PC,
  output [31:0] WB_PC,
  output [31:0] RDin,
  output [31:0] MDin,
  output [31:0] LedData
);

  wire alu_1_equal, alu_1_out_6, and_1_out, and_2_out, and_3_out, and_4_out, and_5_out, and_6_out, and_7_out,
       and_8_out, BGEU, branch, branch_conf, CLK, clock_1_out, comparator_1_eq, comparator_1_lt,
       comparator_2_eq, CSR, d_ff_1_q, DASB, ecall, ex_mem_1_halt_2, ex_mem_1_memtoreg_2,
       ex_mem_1_regwrite_2, Go, halt, id_ex_1_alusrc_2, id_ex_1_memtoreg_2, id_ex_1_memwrite_2,
       id_ex_1_regwrite_2, IR1, IR2, IR3, JAL, JALR, jump, LoadUse, mem_wb_1_out_24, nand_1_out, not_1_out,
       not_2_out, not_3_out, not_4_out, or_1_out, or_2_out, or_5_out, RST, S_type, URET, W1, W2, W3,
       \单周期硬布线控制器_1_alu_src , \单周期硬布线控制器_1_memtoreg , \单周期硬布线控制器_1_memwrite , \单周期硬布线控制器_1_regwrite ,
       \寄存器使用情况_1_rs1_used , \寄存器使用情况_1_rs2_used ;
  wire [0:0] mem_wb_1_memtoreg_2;
  wire [1:0] id_ex_1_rs1fwd_2, id_ex_1_rs2fwd_2, priority_encoder_1_out, \数据相关监测_1_rs1fwd , \数据相关监测_1_rs2fwd ;
  wire [3:0] id_ex_1_aluop_2, \单周期硬布线控制器_1_alu_op ;
  wire [4:0] ex_mem_1_writereg_num_2, id_ex_1_writereg_num_2, mem_wb_1_writereg_num_2, multiplexer_2_out,
       multiplexer_3_out;
  wire [8:0] \单周期硬布线控制器_1_beq ;
  wire [9:0] \ex_mem_1_指令译码信号_2 , \id_ex_1_指令译码信号_2 , \mem_wb_1_指令译码信号_2 ;
  wire [11:0] multiplexer_4_out;
  wire [12:0] CNT_num;
  wire [15:0] \LoadUse次数 , \总周期数 , \插入气泡数 , \无条件分支数 , \条件分支成功数 ;
  wire [31:0] adder_1_out, adder_2_out, adder_3_out, adder_4_out, alu_1_result, bit_extender_1_out,
       bit_extender_2_out, bit_extender_3_out, bit_extender_4_out, EX_IR, ex_mem_1_aluresult_2,
       ex_mem_1_reserved1_2, ex_mem_1_reserved2_2, ex_mem_1_writedata_2, id_ex_1_imm32_2, id_ex_1_immb_2,
       id_ex_1_immj_2, id_ex_1_rs1_2, id_ex_1_rs2_2, ID_IR, IF_IR, IR, MEM_IR, mem_wb_1_aluresult_2,
       mem_wb_1_memdata_2, multiplexer_1_out, multiplexer_5_out, multiplexer_6_out, multiplexer_7_out,
       multiplexer_9_out, R1, ram_1_data, regifile_1_r2, SB, shifter_1_out, shifter_2_out, shifter_3_out,
       shifter_4_out, shifter_5_out, WB_IR;

  Button \u_总复位  (.out(RST));
  Button _1 (.out(IR1));
  Button _2 (.out(IR2));
  Button _3 (.out(IR3));
  // Probe on \总周期数 
  // Probe on \总周期数 
  Button \u_继续运行  (.out(Go));
  LED #(.active("true")) led_1 (.in(W1));
  LED #(.active("true")) led_2 (.in(W2));
  LED #(.active("true")) led_3 (.in(W3));
  Multiplexer #(.select(2), .width(32), .disabled("Z"), .enable("false")) multiplexer_1 (
    .in0(adder_1_out), .in1(alu_1_result), .in2(adder_2_out), .in3(adder_3_out), .out(multiplexer_1_out),
    .sel(priority_encoder_1_out));
  not not_1 (not_1_out, or_1_out);
  or or_1 (or_1_out, LoadUse, halt);
  Hex_Digit_Display hex_digit_display_1 (.value(LedData[31:28]));  // open: dp
  // Probe on IF_PC[19:0]
  // RiscV_Probe riscv_probe_1: pin names not known; wires that end beside it: IF_IR
  Register #(.width(32), .trigger("rising"), .Select("low")) PC (
    .D(multiplexer_1_out), .en(not_1_out), .Q(IF_PC), .clk(CLK), .clr(RST));
  Hex_Digit_Display hex_digit_display_2 (.value(LedData[27:24]));  // open: dp
  Hex_Digit_Display hex_digit_display_3 (.value(LedData[23:20]));  // open: dp
  // Probe on ID_PC[19:0]
  // RiscV_Probe riscv_probe_2: pin names not known; wires that end beside it: ID_IR
  Adder #(.width(32)) adder_1 (.a(IF_PC), .b(32'h4), .out(adder_1_out));  // open: cin, cout
  Hex_Digit_Display hex_digit_display_4 (.value(LedData[19:16]));  // open: dp
  Hex_Digit_Display hex_digit_display_5 (.value(LedData[15:12]));  // open: dp
  ROM #(.addrWidth(10), .dataWidth(32), .Select("low")) rom_1 (.addr(IF_PC[11:2]), .data(IF_IR));
  Hex_Digit_Display hex_digit_display_6 (.value(LedData[11:8]));  // open: dp
  Hex_Digit_Display hex_digit_display_7 (.value(LedData[7:4]));  // open: dp
  // Probe on EX_PC[19:0]
  // RiscV_Probe riscv_probe_3: pin names not known; wires that end beside it: EX_IR
  or or_2 (or_2_out, halt, LoadUse);
  Hex_Digit_Display hex_digit_display_8 (.value(LedData[3:0]));  // open: dp
  IF_ID if_id_1 (
    .IR(IF_IR), .\气泡 (branch_conf), .IR_2(IR), .\EN_低电平有效 (or_2_out), .CLK(CLK), .PC_2(ID_PC), .PC(IF_PC),
    .IR_3(ID_IR));  // open: PredictJump, PredictJump_2
  // Probe on \总周期数 
  // Probe on M_PC[19:0]
  // RiscV_Probe riscv_probe_4: pin names not known; wires that end beside it: MEM_IR
  \数据相关监测  \u_数据相关监测_1  (
    .rs1_id(multiplexer_2_out), .rs2_id(multiplexer_3_out), .rs1_used(\寄存器使用情况_1_rs1_used ),
    .rs2_used(\寄存器使用情况_1_rs2_used ), .EX_RegWrite(id_ex_1_regwrite_2), .MEM_RegWrite(ex_mem_1_regwrite_2),
    .EX_MemToReg(id_ex_1_memtoreg_2), .EX_rd(id_ex_1_writereg_num_2), .MEM_rd(ex_mem_1_writereg_num_2),
    .rs1Fwd(\数据相关监测_1_rs1fwd ), .rs2Fwd(\数据相关监测_1_rs2fwd ), .LoadUse(LoadUse));  // open: DataCorrelate
  \寄存器使用情况  \u_寄存器使用情况_1  (
    .OP(IR[6:2]), .Funct({IR[30], IR[25], IR[14:12]}), .rs1_used(\寄存器使用情况_1_rs1_used ),
    .rs2_used(\寄存器使用情况_1_rs2_used ));
  // Probe on \总周期数 
  // Probe on \无条件分支数 
  // Probe on \条件分支成功数 
  // Probe on \插入气泡数 
  // Probe on \LoadUse次数 
  // Probe on IF_PC[11:0]
  // Probe on WB_PC[19:0]
  // RiscV_Probe riscv_probe_5: pin names not known; wires that end beside it: WB_IR
  // Probe on ID_PC[11:0]
  // Probe on EX_PC[11:0]
  \单周期硬布线控制器  \u_单周期硬布线控制器_1  (
    .OP(IR[6:2]), .Funct({IR[30], IR[25], IR[14:12]}), .ALU_OP(\单周期硬布线控制器_1_alu_op ), .in_3(IR[21]),
    .uret(URET), .MemToReg(\单周期硬布线控制器_1_memtoreg ), .ecall(ecall), .MemWrite(\单周期硬布线控制器_1_memwrite ),
    .ALU_SRC(\单周期硬布线控制器_1_alu_src ), .RegWrite(\单周期硬布线控制器_1_regwrite ), .S_type(S_type),
    .Beq(\单周期硬布线控制器_1_beq [0]), .Bne(\单周期硬布线控制器_1_beq [1]), .Jalr(JALR), .JAL(JAL), .blt(BGEU), .csrrsi(CSR),
    .dasb(DASB));  // open: U_type, csrrci
  Multiplexer #(.select(1), .width(5), .disabled("Z"), .enable("false")) multiplexer_2 (
    .in0(IR[19:15]), .in1(5'b10001), .out(multiplexer_2_out), .sel(ecall));
  Multiplexer #(.select(1), .width(5), .disabled("Z"), .enable("false")) multiplexer_3 (
    .in0(IR[24:20]), .in1(5'b01010), .out(multiplexer_3_out), .sel(ecall));
  Multiplexer #(.select(1), .width(12), .disabled("Z"), .enable("false")) multiplexer_4 (
    .in0(IR[31:20]), .in1({IR[31:25], IR[11:7]}), .out(multiplexer_4_out), .sel(S_type));
  assign bit_extender_1_out = {{20{IR[31]}}, {IR[31], IR[7], IR[30:25], IR[11:8]}};  // Bit_Extender bit_extender_1
  assign bit_extender_2_out = {{12{IR[31]}}, {IR[31], IR[19:12], IR[20], IR[30:21]}};  // Bit_Extender bit_extender_2
  // Probe on M_PC[11:0]
  D_Flip_Flop #(.trigger("high"), .Pre_Clr_Positions("LEGACY"), .NegatePresetClear("false"), .enable("true"), .NewFFLayout("false")) d_ff_1 (.Q(d_ff_1_q));  // open: clk, D, Qn, preset, en, reset
  // Probe on 13'hc
  assign bit_extender_3_out = {{20{multiplexer_4_out[11]}}, multiplexer_4_out};  // Bit_Extender bit_extender_3
  // Probe on WB_PC[11:0]
  Comparator #(.width(13), .mode("twosComplement")) comparator_1 (
    .a(CNT_num), .b(13'hc), .eq(comparator_1_eq), .lt(comparator_1_lt));  // open: gt
  Clock #(.highDuration(1), .lowDuration(1)) clock_1 (.out(clock_1_out));
  not not_2 (not_2_out, CLK);
  Regifile regifile_1 (
    .Din(RDin), .Clk(not_2_out), .R1(R1), .R2(regifile_1_r2), .WE(RegWrite), .W_num(mem_wb_1_writereg_num_2),
    .R1_num(multiplexer_2_out), .R2_num(multiplexer_3_out));
  Shifter #(.width(32), .shift("ll")) shifter_1 (.in(bit_extender_1_out), .\dist (5'b00001), .out(shifter_1_out));
  Shifter #(.width(32), .shift("ll")) shifter_2 (.in(bit_extender_2_out), .\dist (5'b00001), .out(shifter_2_out));
  nand nand_1 (nand_1_out, d_ff_1_q, comparator_1_eq);
  Counter #(.width(13), .max('h1fff), .ongoal("stay"), .trigger("rising"), .behavior("old")) counter_1 (
    .count(comparator_1_lt), .Q(CNT_num), .clk(clock_1_out));  // open: load, D, carry, clr, preset
  Priority_Encoder #(.select(2), .disabled("Z")) priority_encoder_1 (
    .in0(1'b1), .in1(\id_ex_1_指令译码信号_2 [3]), .in2(branch), .in3(\id_ex_1_指令译码信号_2 [2]),
    .out(priority_encoder_1_out));  // open: gs, en_out, en_in
  assign CLK = nand_1_out ? clock_1_out : 1'bz;  // Controlled_Buffer controlled_buffer_1
  or or_3 (branch_conf, \id_ex_1_指令译码信号_2 [3], \id_ex_1_指令译码信号_2 [2], branch);
  Pull_Resistor #(.pull(1)) pull_resistor_1 (.node(CLK));
  or or_4 (branch, and_1_out, and_2_out, and_3_out);
  or or_5 (or_5_out, branch_conf, LoadUse);
  ID_EX id_ex_1 (
    .PC(ID_PC), .RS1(R1), .RS2(regifile_1_r2), .IR(IR), .WriteReg_num(IR[11:7]),
    .ALUOP(\单周期硬布线控制器_1_alu_op ), .\气泡 (or_5_out), .PC_2(EX_PC), .RS1_2(id_ex_1_rs1_2),
    .RS2_2(id_ex_1_rs2_2), .IR_2(EX_IR), .RegWrite_2(id_ex_1_regwrite_2), .MemToReg_2(id_ex_1_memtoreg_2),
    .MemWrite_2(id_ex_1_memwrite_2), .ALuSrc_2(id_ex_1_alusrc_2), .WriteReg_num_2(id_ex_1_writereg_num_2),
    .RegWrite(\单周期硬布线控制器_1_regwrite ), .MemToReg(\单周期硬布线控制器_1_memtoreg ), .MemWrite(\单周期硬布线控制器_1_memwrite ),
    .ALuSrc(\单周期硬布线控制器_1_alu_src ), .ALUOP_2(id_ex_1_aluop_2), .CLK(CLK), .immb_2(id_ex_1_immb_2),
    .immb(shifter_1_out), .Imm32_2(id_ex_1_imm32_2), .Imm32(bit_extender_3_out), .rs2Fwd_2(id_ex_1_rs2fwd_2),
    .rs1Fwd_2(id_ex_1_rs1fwd_2), .rs2Fwd(\数据相关监测_1_rs2fwd ), .rs1Fwd(\数据相关监测_1_rs1fwd ),
    .\指令译码信号 ({ecall, \单周期硬布线控制器_1_beq [8], DASB, CSR, BGEU, URET, JALR, JAL, \单周期硬布线控制器_1_beq [1:0]}),
    .\指令译码信号_2 (\id_ex_1_指令译码信号_2 ), .immj(shifter_2_out), .immj_2(id_ex_1_immj_2), .\EN_低电平有效 (halt));  // open: PredictJump_2, PredictJump
  and and_1 (and_1_out, \id_ex_1_指令译码信号_2 [5], ~alu_1_out_6);  // AND_Gate
  and and_2 (and_2_out, \id_ex_1_指令译码信号_2 [0], alu_1_equal);
  and and_3 (and_3_out, \id_ex_1_指令译码信号_2 [1], ~alu_1_equal);  // AND_Gate
  Multiplexer #(.select(2), .width(32), .disabled("Z"), .enable("false")) multiplexer_5 (
    .in0(id_ex_1_rs1_2), .in1(ex_mem_1_aluresult_2), .in2(RDin), .out(multiplexer_5_out),
    .sel(id_ex_1_rs1fwd_2));  // open: in3
  Multiplexer #(.select(2), .width(32), .disabled("Z"), .enable("false")) multiplexer_6 (
    .in0(id_ex_1_rs2_2), .in1(ex_mem_1_aluresult_2), .in2(RDin), .out(multiplexer_6_out),
    .sel(id_ex_1_rs2fwd_2));  // open: in3
  Multiplexer #(.select(1), .width(32), .disabled("Z"), .enable("false")) multiplexer_7 (
    .in0(multiplexer_6_out), .in1(id_ex_1_imm32_2), .out(multiplexer_7_out), .sel(id_ex_1_alusrc_2));
  not not_3 (not_3_out, comparator_2_eq);
  Adder #(.width(32)) adder_2 (.a(id_ex_1_immb_2), .b(EX_PC), .out(adder_2_out));  // open: cin, cout
  Adder #(.width(32)) adder_3 (.a(EX_PC), .b(id_ex_1_immj_2), .out(adder_3_out));  // open: cin, cout
  not not_4 (not_4_out, halt);
  ALU alu_1 (
    .X(multiplexer_5_out), .Y(multiplexer_7_out), .AluOP(id_ex_1_aluop_2), .Equal(alu_1_equal),
    .Result(alu_1_result), .out_6(alu_1_out_6));  // open: Result_2, out_4
  and and_4 (and_4_out, not_3_out, \id_ex_1_指令译码信号_2 [9]);
  Register #(.width(32), .trigger("rising"), .Select("low")) register_1 (
    .D(multiplexer_6_out), .en(and_5_out), .Q(LedData), .clk(CLK));  // open: clr
  and and_5 (and_5_out, comparator_2_eq, \id_ex_1_指令译码信号_2 [9]);
  Counter #(.width(16), .max('hffff), .ongoal("wrap"), .trigger("rising"), .behavior("old")) counter_2 (
    .count(not_4_out), .Q(\总周期数 ), .clk(CLK));  // open: load, D, carry, clr, preset
  Comparator #(.width(32), .mode("twosComplement")) comparator_2 (
    .a(multiplexer_5_out), .b(32'h22), .eq(comparator_2_eq));  // open: gt, lt
  and and_6 (and_6_out, not_4_out, jump);
  Counter #(.width(16), .max('hffff), .ongoal("wrap"), .trigger("rising"), .behavior("old")) counter_3 (
    .count(and_6_out), .Q(\无条件分支数 ), .clk(CLK));  // open: load, D, carry, clr, preset
  EX_MEM ex_mem_1 (
    .PC(EX_PC), .IR(EX_IR), .WriteReg_num(id_ex_1_writereg_num_2), .\气泡 (1'b0), .PC_2(M_PC), .IR_2(MEM_IR),
    .RegWrite_2(ex_mem_1_regwrite_2), .MemToReg_2(ex_mem_1_memtoreg_2), .MemWrite_2(MemWrite),
    .WriteReg_num_2(ex_mem_1_writereg_num_2), .RegWrite(id_ex_1_regwrite_2), .MemToReg(id_ex_1_memtoreg_2),
    .MemWrite(id_ex_1_memwrite_2), .\EN_低电平有效 (halt), .CLK(CLK), .Reserved1_2(ex_mem_1_reserved1_2),
    .Reserved1(id_ex_1_immb_2), .\指令译码信号 (\id_ex_1_指令译码信号_2 ), .\指令译码信号_2 (\ex_mem_1_指令译码信号_2 ),
    .Reserved2(id_ex_1_immj_2), .Reserved2_2(ex_mem_1_reserved2_2), .WriteData(multiplexer_6_out),
    .WriteData_2(ex_mem_1_writedata_2), .AluResult(alu_1_result), .AluResult_2(ex_mem_1_aluresult_2),
    .halt(and_4_out), .halt_2(ex_mem_1_halt_2));
  and and_7 (and_7_out, not_4_out, branch);
  assign bit_extender_4_out = {{24{1'b0}}, ex_mem_1_writedata_2[7:0]};  // Bit_Extender bit_extender_4
  Counter #(.width(16), .max('hffff), .ongoal("wrap"), .trigger("rising"), .behavior("old")) counter_4 (
    .count(and_7_out), .Q(\条件分支成功数 ), .clk(CLK));  // open: load, D, carry, clr, preset
  Multiplexer #(.select(1), .width(32), .disabled("Z"), .enable("false")) multiplexer_8 (
    .in0(ex_mem_1_writedata_2), .in1(SB), .out(MDin), .sel(\ex_mem_1_指令译码信号_2 [7]));
  Shifter #(.width(32), .shift("ll")) shifter_3 (.in(bit_extender_4_out), .\dist (5'b01000), .out(shifter_3_out));
  Shifter #(.width(32), .shift("ll")) shifter_4 (.in(bit_extender_4_out), .\dist (5'b10000), .out(shifter_4_out));
  Shifter #(.width(32), .shift("ll")) shifter_5 (.in(bit_extender_4_out), .\dist (5'b11000), .out(shifter_5_out));
  and and_8 (and_8_out, not_4_out, LoadUse);
  RAM #(.addrWidth(10), .dataWidth(32), .bus("separate"), .Select("low")) ram_1 (
    .addr(ex_mem_1_aluresult_2[11:2]), .din(MDin), .data(ram_1_data), .str(MemWrite), .sel(1'b0), .clk(CLK),
    .ld(1'b1));  // open: clr
  Multiplexer #(.select(2), .width(32), .disabled("Z"), .enable("false")) multiplexer_9 (
    .in0(bit_extender_4_out), .in1(shifter_3_out), .in2(shifter_4_out), .in3(shifter_5_out),
    .out(multiplexer_9_out), .sel(ex_mem_1_aluresult_2[1:0]));
  Counter #(.width(16), .max('hffff), .ongoal("wrap"), .trigger("rising"), .behavior("old")) counter_5 (
    .count(and_8_out), .Q(\LoadUse次数 ), .clk(CLK));  // open: load, D, carry, clr, preset
  MEM_WB mem_wb_1 (
    .PC(M_PC), .IR(MEM_IR), .WriteReg_num(ex_mem_1_writereg_num_2), .\气泡 (1'b0), .PC_2(WB_PC), .IR_2(WB_IR),
    .RegWrite_2(RegWrite), .MemToReg_2(mem_wb_1_memtoreg_2[0]), .WriteReg_num_2(mem_wb_1_writereg_num_2),
    .RegWrite(ex_mem_1_regwrite_2), .MemToReg(ex_mem_1_memtoreg_2), .\EN_低电平有效 (halt), .CLK(CLK),
    .Reserved1(ex_mem_1_reserved1_2), .\指令译码信号 (\ex_mem_1_指令译码信号_2 ), .\指令译码信号_2 (\mem_wb_1_指令译码信号_2 ),
    .Reserved2(ex_mem_1_reserved2_2), .MemData(ram_1_data), .MemData_2(mem_wb_1_memdata_2),
    .AluResult(ex_mem_1_aluresult_2), .AluResult_2(mem_wb_1_aluresult_2), .halt(ex_mem_1_halt_2),
    .out_24(mem_wb_1_out_24));  // open: Reserved1_2, Reserved2_2
  assign SB = multiplexer_9_out | ram_1_data;  // OR_Gate or_6, 32 bits wide
  Multiplexer #(.select(1), .width(1), .disabled("Z"), .enable("false")) multiplexer_10 (
    .in0(mem_wb_1_out_24), .in1(1'b0), .out(halt), .sel(Go));
  Adder #(.width(32)) adder_4 (.a(32'h4), .b(WB_PC), .out(adder_4_out));  // open: cin, cout
  or or_7 (jump, \mem_wb_1_指令译码信号_2 [2], \mem_wb_1_指令译码信号_2 [3]);
  Multiplexer #(.select(2), .width(32), .disabled("Z"), .enable("false")) multiplexer_11 (
    .in0(mem_wb_1_aluresult_2), .in1(mem_wb_1_memdata_2), .in2(adder_4_out), .out(RDin),
    .sel({jump, mem_wb_1_memtoreg_2[0]}));  // open: in3
  Multiplexer #(.select(1), .width(32), .disabled("Z"), .enable("false")) multiplexer_12 (
    .in0(mem_wb_1_aluresult_2), .in1(adder_4_out), .sel(\mem_wb_1_指令译码信号_2 [2]));  // open: out

  // Other names for the same wires on the sheet: rd[4:0] = IR[11:7]; MEM_PC[31:0] = M_PC

  // Notes on the sheet:
  //   中断源
  //   时空图监测，可删除
  //   中断等待指示
  //   数码管输出
  //   contents of rom_1 (hex, n*v repeats v):
  //   100493 100006f 100493 200913 300993 100006f 100493 200913 300993 100006f 100493 200913 300993
  //   100006f 100493 200913 300993 3c8000ef 100413 100493 1f49493 900533 2200893 73 24d493 48463 fedff06f
  //   900533 2200893 73 100493 249493 900533 2200893 73 48463 fedff06f 100493 1f49493 900533 2200893 73
  //   4034d493 900533 2200893 73 4044d493 900533 2200893 73 4044d493 900533 2200893 73 4044d493 900533
  //   2200893 73 4044d493 900533 2200893 73 4044d493 900533 2200893 73 4044d493 900533 2200893 73 4044d493
  //   900533 2200893 73 100413 1f41993 41f9d993 433 c00913 300b13 140413 f47413 800293 100313 499993
  //   89e9b3 1300533 2200893 73 406282b3 fe0294e3 140413 f00f93 1f47433 1c41413 800293 100313 49d993
  //   89e9b3 1300533 2200893 73 406282b3 fe0294e3 1c45413 406b0b33 b0463 f95ff06f 2b3 fff2c293 829293
  //   ff2e293 500533 2200893 73 fff00413 493 84a023 140413 448493 84a023 140413 448493 84a023 140413
  //   448493 84a023 140413 448493 84a023 140413 448493 84a023 140413 448493 84a023 140413 448493 84a023
  //   140413 448493 84a023 140413 448493 84a023 140413 448493 84a023 140413 448493 84a023 140413 448493
  //   84a023 140413 448493 84a023 140413 448493 84a023 140413 448493 84a023 140413 448493 140413 433
  //   3c00493 42983 4aa03 149a2b3 28663 134a023 1442023 ffc48493 fe9412e3 800533 2200893 73 440413 3c00493
  //   fc9416e3 a00893 73 100293 300313 800493 849493 7648493 1449493 900533 2200893 73 800e13 4054d4b3
  //   4064d4b3 900533 2200893 73 fffe0e13 fe0e14e3 a00893 73 fff00293 7700493 849493 7748493 900533
  //   2200893 73 1000e13 54c4b3 900533 2200893 73 fffe0e13 fe0e16e3 a00893 73 313 1000e13 8400493 849493
  //   8348493 400913 891913 490913 849493 8248493 849493 8148493 891913 490913 891913 490913 932023
  //   12484b3 430313 fffe0e13 fe0e18e3 2000e13 313 31483 900533 2200893 73 230313 fffe0e13 fe0e14e3 a00893
  //   73 f00493 900533 2200893 73 fff48493 fe04d8e3 a00893 73 413 140413 800533 2200893 73 240413 800533
  //   2200893 73 340413 800533 2200893 73 440413 800533 2200893 73 540413 800533 2200893 73 640413 800533
  //   2200893 73 740413 800533 2200893 73 840413 800533 2200893 2200893 73 8067
  //   指令字
  //   JALR
  //   URET
  //   b型
  //   j型
  //   控制位
  //   Beq
  //   Bne
  //   MemToReg
  //   MemWrite
  //   AluOP
  //   AluSrcB
  //   RegWrite
  //   流水调试日志用
  //   暂停节拍，不能为0
  //   戳工具置1进入计数暂停模式，ctrl+k时钟自动运行到对应节拍暂停
  //   ctrl+k关闭时钟连续运行，将控制位置零，进入单步调试模式调试
  //   可计数暂停的时钟源
  //   为方便自动评测，需要输出流水线各段保存的PC值，注意是PC不是PC+4，另外ID段寄存器写入信息，Mem段内存写入信息也要输出
endmodule

// IF / ID
module IF_ID (
  input  PredictJump,
  input  [31:0] IR,
  input  [31:0] PC,
  input  \气泡 ,
  input  \EN_低电平有效 ,
  input  CLK,
  output PredictJump_2,
  output [31:0] IR_2,
  output [31:0] PC_2,
  output [31:0] IR_3
);

  wire multiplexer_1_out, not_1_out, pull_resistor_3_node;
  wire [31:0] multiplexer_2_out, multiplexer_3_out;

  Pull_Resistor #(.pull(0)) pull_resistor_1 (.node(\气泡 ));
  Multiplexer #(.select(1), .width(1), .disabled("Z"), .enable("false")) multiplexer_1 (
    .in0(PredictJump), .in1(1'b0), .out(multiplexer_1_out), .sel(\气泡 ));
  Multiplexer #(.select(1), .width(32), .disabled("Z"), .enable("false")) multiplexer_2 (
    .in0(IR), .in1({32{1'b0}}), .out(multiplexer_2_out), .sel(\气泡 ));
  Multiplexer #(.select(1), .width(32), .disabled("Z"), .enable("false")) multiplexer_3 (
    .in0(PC), .in1({32{1'b0}}), .out(multiplexer_3_out), .sel(\气泡 ));
  Pull_Resistor #(.pull(0)) pull_resistor_2 (.node(\EN_低电平有效 ));
  Pull_Resistor #(.pull(0)) pull_resistor_3 (.node(pull_resistor_3_node));
  not not_1 (not_1_out, \EN_低电平有效 );
  Register #(.width(1), .trigger("rising"), .Select("low")) u_PredictJump (
    .D(multiplexer_1_out), .en(not_1_out), .Q(PredictJump_2), .clk(CLK));  // open: clr
  Register #(.width(32), .trigger("rising"), .Select("low")) u_IR (
    .D(multiplexer_2_out), .en(not_1_out), .Q(IR_2), .clk(CLK));  // open: clr
  Register #(.width(32), .trigger("rising"), .Select("low")) u_PC (
    .D(multiplexer_3_out), .en(not_1_out), .Q(PC_2), .clk(CLK));  // open: clr

  assign IR_3 = IR_2;

  // Notes on the sheet:
  //   气泡: pull=down
endmodule

// ID / EX
module ID_EX (
  input  [31:0] PC,
  input  [31:0] RS1,
  input  [31:0] RS2,
  input  RegWrite,
  input  MemToReg,
  input  MemWrite,
  input  ALuSrc,
  input  [31:0] Imm32,
  input  [1:0] rs2Fwd,
  input  [1:0] rs1Fwd,
  input  PredictJump,
  input  [31:0] IR,
  input  [31:0] immb,
  input  [31:0] immj,
  input  [4:0] WriteReg_num,
  input  [3:0] ALUOP,
  input  [9:0] \指令译码信号 ,
  input  \气泡 ,
  input  CLK,
  input  \EN_低电平有效 ,
  output [31:0] PC_2,
  output [31:0] RS1_2,
  output [31:0] RS2_2,
  output [31:0] Imm32_2,
  output [31:0] IR_2,
  output RegWrite_2,
  output MemToReg_2,
  output MemWrite_2,
  output ALuSrc_2,
  output [1:0] rs2Fwd_2,
  output [31:0] immb_2,
  output [1:0] rs1Fwd_2,
  output PredictJump_2,
  output [31:0] immj_2,
  output [4:0] WriteReg_num_2,
  output [3:0] ALUOP_2,
  output [9:0] \指令译码信号_2 
);

  wire not_1_out;
  wire [3:0] multiplexer_10_out;
  wire [4:0] multiplexer_9_out;
  wire [9:0] multiplexer_11_out;
  wire [15:0] multiplexer_8_out;
  wire [15:9] ControlBusIn, ControlBusOut;
  wire [31:0] multiplexer_1_out, multiplexer_2_out, multiplexer_3_out, multiplexer_4_out, multiplexer_5_out,
       multiplexer_6_out, multiplexer_7_out;

  Pull_Resistor #(.pull(0)) pull_resistor_1 (.node({ControlBusIn, PredictJump, rs1Fwd, rs2Fwd, ALuSrc, MemWrite, MemToReg, RegWrite}));
  Pull_Resistor #(.pull(0)) pull_resistor_2 (.node(\指令译码信号 ));
  Pull_Resistor #(.pull(0)) pull_resistor_3 (.node(\气泡 ));
  Multiplexer #(.select(1), .width(32), .disabled("Z"), .enable("false")) multiplexer_1 (
    .in0(PC), .in1({32{1'b0}}), .out(multiplexer_1_out), .sel(\气泡 ));
  Multiplexer #(.select(1), .width(32), .disabled("Z"), .enable("false")) multiplexer_2 (
    .in0(RS1), .in1({32{1'b0}}), .out(multiplexer_2_out), .sel(\气泡 ));
  Multiplexer #(.select(1), .width(32), .disabled("Z"), .enable("false")) multiplexer_3 (
    .in0(RS2), .in1({32{1'b0}}), .out(multiplexer_3_out), .sel(\气泡 ));
  Multiplexer #(.select(1), .width(32), .disabled("Z"), .enable("false")) multiplexer_4 (
    .in0(Imm32), .in1({32{1'b0}}), .out(multiplexer_4_out), .sel(\气泡 ));
  Multiplexer #(.select(1), .width(32), .disabled("Z"), .enable("false")) multiplexer_5 (
    .in0(IR), .in1({32{1'b0}}), .out(multiplexer_5_out), .sel(\气泡 ));
  Multiplexer #(.select(1), .width(32), .disabled("Z"), .enable("false")) multiplexer_6 (
    .in0(immb), .in1({32{1'b0}}), .out(multiplexer_6_out), .sel(\气泡 ));
  Multiplexer #(.select(1), .width(32), .disabled("Z"), .enable("false")) multiplexer_7 (
    .in0(immj), .in1({32{1'b0}}), .out(multiplexer_7_out), .sel(\气泡 ));
  Multiplexer #(.select(1), .width(16), .disabled("Z"), .enable("false")) multiplexer_8 (
    .in0({ControlBusIn, PredictJump, rs1Fwd, rs2Fwd, ALuSrc, MemWrite, MemToReg, RegWrite}),
    .in1({16{1'b0}}), .out(multiplexer_8_out), .sel(\气泡 ));
  Multiplexer #(.select(1), .width(5), .disabled("Z"), .enable("false")) multiplexer_9 (
    .in0(WriteReg_num), .in1({5{1'b0}}), .out(multiplexer_9_out), .sel(\气泡 ));
  Multiplexer #(.select(1), .width(4), .disabled("Z"), .enable("false")) multiplexer_10 (
    .in0(ALUOP), .in1(4'b0000), .out(multiplexer_10_out), .sel(\气泡 ));
  Multiplexer #(.select(1), .width(10), .disabled("Z"), .enable("false")) multiplexer_11 (
    .in0(\指令译码信号 ), .in1({10{1'b0}}), .out(multiplexer_11_out), .sel(\气泡 ));
  not not_1 (not_1_out, \EN_低电平有效 );
  Pull_Resistor #(.pull(0)) pull_resistor_4 (.node(\EN_低电平有效 ));
  Register #(.width(32), .trigger("rising"), .Select("low")) u_PC (
    .D(multiplexer_1_out), .en(not_1_out), .Q(PC_2), .clk(CLK));  // open: clr
  Register #(.width(32), .trigger("rising"), .Select("low")) register_1 (
    .D(multiplexer_2_out), .en(not_1_out), .Q(RS1_2), .clk(CLK));  // open: clr
  Register #(.width(32), .trigger("rising"), .Select("low")) register_2 (
    .D(multiplexer_3_out), .en(not_1_out), .Q(RS2_2), .clk(CLK));  // open: clr
  Register #(.width(32), .trigger("rising"), .Select("low")) register_3 (
    .D(multiplexer_4_out), .en(not_1_out), .Q(Imm32_2), .clk(CLK));  // open: clr
  Register #(.width(32), .trigger("rising"), .Select("low")) register_4 (
    .D(multiplexer_5_out), .en(not_1_out), .Q(IR_2), .clk(CLK));  // open: clr
  Register #(.width(32), .trigger("rising"), .Select("low")) register_5 (
    .D(multiplexer_6_out), .en(not_1_out), .Q(immb_2), .clk(CLK));  // open: clr
  Register #(.width(32), .trigger("rising"), .Select("low")) register_6 (
    .D(multiplexer_7_out), .en(not_1_out), .Q(immj_2), .clk(CLK));  // open: clr
  Register #(.width(16), .trigger("rising"), .Select("low")) register_7 (
    .D(multiplexer_8_out), .en(not_1_out),
    .Q({ControlBusOut, PredictJump_2, rs1Fwd_2, rs2Fwd_2, ALuSrc_2, MemWrite_2, MemToReg_2, RegWrite_2}),
    .clk(CLK));  // open: clr
  Register #(.width(5), .trigger("rising"), .Select("low")) register_8 (
    .D(multiplexer_9_out), .en(not_1_out), .Q(WriteReg_num_2), .clk(CLK));  // open: clr
  Register #(.width(4), .trigger("rising"), .Select("low")) register_9 (
    .D(multiplexer_10_out), .en(not_1_out), .Q(ALUOP_2), .clk(CLK));  // open: clr
  Register #(.width(10), .trigger("rising"), .Select("low")) register_10 (
    .D(multiplexer_11_out), .en(not_1_out), .Q(\指令译码信号_2 ), .clk(CLK));  // open: clr

  // Other names for the same wires on the sheet: ControlBusIn[8:0] = {PredictJump, rs1Fwd, rs2Fwd, ALuSrc, MemWrite, MemToReg, RegWrite};
  //   ControlBusOut[8:0] = {PredictJump_2, rs1Fwd_2, rs2Fwd_2, ALuSrc_2, MemWrite_2, MemToReg_2, RegWrite_2}

  // Notes on the sheet:
  //   EN_低电平有效: pull=down
  //   PC、IR都应该一致传送，方便调试保留引脚，自己决定是否使用
  //   保留引脚，自己决定是否使用
  //   指令译码信号汇总在一起传输（bne，beq，jal，jalr，ecall，uret等）
  //   分线器已经设置好了，需要用的复制即可
  //   请将控制器输出的所有指令译码信号通过分线器汇总在一起后进行传输，后段需要使用的时候直接用分线器从多位宽线缆引出即可
  //   控制信号汇总在一起，预留了位宽，需要增加引脚可以利用剩余的线缆进行连接
endmodule

// EX/MEM
module EX_MEM (
  input  [31:0] PC,
  input  [31:0] AluResult,
  input  RegWrite,
  input  MemToReg,
  input  MemWrite,
  input  [31:0] WriteData,
  input  [31:0] IR,
  input  [31:0] Reserved1,
  input  [31:0] Reserved2,
  input  [4:0] WriteReg_num,
  input  [9:0] \指令译码信号 ,
  input  halt,
  input  \气泡 ,
  input  \EN_低电平有效 ,
  input  CLK,
  output [31:0] PC_2,
  output [31:0] AluResult_2,
  output [31:0] WriteData_2,
  output [31:0] IR_2,
  output RegWrite_2,
  output MemToReg_2,
  output MemWrite_2,
  output [31:0] Reserved1_2,
  output [31:0] Reserved2_2,
  output [4:0] WriteReg_num_2,
  output [9:0] \指令译码信号_2 ,
  output halt_2
);

  wire multiplexer_10_out, not_1_out;
  wire [4:0] multiplexer_8_out;
  wire [9:0] multiplexer_9_out;
  wire [15:0] multiplexer_7_out;
  wire [15:3] ControlBusIn, ControlBusOut;
  wire [31:0] multiplexer_1_out, multiplexer_2_out, multiplexer_3_out, multiplexer_4_out, multiplexer_5_out,
       multiplexer_6_out;

  Pull_Resistor #(.pull(0)) pull_resistor_1 (.node({ControlBusIn, MemWrite, MemToReg, RegWrite}));
  Pull_Resistor #(.pull(0)) pull_resistor_2 (.node(\指令译码信号 ));
  Pull_Resistor #(.pull(0)) pull_resistor_3 (.node(\气泡 ));
  Multiplexer #(.select(1), .width(32), .disabled("Z"), .enable("false")) multiplexer_1 (
    .in0(PC), .in1({32{1'b0}}), .out(multiplexer_1_out), .sel(\气泡 ));
  Multiplexer #(.select(1), .width(32), .disabled("Z"), .enable("false")) multiplexer_2 (
    .in0(AluResult), .in1({32{1'b0}}), .out(multiplexer_2_out), .sel(\气泡 ));
  Multiplexer #(.select(1), .width(32), .disabled("Z"), .enable("false")) multiplexer_3 (
    .in0(WriteData), .in1({32{1'b0}}), .out(multiplexer_3_out), .sel(\气泡 ));
  Multiplexer #(.select(1), .width(32), .disabled("Z"), .enable("false")) multiplexer_4 (
    .in0(IR), .in1({32{1'b0}}), .out(multiplexer_4_out), .sel(\气泡 ));
  Multiplexer #(.select(1), .width(32), .disabled("Z"), .enable("false")) multiplexer_5 (
    .in0(Reserved1), .in1({32{1'b0}}), .out(multiplexer_5_out), .sel(\气泡 ));
  Multiplexer #(.select(1), .width(32), .disabled("Z"), .enable("false")) multiplexer_6 (
    .in0(Reserved2), .in1({32{1'b0}}), .out(multiplexer_6_out), .sel(\气泡 ));
  Multiplexer #(.select(1), .width(16), .disabled("Z"), .enable("false")) multiplexer_7 (
    .in0({ControlBusIn, MemWrite, MemToReg, RegWrite}), .in1({16{1'b0}}), .out(multiplexer_7_out), .sel(\气泡 ));
  Multiplexer #(.select(1), .width(5), .disabled("Z"), .enable("false")) multiplexer_8 (
    .in0(WriteReg_num), .in1({5{1'b0}}), .out(multiplexer_8_out), .sel(\气泡 ));
  Multiplexer #(.select(1), .width(10), .disabled("Z"), .enable("false")) multiplexer_9 (
    .in0(\指令译码信号 ), .in1({10{1'b0}}), .out(multiplexer_9_out), .sel(\气泡 ));
  Multiplexer #(.select(1), .width(1), .disabled("Z"), .enable("false")) multiplexer_10 (
    .in0(halt), .in1(1'b0), .out(multiplexer_10_out), .sel(\气泡 ));
  not not_1 (not_1_out, \EN_低电平有效 );
  Pull_Resistor #(.pull(0)) pull_resistor_4 (.node(\EN_低电平有效 ));
  Register #(.width(32), .trigger("rising"), .Select("low")) u_PC (
    .D(multiplexer_1_out), .en(not_1_out), .Q(PC_2), .clk(CLK));  // open: clr
  Register #(.width(32), .trigger("rising"), .Select("low")) register_1 (
    .D(multiplexer_2_out), .en(not_1_out), .Q(AluResult_2), .clk(CLK));  // open: clr
  Register #(.width(32), .trigger("rising"), .Select("low")) register_2 (
    .D(multiplexer_3_out), .en(not_1_out), .Q(WriteData_2), .clk(CLK));  // open: clr
  Register #(.width(32), .trigger("rising"), .Select("low")) register_3 (
    .D(multiplexer_4_out), .en(not_1_out), .Q(IR_2), .clk(CLK));  // open: clr
  Register #(.width(32), .trigger("rising"), .Select("low")) register_4 (
    .D(multiplexer_5_out), .en(not_1_out), .Q(Reserved1_2), .clk(CLK));  // open: clr
  Register #(.width(32), .trigger("rising"), .Select("low")) register_5 (
    .D(multiplexer_6_out), .en(not_1_out), .Q(Reserved2_2), .clk(CLK));  // open: clr
  Register #(.width(16), .trigger("rising"), .Select("low")) register_6 (
    .D(multiplexer_7_out), .en(not_1_out), .Q({ControlBusOut, MemWrite_2, MemToReg_2, RegWrite_2}), .clk(CLK));  // open: clr
  Register #(.width(5), .trigger("rising"), .Select("low")) register_7 (
    .D(multiplexer_8_out), .en(not_1_out), .Q(WriteReg_num_2), .clk(CLK));  // open: clr
  Register #(.width(10), .trigger("rising"), .Select("low")) register_8 (
    .D(multiplexer_9_out), .en(not_1_out), .Q(\指令译码信号_2 ), .clk(CLK));  // open: clr
  Register #(.width(1), .trigger("rising"), .Select("low")) register_9 (
    .D(multiplexer_10_out), .en(not_1_out), .Q(halt_2), .clk(CLK));  // open: clr

  // Other names for the same wires on the sheet: ControlBusIn[2:0] = {MemWrite, MemToReg, RegWrite};
  //   ControlBusOut[2:0] = {MemWrite_2, MemToReg_2, RegWrite_2}

  // Notes on the sheet:
  //   EN_低电平有效: pull=down
  //   保留引脚，自己决定是否使用
  //   PC、IR都应该一致传送，方便调试保留引脚，自己决定是否使用
  //   指令译码信号汇总在一起传输（bne，beq，jal，jalr，ecall，uret等）
  //   分线器已经设置好了，需要用的复制即可
  //   请将控制器输出的所有指令译码信号通过分线器汇总在一起后进行传输，后段需要使用的时候直接用分线器从多位宽线缆引出即可
endmodule

// MEM/WB
module MEM_WB (
  input  [31:0] PC,
  input  [31:0] AluResult,
  input  RegWrite,
  input  MemToReg,
  input  [31:0] MemData,
  input  [31:0] IR,
  input  [31:0] Reserved1,
  input  [31:0] Reserved2,
  input  [4:0] WriteReg_num,
  input  halt,
  input  [9:0] \指令译码信号 ,
  input  \气泡 ,
  input  \EN_低电平有效 ,
  input  CLK,
  output [31:0] PC_2,
  output [31:0] AluResult_2,
  output [31:0] MemData_2,
  output [31:0] IR_2,
  output RegWrite_2,
  output MemToReg_2,
  output [31:0] Reserved1_2,
  output [31:0] Reserved2_2,
  output [4:0] WriteReg_num_2,
  output out_24,
  output [9:0] \指令译码信号_2 
);

  wire and_1_out, multiplexer_9_out, not_1_out, not_2_out, not_3_out;
  wire [4:0] multiplexer_8_out;
  wire [9:0] multiplexer_10_out;
  wire [15:0] multiplexer_7_out, multiplexer_11_out;
  wire [15:2] ControlBusIn, ControlBusOut;
  wire [31:0] bit_extender_1_out, LH_DIN, multiplexer_1_out, multiplexer_2_out, multiplexer_3_out,
       multiplexer_4_out, multiplexer_5_out, multiplexer_6_out;

  Pull_Resistor #(.pull(0)) pull_resistor_1 (.node({ControlBusIn, MemToReg, RegWrite}));
  Pull_Resistor #(.pull(0)) pull_resistor_2 (.node(\指令译码信号 ));
  Pull_Resistor #(.pull(0)) pull_resistor_3 (.node(\气泡 ));
  Multiplexer #(.select(1), .width(32), .disabled("Z"), .enable("false")) multiplexer_1 (
    .in0(PC), .in1({32{1'b0}}), .out(multiplexer_1_out), .sel(\气泡 ));
  Multiplexer #(.select(1), .width(32), .disabled("Z"), .enable("false")) multiplexer_2 (
    .in0(AluResult), .in1({32{1'b0}}), .out(multiplexer_2_out), .sel(\气泡 ));
  Multiplexer #(.select(1), .width(32), .disabled("Z"), .enable("false")) multiplexer_3 (
    .in0(MemData), .in1({32{1'b0}}), .out(multiplexer_3_out), .sel(\气泡 ));
  Multiplexer #(.select(1), .width(32), .disabled("Z"), .enable("false")) multiplexer_4 (
    .in0(IR), .in1({32{1'b0}}), .out(multiplexer_4_out), .sel(\气泡 ));
  Multiplexer #(.select(1), .width(32), .disabled("Z"), .enable("false")) multiplexer_5 (
    .in0(Reserved1), .in1({32{1'b0}}), .out(multiplexer_5_out), .sel(\气泡 ));
  Multiplexer #(.select(1), .width(32), .disabled("Z"), .enable("false")) multiplexer_6 (
    .in0(Reserved2), .in1({32{1'b0}}), .out(multiplexer_6_out), .sel(\气泡 ));
  Multiplexer #(.select(1), .width(16), .disabled("Z"), .enable("false")) multiplexer_7 (
    .in0({ControlBusIn, MemToReg, RegWrite}), .in1({16{1'b0}}), .out(multiplexer_7_out), .sel(\气泡 ));
  Multiplexer #(.select(1), .width(5), .disabled("Z"), .enable("false")) multiplexer_8 (
    .in0(WriteReg_num), .in1({5{1'b0}}), .out(multiplexer_8_out), .sel(\气泡 ));
  Multiplexer #(.select(1), .width(1), .disabled("Z"), .enable("false")) multiplexer_9 (
    .in0(halt), .in1(1'b0), .out(multiplexer_9_out), .sel(\气泡 ));
  Multiplexer #(.select(1), .width(10), .disabled("Z"), .enable("false")) multiplexer_10 (
    .in0(\指令译码信号 ), .in1({10{1'b0}}), .out(multiplexer_10_out), .sel(\气泡 ));
  not not_1 (not_1_out, \EN_低电平有效 );
  Pull_Resistor #(.pull(0)) pull_resistor_4 (.node(\EN_低电平有效 ));
  Register #(.width(32), .trigger("rising"), .Select("low")) u_PC (
    .D(multiplexer_1_out), .en(not_1_out), .Q(PC_2), .clk(CLK));  // open: clr
  Register #(.width(32), .trigger("rising"), .Select("low")) register_1 (
    .D(multiplexer_2_out), .en(not_1_out), .Q(AluResult_2), .clk(CLK));  // open: clr
  Register #(.width(32), .trigger("rising"), .Select("low")) register_2 (
    .D(multiplexer_3_out), .en(not_1_out), .Q(LH_DIN), .clk(CLK));  // open: clr
  Register #(.width(32), .trigger("rising"), .Select("low")) register_3 (
    .D(multiplexer_4_out), .en(not_1_out), .Q(IR_2), .clk(CLK));  // open: clr
  Register #(.width(32), .trigger("rising"), .Select("low")) register_4 (
    .D(multiplexer_5_out), .en(not_1_out), .Q(Reserved1_2), .clk(CLK));  // open: clr
  Register #(.width(32), .trigger("rising"), .Select("low")) register_5 (
    .D(multiplexer_6_out), .en(not_1_out), .Q(Reserved2_2), .clk(CLK));  // open: clr
  Register #(.width(16), .trigger("rising"), .Select("low")) register_6 (
    .D(multiplexer_7_out), .en(not_1_out), .Q({ControlBusOut, MemToReg_2, RegWrite_2}), .clk(CLK));  // open: clr
  Register #(.width(5), .trigger("rising"), .Select("low")) register_7 (
    .D(multiplexer_8_out), .en(not_1_out), .Q(WriteReg_num_2), .clk(CLK));  // open: clr
  Register #(.width(1), .trigger("rising"), .Select("low")) register_8 (
    .D(multiplexer_9_out), .en(not_1_out), .Q(out_24), .clk(CLK));  // open: clr
  Register #(.width(10), .trigger("rising"), .Select("low")) register_9 (
    .D(multiplexer_10_out), .en(not_1_out), .Q(\指令译码信号_2 ), .clk(CLK));  // open: clr
  not not_2 (not_2_out, IR_2[13]);
  not not_3 (not_3_out, IR_2[14]);
  and and_1 (and_1_out, IR_2[12], not_2_out, not_3_out, MemToReg_2);
  Multiplexer #(.select(1), .width(16), .disabled("Z"), .enable("false")) multiplexer_11 (
    .in0(LH_DIN[15:0]), .in1(LH_DIN[31:16]), .out(multiplexer_11_out), .sel(AluResult_2[1]));
  assign bit_extender_1_out = {{16{multiplexer_11_out[15]}}, multiplexer_11_out};  // Bit_Extender bit_extender_1
  Multiplexer #(.select(1), .width(32), .disabled("Z"), .enable("false")) multiplexer_12 (
    .in0(LH_DIN), .in1(bit_extender_1_out), .out(MemData_2), .sel(and_1_out));

  // Other names for the same wires on the sheet: ControlBusIn[1:0] = {MemToReg, RegWrite};
  //   ControlBusOut[1:0] = {MemToReg_2, RegWrite_2}; LH_MTR = MemToReg_2; LH_ADDR[31:0] = AluResult_2;
  //   LH_DOUT[31:0] = MemData_2; LH_IR[31:0] = IR_2

  // Notes on the sheet:
  //   EN_低电平有效: pull=down
  //   保留引脚，自己决定是否使用
  //   PC、IR都应该一致传送，方便调试保留引脚，自己决定是否使用
  //   指令译码信号汇总在一起传输（bne，beq，jal，jalr，ecall，uret等）
  //   分线器已经设置好了，需要用的复制即可
  //   请将控制器输出的所有指令译码信号通过分线器汇总在一起后进行传输，后段需要使用的时候直接用分线器从多位宽线缆引出即可
endmodule

module \中断按键参考电路  (
  input  \同步清零信号 ,
  output \与中断屏蔽位与 
);

  wire \_1号中断_out , and_1_out, clock_1_out, d_ff_1_q, or_1_out, or_2_out;

  Clock #(.highDuration(1), .lowDuration(1)) clock_1 (.out(clock_1_out));
  Button \_1号中断  (.out(\_1号中断_out ));
  or or_1 (or_1_out, \与中断屏蔽位与 , d_ff_1_q);
  LED #(.active("true")) \_1号中断等待指示灯  (.in(or_1_out));
  D_Flip_Flop #(.trigger("rising"), .Pre_Clr_Positions("LEGACY"), .NegatePresetClear("false"), .enable("true"), .NewFFLayout("false")) d_ff_1 (
    .clk(\_1号中断_out ), .D(1'b1), .Q(d_ff_1_q), .reset(\与中断屏蔽位与 ));  // open: Qn, preset, en
  or or_2 (or_2_out, d_ff_1_q, \与中断屏蔽位与 );
  and and_1 (and_1_out, or_2_out, ~\同步清零信号 );  // AND_Gate
  D_Flip_Flop #(.trigger("rising"), .Pre_Clr_Positions("LEGACY"), .NegatePresetClear("false"), .enable("true"), .NewFFLayout("false")) IR1 (
    .clk(clock_1_out), .D(and_1_out), .Q(\与中断屏蔽位与 ));  // open: Qn, preset, en, reset

  // Notes on the sheet:
  //   中断信号采样参考电路
  //   Reset 
endmodule

module \单周期_单级中断  (
  input  IR1,
  input  IR2,
  input  IR3,
  output RegWrite,
  output MemWrite,
  output [31:0] PC,
  output [31:0] IR,
  output [31:0] RDin,
  output [31:0] MDin,
  output [31:0] LedData
);

  wire alu_1_equal, alu_1_out_6, and_1_out, and_2_out, and_3_out, and_5_out, and_6_out, and_7_out, and_8_out,
       and_9_out, and_10_out, branch, CLK, clock_1_out, comparator_1_eq, comparator_1_lt, comparator_2_eq,
       comparator_3_eq, comparator_4_eq, comparator_5_eq, comparator_6_eq, d_ff_1_q, d_ff_2_q, d_ff_3_q,
       d_ff_4_q, d_ff_5_q, d_ff_6_q, d_ff_7_q, d_ff_8_q, DASB, demultiplexer_1_out0, demultiplexer_1_out1,
       demultiplexer_1_out2, ecall, Go, halt, INT, IR1_t, IR2_t, IR3_t, IRA, IRB, IRC, MemToReg, nand_1_out,
       NextPC2Reg, not_1_out, not_2_out, not_3_out, not_4_out, or_4_out, or_5_out, or_6_out, or_7_out,
       or_9_out, or_14_out, riscv_probe_1_p2, RST, undriven, W1, W2, W3, \单周期硬布线控制器_1_alu_src ,
       \单周期硬布线控制器_1_beq , \单周期硬布线控制器_1_blt , \单周期硬布线控制器_1_bne , \单周期硬布线控制器_1_jal , \单周期硬布线控制器_1_jalr ,
       \单周期硬布线控制器_1_uret ;
  wire [1:0] priority_encoder_1_out, priority_encoder_2_out, priority_encoder_3_out, register_1_q,
       \单周期硬布线控制器_1_s_type ;
  wire [3:0] \单周期硬布线控制器_1_alu_op ;
  wire [4:0] multiplexer_4_out, multiplexer_5_out;
  wire [12:0] CNT_num;
  wire [15:0] multiplexer_12_out, \总周期数 ;
  wire [31:0] adder_2_out, adder_3_out, bit_extender_1_out, bit_extender_2_out, bit_extender_3_out,
       bit_extender_4_out, bit_extender_5_out, bit_extender_6_out, calc, EPC_q, LH_DIN, LH_DOUT,
       multiplexer_1_out, multiplexer_2_out, multiplexer_3_out, multiplexer_6_out, multiplexer_7_out,
       multiplexer_10_out, PC_4, R1, R2, SB, shifter_1_out, shifter_2_out, shifter_3_out, shifter_4_out,
       shifter_5_out;

  Button \u_继续运行  (.out(Go));
  Button _1 (.out(IRA));
  Button _2 (.out(IRB));
  Button _3 (.out(IRC));
  LED #(.active("true")) led_1 (.in(W1));
  LED #(.active("true")) led_2 (.in(W2));
  LED #(.active("true")) led_3 (.in(W3));
  Hex_Digit_Display hex_digit_display_1 (.value(LedData[31:28]));  // open: dp
  or or_1 (W1, d_ff_4_q, d_ff_1_q);
  or or_2 (W2, d_ff_5_q, d_ff_2_q);
  or or_3 (W3, d_ff_6_q, d_ff_3_q);
  Hex_Digit_Display hex_digit_display_2 (.value(LedData[27:24]));  // open: dp
  Hex_Digit_Display hex_digit_display_3 (.value(LedData[23:20]));  // open: dp
  D_Flip_Flop #(.trigger("rising"), .Pre_Clr_Positions("LEGACY"), .NegatePresetClear("false"), .enable("true"), .NewFFLayout("false")) d_ff_1 (
    .clk(IRA), .D(1'b1), .Q(d_ff_1_q), .reset(d_ff_4_q));  // open: Qn, preset, en
  D_Flip_Flop #(.trigger("rising"), .Pre_Clr_Positions("LEGACY"), .NegatePresetClear("false"), .enable("true"), .NewFFLayout("false")) d_ff_2 (
    .clk(IRB), .D(1'b1), .Q(d_ff_2_q), .reset(d_ff_5_q));  // open: Qn, preset, en
  D_Flip_Flop #(.trigger("rising"), .Pre_Clr_Positions("LEGACY"), .NegatePresetClear("false"), .enable("true"), .NewFFLayout("false")) d_ff_3 (
    .clk(IRC), .D(1'b1), .Q(d_ff_3_q), .reset(d_ff_6_q));  // open: Qn, preset, en
  Hex_Digit_Display hex_digit_display_4 (.value(LedData[15:12]));  // open: dp
  Hex_Digit_Display hex_digit_display_5 (.value(LedData[19:16]));  // open: dp
  or or_4 (or_4_out, d_ff_1_q, d_ff_4_q);
  or or_5 (or_5_out, d_ff_2_q, d_ff_5_q);
  or or_6 (or_6_out, d_ff_3_q, d_ff_6_q);
  Hex_Digit_Display hex_digit_display_6 (.value(LedData[7:4]));  // open: dp
  Hex_Digit_Display hex_digit_display_7 (.value(LedData[11:8]));  // open: dp
  // Probe on \总周期数 
  and and_1 (and_1_out, or_4_out, ~demultiplexer_1_out0);  // AND_Gate
  and and_2 (and_2_out, or_5_out, ~demultiplexer_1_out1);  // AND_Gate
  and and_3 (and_3_out, or_6_out, ~demultiplexer_1_out2);  // AND_Gate
  Hex_Digit_Display hex_digit_display_8 (.value(LedData[3:0]));  // open: dp
  D_Flip_Flop #(.trigger("rising"), .Pre_Clr_Positions("LEGACY"), .NegatePresetClear("false"), .enable("true"), .NewFFLayout("false")) d_ff_4 (
    .clk(CLK), .D(and_1_out), .Q(d_ff_4_q));  // open: Qn, preset, en, reset
  D_Flip_Flop #(.trigger("rising"), .Pre_Clr_Positions("LEGACY"), .NegatePresetClear("false"), .enable("true"), .NewFFLayout("false")) d_ff_5 (
    .clk(CLK), .D(and_2_out), .Q(d_ff_5_q));  // open: Qn, preset, en, reset
  D_Flip_Flop #(.trigger("rising"), .Pre_Clr_Positions("LEGACY"), .NegatePresetClear("false"), .enable("true"), .NewFFLayout("false")) d_ff_6 (
    .clk(CLK), .D(and_3_out), .Q(d_ff_6_q));  // open: Qn, preset, en, reset
  or or_7 (or_7_out, d_ff_4_q, d_ff_5_q, d_ff_6_q);
  Priority_Encoder #(.select(2), .disabled("Z")) priority_encoder_1 (
    .in0(d_ff_4_q), .in1(d_ff_5_q), .in2(d_ff_6_q), .out(priority_encoder_1_out));  // open: in3, gs, en_out, en_in
  Register #(.width(2), .trigger("rising"), .Select("low")) register_1 (
    .D(priority_encoder_1_out), .en(INT), .Q(register_1_q), .clk(CLK));  // open: clr
  Demultiplexer #(.select(2), .width(1), .tristate("false"), .disabled("Z"), .enable("false")) demultiplexer_1 (
    .out0(demultiplexer_1_out0), .out1(demultiplexer_1_out1), .out2(demultiplexer_1_out2),
    .in(\单周期硬布线控制器_1_uret ), .sel(register_1_q));  // open: out3
  or or_8 (IR1_t, IR1, IRA);
  or or_9 (or_9_out, \单周期硬布线控制器_1_uret , ~or_7_out);  // OR_Gate
  Multiplexer #(.select(2), .width(32), .disabled("Z"), .enable("false")) multiplexer_1 (
    .in0(32'h30ac), .in1(32'h31d0), .in2(32'h32b4), .out(multiplexer_1_out), .sel(priority_encoder_1_out));  // open: in3
  or or_10 (IR2_t, IR2, IRB);
  D_Flip_Flop #(.trigger("rising"), .Pre_Clr_Positions("ABOVE_BELOW"), .NegatePresetClear("false"), .enable("false"), .NewFFLayout("true")) d_ff_7 (
    .clk(CLK), .D(or_9_out), .Q(d_ff_7_q));  // open: Qn, preset, reset
  and and_4 (INT, d_ff_7_q, or_7_out);
  Priority_Encoder #(.select(2), .disabled("Z")) priority_encoder_2 (
    .in0(1'b1), .in1(INT), .in2(\单周期硬布线控制器_1_uret ), .out(priority_encoder_2_out));  // open: in3, gs, en_out, en_in
  Register #(.width(32), .trigger("rising"), .Select("low")) EPC (
    .D(multiplexer_3_out), .en(INT), .Q(EPC_q), .clk(CLK));  // open: clr
  Multiplexer #(.select(2), .width(32), .disabled("Z"), .enable("false")) multiplexer_2 (
    .in0(multiplexer_3_out), .in1(multiplexer_1_out), .in2(EPC_q), .out(multiplexer_2_out),
    .sel(priority_encoder_2_out));  // open: in3
  Multiplexer #(.select(2), .width(32), .disabled("Z"), .enable("false")) multiplexer_3 (
    .in0(PC_4), .in1(calc), .in2(adder_3_out), .in3(adder_2_out), .out(multiplexer_3_out),
    .sel(priority_encoder_3_out));
  not not_1 (not_1_out, halt);
  not not_2 (not_2_out, halt);
  or or_11 (IR3_t, IR3, IRC);
  Priority_Encoder #(.select(2), .disabled("Z")) priority_encoder_3 (
    .in0(1'b1), .in1(\单周期硬布线控制器_1_jalr ), .in2(\单周期硬布线控制器_1_jal ), .in3(branch), .out(priority_encoder_3_out));  // open: gs, en_out, en_in
  Adder #(.width(32)) adder_1 (.a(32'h4), .b(PC), .out(PC_4));  // open: cin, cout
  Register #(.width(32), .trigger("rising"), .Select("low")) u_PC (
    .D(multiplexer_2_out), .en(not_1_out), .Q(PC), .clk(CLK), .clr(RST));
  Counter #(.width(16), .max('hffff), .ongoal("wrap"), .trigger("rising"), .behavior("new")) counter_1 (
    .count(not_2_out), .Q(\总周期数 ), .clk(CLK));  // open: load, D, carry, clr, preset, down
  or or_12 (NextPC2Reg, \单周期硬布线控制器_1_jal , \单周期硬布线控制器_1_jalr );
  // RiscV_Probe riscv_probe_1: pin names not known; wires that end beside it: IR, riscv_probe_1_p2
  ROM #(.addrWidth(10), .dataWidth(32), .Select("high")) rom_1 (.addr(PC[11:2]), .data(IR));
  \单周期硬布线控制器  \u_单周期硬布线控制器_1  (
    .OP(IR[6:2]), .Funct({IR[30], IR[25], IR[14:12]}), .ALU_OP(\单周期硬布线控制器_1_alu_op ), .in_3(IR[21]),
    .uret(\单周期硬布线控制器_1_uret ), .MemToReg(MemToReg), .ecall(ecall), .MemWrite(MemWrite),
    .ALU_SRC(\单周期硬布线控制器_1_alu_src ), .RegWrite(RegWrite), .S_type(\单周期硬布线控制器_1_s_type [0]),
    .Beq(\单周期硬布线控制器_1_beq ), .Bne(\单周期硬布线控制器_1_bne ), .Jalr(\单周期硬布线控制器_1_jalr ), .JAL(\单周期硬布线控制器_1_jal ),
    .blt(\单周期硬布线控制器_1_blt ), .csrrsi(riscv_probe_1_p2), .dasb(DASB), .U_type(\单周期硬布线控制器_1_s_type [1]));  // open: csrrci
  assign bit_extender_1_out = {{20{IR[31]}}, IR[31:20]};  // Bit_Extender bit_extender_1
  assign bit_extender_2_out = {{20{IR[31]}}, {IR[31:25], IR[11:7]}};  // Bit_Extender bit_extender_2
  Multiplexer #(.select(1), .width(5), .disabled("Z"), .enable("false")) multiplexer_4 (
    .in0(IR[19:15]), .in1(5'b10001), .out(multiplexer_4_out), .sel(ecall));
  Multiplexer #(.select(1), .width(5), .disabled("Z"), .enable("false")) multiplexer_5 (
    .in0(IR[24:20]), .in1(5'b01010), .out(multiplexer_5_out), .sel(ecall));
  Multiplexer #(.select(2), .width(32), .disabled("Z"), .enable("false")) multiplexer_6 (
    .in0(bit_extender_1_out), .in1(bit_extender_2_out), .in2({IR[31:12], {12{1'b0}}}),
    .out(multiplexer_6_out), .sel(\单周期硬布线控制器_1_s_type ));  // open: in3
  assign bit_extender_3_out = {{20{IR[31]}}, {IR[31], IR[7], IR[30:25], IR[11:8]}};  // Bit_Extender bit_extender_3
  Shifter #(.width(32), .shift("ll")) shifter_1 (.in(bit_extender_3_out), .\dist (5'b00001), .out(shifter_1_out));
  assign bit_extender_4_out = {{12{IR[31]}}, {IR[31], IR[19:12], IR[20], IR[30:21]}};  // Bit_Extender bit_extender_4
  Shifter #(.width(32), .shift("ll")) shifter_2 (.in(bit_extender_4_out), .\dist (5'b00001), .out(shifter_2_out));
  D_Flip_Flop #(.trigger("high"), .Pre_Clr_Positions("LEGACY"), .NegatePresetClear("false"), .enable("true"), .NewFFLayout("false")) d_ff_8 (.Q(d_ff_8_q));  // open: clk, D, Qn, preset, en, reset
  // Probe on 13'hc
  Regifile regifile_1 (
    .Din(RDin), .Clk(CLK), .R1(R1), .R2(R2), .WE(RegWrite), .W_num(IR[11:7]), .R1_num(multiplexer_4_out),
    .R2_num(multiplexer_5_out));
  Comparator #(.width(13), .mode("twosComplement")) comparator_1 (
    .a(CNT_num), .b(13'hc), .eq(comparator_1_eq), .lt(comparator_1_lt));  // open: gt
  Clock #(.highDuration(1), .lowDuration(1)) clock_1 (.out(clock_1_out));
  Multiplexer #(.select(1), .width(32), .disabled("Z"), .enable("false")) multiplexer_7 (
    .in0(R2), .in1(multiplexer_6_out), .out(multiplexer_7_out), .sel(\单周期硬布线控制器_1_alu_src ));
  Multiplexer #(.select(2), .width(32), .disabled("Z"), .enable("false")) multiplexer_8 (
    .in0(calc), .in1(LH_DOUT), .in2(PC_4), .in3(multiplexer_6_out), .out(RDin), .sel({NextPC2Reg, MemToReg}));
  Adder #(.width(32)) adder_2 (.a(shifter_1_out), .b(PC), .out(adder_2_out));  // open: cin, cout
  Adder #(.width(32)) adder_3 (.a(shifter_2_out), .b(PC), .out(adder_3_out));  // open: cin, cout
  Counter #(.width(13), .max('h1fff), .ongoal("stay"), .trigger("rising"), .behavior("old")) counter_2 (
    .count(comparator_1_lt), .Q(CNT_num), .clk(clock_1_out));  // open: load, D, carry, clr, preset
  ALU alu_1 (
    .X(R1), .Y(multiplexer_7_out), .AluOP(\单周期硬布线控制器_1_alu_op ), .Equal(alu_1_equal), .Result(calc),
    .out_6(alu_1_out_6));  // open: Result_2, out_4
  Multiplexer #(.select(1), .width(32), .disabled("Z"), .enable("false")) multiplexer_9 (
    .in0(R2), .in1(SB), .out(MDin), .sel(DASB));
  nand nand_1 (nand_1_out, d_ff_8_q, comparator_1_eq);
  and and_5 (and_5_out, \单周期硬布线控制器_1_blt , ~alu_1_out_6);  // AND_Gate
  and and_6 (and_6_out, \单周期硬布线控制器_1_beq , alu_1_equal);
  and and_7 (and_7_out, \单周期硬布线控制器_1_bne , ~alu_1_equal);  // AND_Gate
  assign CLK = nand_1_out ? clock_1_out : 1'bz;  // Controlled_Buffer controlled_buffer_1
  Pull_Resistor #(.pull(1)) pull_resistor_1 (.node(CLK));
  or or_13 (branch, and_5_out, and_6_out, and_7_out);
  RAM #(.addrWidth(10), .dataWidth(32), .bus("separate"), .Select("high")) ram_1 (
    .addr(calc[11:2]), .din(MDin), .data(LH_DIN), .str(MemWrite), .clk(CLK), .ld(undriven));  // open: sel, clr
  assign bit_extender_5_out = {{24{1'b0}}, R2[7:0]};  // Bit_Extender bit_extender_5
  Shifter #(.width(32), .shift("ll")) shifter_3 (.in(bit_extender_5_out), .\dist (5'b01000), .out(shifter_3_out));
  Shifter #(.width(32), .shift("ll")) shifter_4 (.in(bit_extender_5_out), .\dist (5'b10000), .out(shifter_4_out));
  Shifter #(.width(32), .shift("ll")) shifter_5 (.in(bit_extender_5_out), .\dist (5'b11000), .out(shifter_5_out));
  Comparator #(.width(32), .mode("twosComplement")) comparator_2 (
    .a(R1), .b(32'h22), .eq(comparator_2_eq));  // open: gt, lt
  Comparator #(.width(16), .mode("twosComplement")) comparator_3 (
    .a(16'h43e), .b(\总周期数 ), .eq(comparator_3_eq));  // open: gt, lt
  Comparator #(.width(16), .mode("twosComplement")) comparator_4 (
    .a(\总周期数 ), .b(16'h1), .eq(comparator_4_eq));  // open: gt, lt
  Comparator #(.width(16), .mode("twosComplement")) comparator_5 (
    .a(\总周期数 ), .b(16'h4), .eq(comparator_5_eq));  // open: gt, lt
  Comparator #(.width(16), .mode("twosComplement")) comparator_6 (
    .a(\总周期数 ), .b(16'h7), .eq(comparator_6_eq));  // open: gt, lt
  Multiplexer #(.select(2), .width(32), .disabled("Z"), .enable("false")) multiplexer_10 (
    .in0(bit_extender_5_out), .in1(shifter_3_out), .in2(shifter_4_out), .in3(shifter_5_out),
    .out(multiplexer_10_out), .sel(calc[1:0]));
  and and_8 (and_8_out, ecall, ~comparator_2_eq);  // AND_Gate
  and and_9 (and_9_out, comparator_2_eq, ecall);
  or or_14 (or_14_out, comparator_3_eq, comparator_4_eq);
  Pull_Resistor #(.pull(0)) pull_resistor_2 (.node(IRA));
  assign IRA = or_14_out ? ~CLK : 1'bz;  // Controlled_Inverter controlled_inverter_1
  Pull_Resistor #(.pull(0)) pull_resistor_3 (.node(IRB));
  assign IRB = comparator_5_eq ? ~CLK : 1'bz;  // Controlled_Inverter controlled_inverter_2
  Pull_Resistor #(.pull(0)) pull_resistor_4 (.node(IRC));
  assign IRC = comparator_6_eq ? ~CLK : 1'bz;  // Controlled_Inverter controlled_inverter_3
  assign SB = multiplexer_10_out | LH_DIN;  // OR_Gate or_15, 32 bits wide
  Multiplexer #(.select(1), .width(1), .disabled("Z"), .enable("false")) multiplexer_11 (
    .in0(and_8_out), .in1(1'b0), .out(halt), .sel(Go));
  Register #(.width(32), .trigger("rising"), .Select("low")) register_2 (
    .D(R2), .en(and_9_out), .Q(LedData), .clk(CLK));  // open: clr
  not not_3 (not_3_out, IR[13]);
  not not_4 (not_4_out, IR[14]);
  and and_10 (and_10_out, IR[12], not_3_out, not_4_out, MemToReg);
  Multiplexer #(.select(1), .width(16), .disabled("Z"), .enable("false")) multiplexer_12 (
    .in0(LH_DIN[15:0]), .in1(LH_DIN[31:16]), .out(multiplexer_12_out), .sel(calc[1]));
  assign bit_extender_6_out = {{16{multiplexer_12_out[15]}}, multiplexer_12_out};  // Bit_Extender bit_extender_6
  Multiplexer #(.select(1), .width(32), .disabled("Z"), .enable("false")) multiplexer_13 (
    .in0(LH_DIN), .in1(bit_extender_6_out), .out(LH_DOUT), .sel(and_10_out));

  // Notes on the sheet:
  //   中断源
  //   中断等待指示
  //   总复位信号应将除ROM以外所有存储组件全部清零
  //   数码管输出
  //   数码管输出应该用寄存器锁存，否则显示数据只能一闪而过
  //   指令探针
  //   指令存储器
  //   contents of rom_1 (hex, n*v repeats v):
  //   7d000113 100413 1f41993 41f9d993 433 c00913 800b13 140413 f47413 800293 100313 499993 89e9b3 1300533
  //   2200893 73 406282b3 fe0294e3 140413 f00f93 1f47433 1c41413 800293 100313 49d993 89e9b3 1300533
  //   2200893 73 406282b3 fe0294e3 1c45413 406b0b33 b0463 f95ff06f 2b3 fff2c293 1029293 fff2e293 500533
  //   2200893 73 f5dff06f 1112023 410113 a12023 410113 812023 410113 1312023 410113 1412023 410113 1512023
  //   410113 1612023 410113 100b13 300a13 100a93 1600433 441413 14469b3 1300533 2200893 73 fe0416e3
  //   415a0a33 fe0a10e3 ffc10113 12b03 ffc10113 12a83 ffc10113 12a03 ffc10113 12983 ffc10113 12403
  //   ffc10113 12503 ffc10113 12883 1d80006f 1112023 410113 a12023 410113 812023 410113 1312023 410113
  //   1412023 410113 1512023 410113 1612023 410113 200b13 300a13 100a93 1600433 441413 14469b3 1300533
  //   2200893 73 fe0416e3 415a0a33 fe0a10e3 ffc10113 12b03 ffc10113 12a83 ffc10113 12a03 ffc10113 12983
  //   ffc10113 12403 ffc10113 12503 ffc10113 12883 1ec0006f 1112023 410113 a12023 410113 812023 410113
  //   1312023 410113 1412023 410113 1512023 410113 1612023 410113 300b13 300a13 100a93 1600433 441413
  //   14469b3 1300533 2200893 73 fe0416e3 415a0a33 fe0a10e3 ffc10113 12b03 ffc10113 12a83 ffc10113 12a03
  //   ffc10113 12983 ffc10113 12403 ffc10113 12503 ffc10113 12883 40006f 1112023 410113 a12023 410113
  //   812023 410113 1312023 410113 1412023 410113 1512023 410113 1612023 410113 f00a13 1400533 2200893 73
  //   fffa0a13 fe0a58e3 ffc10113 12b03 ffc10113 12a83 ffc10113 12a03 ffc10113 12983 ffc10113 12403
  //   ffc10113 12503 ffc10113 12883 200073 1112023 410113 a12023 410113 812023 410113 1312023 410113
  //   1412023 410113 1512023 410113 1612023 410113 100a93 300b13 800413 841413 7640413 1441413 800533
  //   2200893 73 800a13 41545433 41645433 800533 2200893 73 fffa0a13 fe0a14e3 ffc10113 12b03 ffc10113
  //   12a83 ffc10113 12a03 ffc10113 12983 ffc10113 12403 ffc10113 12503 ffc10113 12883 200073 1112023
  //   410113 a12023 410113 812023 410113 1312023 410113 1412023 410113 1512023 410113 1612023 410113 413
  //   1000a13 8400a93 8a9a93 83a8a93 400b13 8b1b13 4b0b13 8a9a93 82a8a93 8a9a93 81a8a93 8b1b13 4b0b13
  //   8b1b13 4b0b13 1542023 16a8ab3 440413 fffa0a13 fe0a18e3 2000a13 413 41a83 1500533 2200893 73 240413
  //   fffa0a13 fe0a14e3 ffc10113 12b03 ffc10113 12a83 ffc10113 12a03 ffc10113 12983 ffc10113 12403
  //   ffc10113 12503 ffc10113 12883 200073
  //   为方便自动评测，需要输出PC，IR，寄存器堆写如数据RDin
  //   指令字
  //   RAM写使能MemWrite、RAM写入数据MDin等信号
  //   JAL
  //   JALR
  //   URET
  //   BGEU
  //   CSR
  //   DASB
  //   Beq
  //   Bne
  //   MemToReg
  //   MemWrite
  //   AluOP
  //   AluSrcB
  //   RegWrite
  //   控制位
  //   暂停节拍，不能为0
  //   戳工具置1进入计数暂停模式，ctrl+k时钟自动运行到对应节拍暂停
  //   ctrl+k关闭时钟连续运行，将控制位置零，进入单步调试模式调试
  //   可计数暂停的时钟源
  //   数据存储器
  //   单级中断测试信号模拟器
endmodule

module \单周期_多级中断  (
  input  IR1,
  input  IR2,
  input  IR3,
  output RegWrite,
  output MemWrite,
  output [31:0] PC,
  output [31:0] IR,
  output [31:0] RDin,
  output [31:0] MDin,
  output [31:0] LedData
);

  wire alu_1_equal, alu_1_out_6, and_1_out, and_2_out, and_3_out, and_4_out, and_5_out, and_6_out, and_7_out,
       and_8_out, and_16_out, AUTO_IRQ1, AUTO_IRQ2, AUTO_IRQ3, AUTO_IRQ_EN, branch, CLK, clock_1_out,
       comparator_1_eq, comparator_1_lt, comparator_2_eq, comparator_3_eq, comparator_4_eq, comparator_5_eq,
       comparator_6_eq, comparator_7_eq, comparator_9_eq, CSRRCI, CSRRSI, d_ff_1_q, d_ff_2_q, d_ff_3_q,
       d_ff_4_q, d_ff_5_q, d_ff_6_q, d_ff_8_q, DASB, demultiplexer_1_out0, demultiplexer_1_out1,
       demultiplexer_1_out2, DEPTH_LT3, DEPTH_NONZERO, DEPTH_WE, DEPTH_ZERO, DO_URET, ecall, EPC_WE0,
       EPC_WE1, EPC_WE2, Go, halt, HIGHER_OK, IE, IE_CLEAR, IE_D, IE_KEEP, IE_MID, IE_SET, IE_SET_OR_OLD,
       INT, IRA, IRB, IRC, IRQ_GATE1, IRQ_GATE2, IRQ_GATE3, IRQ_GATE4, IRQ_VALID, IRQ_WE0, IRQ_WE1, IRQ_WE2,
       LOCAL_IRQ1, LOCAL_IRQ2, LOCAL_IRQ3, MAN_IRQ1, MAN_IRQ2, MAN_IRQ3, MemToReg, nand_1_out, NextPC2Reg,
       not_1_out, not_2_out, not_8_out, not_9_out, NOT_CSRRCI, NOT_URET, or_4_out, or_5_out, or_6_out,
       or_13_out, or_14_out, PRIO_OK, RST, undriven, URET_RAW, W1, W2, W3, \单周期硬布线控制器_1_alu_src ,
       \单周期硬布线控制器_1_beq , \单周期硬布线控制器_1_blt , \单周期硬布线控制器_1_bne , \单周期硬布线控制器_1_jal , \单周期硬布线控制器_1_jalr ;
  wire [1:0] adder_4_out, CUR_PRIO, DEPTH, IRQ0, IRQ1, IRQ2, IRQ_ID, multiplexer_15_out,
       priority_encoder_2_out, priority_encoder_3_out, \单周期硬布线控制器_1_s_type ;
  wire [3:0] \单周期硬布线控制器_1_alu_op ;
  wire [4:0] multiplexer_4_out, multiplexer_5_out;
  wire [12:0] CNT_num;
  wire [15:0] multiplexer_18_out, \总周期数 ;
  wire [31:0] adder_2_out, adder_3_out, bit_extender_1_out, bit_extender_2_out, bit_extender_3_out,
       bit_extender_4_out, bit_extender_5_out, bit_extender_6_out, calc, EPC0, EPC1, EPC2, EPC_CAPTURE,
       EPC_TOP, LH_DIN, LH_DOUT, multiplexer_1_out, multiplexer_2_out, multiplexer_6_out, multiplexer_7_out,
       multiplexer_10_out, PC_4, R1, R2, SB, shifter_1_out, shifter_2_out, shifter_3_out, shifter_4_out,
       shifter_5_out;

  Button \u_继续运行  (.out(Go));
  Button _1 (.out(MAN_IRQ1));
  Button _2 (.out(MAN_IRQ2));
  Button _3 (.out(MAN_IRQ3));
  LED #(.active("true")) led_1 (.in(W1));
  LED #(.active("true")) led_2 (.in(W2));
  LED #(.active("true")) led_3 (.in(W3));
  Hex_Digit_Display hex_digit_display_1 (.value(LedData[31:28]));  // open: dp
  Button u_RST (.out(RST));
  or or_1 (W1, d_ff_4_q, d_ff_1_q);
  or or_2 (W2, d_ff_5_q, d_ff_2_q);
  or or_3 (W3, d_ff_6_q, d_ff_3_q);
  Hex_Digit_Display hex_digit_display_2 (.value(LedData[27:24]));  // open: dp
  Hex_Digit_Display hex_digit_display_3 (.value(LedData[23:20]));  // open: dp
  D_Flip_Flop #(.trigger("rising"), .Pre_Clr_Positions("LEGACY"), .NegatePresetClear("false"), .enable("true"), .NewFFLayout("false")) d_ff_1 (
    .clk(IRA), .D(1'b1), .Q(d_ff_1_q), .reset(d_ff_4_q));  // open: Qn, preset, en
  D_Flip_Flop #(.trigger("rising"), .Pre_Clr_Positions("LEGACY"), .NegatePresetClear("false"), .enable("true"), .NewFFLayout("false")) d_ff_2 (
    .clk(IRB), .D(1'b1), .Q(d_ff_2_q), .reset(d_ff_5_q));  // open: Qn, preset, en
  D_Flip_Flop #(.trigger("rising"), .Pre_Clr_Positions("LEGACY"), .NegatePresetClear("false"), .enable("true"), .NewFFLayout("false")) d_ff_3 (
    .clk(IRC), .D(1'b1), .Q(d_ff_3_q), .reset(d_ff_6_q));  // open: Qn, preset, en
  Hex_Digit_Display hex_digit_display_4 (.value(LedData[15:12]));  // open: dp
  Hex_Digit_Display hex_digit_display_5 (.value(LedData[19:16]));  // open: dp
  or or_4 (or_4_out, d_ff_1_q, d_ff_4_q);
  or or_5 (or_5_out, d_ff_2_q, d_ff_5_q);
  or or_6 (or_6_out, d_ff_3_q, d_ff_6_q);
  Hex_Digit_Display hex_digit_display_6 (.value(LedData[11:8]));  // open: dp
  Hex_Digit_Display hex_digit_display_7 (.value(LedData[7:4]));  // open: dp
  // Probe on \总周期数 
  and and_1 (and_1_out, or_4_out, ~demultiplexer_1_out0);  // AND_Gate
  and and_2 (and_2_out, or_5_out, ~demultiplexer_1_out1);  // AND_Gate
  and and_3 (and_3_out, or_6_out, ~demultiplexer_1_out2);  // AND_Gate
  Hex_Digit_Display hex_digit_display_8 (.value(LedData[3:0]));  // open: dp
  D_Flip_Flop #(.trigger("rising"), .Pre_Clr_Positions("LEGACY"), .NegatePresetClear("false"), .enable("true"), .NewFFLayout("false")) d_ff_4 (
    .clk(CLK), .D(and_1_out), .Q(d_ff_4_q));  // open: Qn, preset, en, reset
  D_Flip_Flop #(.trigger("rising"), .Pre_Clr_Positions("LEGACY"), .NegatePresetClear("false"), .enable("true"), .NewFFLayout("false")) d_ff_5 (
    .clk(CLK), .D(and_2_out), .Q(d_ff_5_q));  // open: Qn, preset, en, reset
  D_Flip_Flop #(.trigger("rising"), .Pre_Clr_Positions("LEGACY"), .NegatePresetClear("false"), .enable("true"), .NewFFLayout("false")) d_ff_6 (
    .clk(CLK), .D(and_3_out), .Q(d_ff_6_q));  // open: Qn, preset, en, reset
  or or_7 (IRQ_VALID, d_ff_4_q, d_ff_5_q, d_ff_6_q);
  Priority_Encoder #(.select(2), .disabled("Z")) priority_encoder_1 (
    .in0(d_ff_4_q), .in1(d_ff_5_q), .in2(d_ff_6_q), .out(IRQ_ID));  // open: in3, gs, en_out, en_in
  Register #(.width(2), .trigger("rising"), .Select("low")) u_IRQ0 (
    .D(IRQ_ID), .en(IRQ_WE0), .Q(IRQ0), .clk(CLK), .clr(RST));
  Demultiplexer #(.select(2), .width(1), .tristate("false"), .disabled("Z"), .enable("false")) demultiplexer_1 (
    .out0(demultiplexer_1_out0), .out1(demultiplexer_1_out1), .out2(demultiplexer_1_out2), .in(DO_URET),
    .sel(CUR_PRIO));  // open: out3
  or or_8 (IRA, IR1, LOCAL_IRQ1);
  Multiplexer #(.select(2), .width(32), .disabled("Z"), .enable("false")) multiplexer_1 (
    .in0(32'h30ac), .in1(32'h31d8), .in2(32'h32e0), .out(multiplexer_1_out), .sel(IRQ_ID));  // open: in3
  or or_9 (IRB, IR2, LOCAL_IRQ2);
  D_Flip_Flop #(.trigger("rising"), .Pre_Clr_Positions("ABOVE_BELOW"), .NegatePresetClear("false"), .enable("false"), .NewFFLayout("true")) d_ff_7 (
    .clk(CLK), .D(IE_D), .Q(IE));  // open: Qn, preset, reset
  Priority_Encoder #(.select(2), .disabled("Z")) priority_encoder_2 (
    .in0(1'b1), .in1(INT), .in2(DO_URET), .out(priority_encoder_2_out));  // open: in3, gs, en_out, en_in
  Register #(.width(32), .trigger("rising"), .Select("low")) u_EPC0 (
    .D(EPC_CAPTURE), .en(EPC_WE0), .Q(EPC0), .clk(CLK), .clr(RST));
  Multiplexer #(.select(2), .width(32), .disabled("Z"), .enable("false")) multiplexer_2 (
    .in0(EPC_CAPTURE), .in1(multiplexer_1_out), .in2(EPC_TOP), .out(multiplexer_2_out),
    .sel(priority_encoder_2_out));  // open: in3
  Multiplexer #(.select(2), .width(32), .disabled("Z"), .enable("false")) multiplexer_3 (
    .in0(PC_4), .in1(calc), .in2(adder_3_out), .in3(adder_2_out), .out(EPC_CAPTURE),
    .sel(priority_encoder_3_out));
  not not_1 (not_1_out, halt);
  not not_2 (not_2_out, halt);
  or or_10 (IRC, IR3, LOCAL_IRQ3);
  Priority_Encoder #(.select(2), .disabled("Z")) priority_encoder_3 (
    .in0(1'b1), .in1(\单周期硬布线控制器_1_jalr ), .in2(\单周期硬布线控制器_1_jal ), .in3(branch), .out(priority_encoder_3_out));  // open: gs, en_out, en_in
  Adder #(.width(32)) adder_1 (.a(32'h4), .b(PC), .out(PC_4));  // open: cin, cout
  Register #(.width(32), .trigger("rising"), .Select("low")) u_PC (
    .D(multiplexer_2_out), .en(not_1_out), .Q(PC), .clk(CLK), .clr(RST));
  Counter #(.width(16), .max('hffff), .ongoal("wrap"), .trigger("rising"), .behavior("new")) counter_1 (
    .count(not_2_out), .Q(\总周期数 ), .clk(CLK));  // open: load, D, carry, clr, preset, down
  or or_11 (NextPC2Reg, \单周期硬布线控制器_1_jal , \单周期硬布线控制器_1_jalr );
  // RiscV_Probe riscv_probe_1: pin names not known; wires that end beside it: IR
  ROM #(.addrWidth(10), .dataWidth(32), .Select("high")) rom_1 (.addr(PC[11:2]), .data(IR));
  \单周期硬布线控制器  \u_单周期硬布线控制器_1  (
    .OP(IR[6:2]), .Funct({IR[30], IR[25], IR[14:12]}), .ALU_OP(\单周期硬布线控制器_1_alu_op ), .in_3(IR[21]),
    .uret(URET_RAW), .MemToReg(MemToReg), .ecall(ecall), .MemWrite(MemWrite),
    .ALU_SRC(\单周期硬布线控制器_1_alu_src ), .RegWrite(RegWrite), .S_type(\单周期硬布线控制器_1_s_type [0]),
    .Beq(\单周期硬布线控制器_1_beq ), .Bne(\单周期硬布线控制器_1_bne ), .Jalr(\单周期硬布线控制器_1_jalr ), .JAL(\单周期硬布线控制器_1_jal ),
    .blt(\单周期硬布线控制器_1_blt ), .csrrsi(CSRRSI), .dasb(DASB), .U_type(\单周期硬布线控制器_1_s_type [1]), .csrrci(CSRRCI));
  assign bit_extender_1_out = {{20{IR[31]}}, IR[31:20]};  // Bit_Extender bit_extender_1
  assign bit_extender_2_out = {{20{IR[31]}}, {IR[31:25], IR[11:7]}};  // Bit_Extender bit_extender_2
  Multiplexer #(.select(1), .width(5), .disabled("Z"), .enable("false")) multiplexer_4 (
    .in0(IR[19:15]), .in1(5'b10001), .out(multiplexer_4_out), .sel(ecall));
  Multiplexer #(.select(1), .width(5), .disabled("Z"), .enable("false")) multiplexer_5 (
    .in0(IR[24:20]), .in1(5'b01010), .out(multiplexer_5_out), .sel(ecall));
  Multiplexer #(.select(2), .width(32), .disabled("Z"), .enable("false")) multiplexer_6 (
    .in0(bit_extender_1_out), .in1(bit_extender_2_out), .in2({IR[31:12], {12{1'b0}}}),
    .out(multiplexer_6_out), .sel(\单周期硬布线控制器_1_s_type ));  // open: in3
  assign bit_extender_3_out = {{20{IR[31]}}, {IR[31], IR[7], IR[30:25], IR[11:8]}};  // Bit_Extender bit_extender_3
  Shifter #(.width(32), .shift("ll")) shifter_1 (.in(bit_extender_3_out), .\dist (5'b00001), .out(shifter_1_out));
  assign bit_extender_4_out = {{12{IR[31]}}, {IR[31], IR[19:12], IR[20], IR[30:21]}};  // Bit_Extender bit_extender_4
  Shifter #(.width(32), .shift("ll")) shifter_2 (.in(bit_extender_4_out), .\dist (5'b00001), .out(shifter_2_out));
  D_Flip_Flop #(.trigger("high"), .Pre_Clr_Positions("LEGACY"), .NegatePresetClear("false"), .enable("true"), .NewFFLayout("false")) d_ff_8 (.Q(d_ff_8_q));  // open: clk, D, Qn, preset, en, reset
  // Probe on 13'hc
  Regifile regifile_1 (
    .Din(RDin), .Clk(CLK), .R1(R1), .R2(R2), .WE(RegWrite), .W_num(IR[11:7]), .R1_num(multiplexer_4_out),
    .R2_num(multiplexer_5_out));
  Comparator #(.width(13), .mode("twosComplement")) comparator_1 (
    .a(CNT_num), .b(13'hc), .eq(comparator_1_eq), .lt(comparator_1_lt));  // open: gt
  Clock #(.highDuration(1), .lowDuration(1)) clock_1 (.out(clock_1_out));
  Multiplexer #(.select(1), .width(32), .disabled("Z"), .enable("false")) multiplexer_7 (
    .in0(R2), .in1(multiplexer_6_out), .out(multiplexer_7_out), .sel(\单周期硬布线控制器_1_alu_src ));
  Multiplexer #(.select(2), .width(32), .disabled("Z"), .enable("false")) multiplexer_8 (
    .in0(calc), .in1(LH_DOUT), .in2(PC_4), .in3(multiplexer_6_out), .out(RDin), .sel({NextPC2Reg, MemToReg}));
  Adder #(.width(32)) adder_2 (.a(shifter_1_out), .b(PC), .out(adder_2_out));  // open: cin, cout
  Adder #(.width(32)) adder_3 (.a(shifter_2_out), .b(PC), .out(adder_3_out));  // open: cin, cout
  Counter #(.width(13), .max('h1fff), .ongoal("stay"), .trigger("rising"), .behavior("old")) counter_2 (
    .count(comparator_1_lt), .Q(CNT_num), .clk(clock_1_out));  // open: load, D, carry, clr, preset
  ALU alu_1 (
    .X(R1), .Y(multiplexer_7_out), .AluOP(\单周期硬布线控制器_1_alu_op ), .Equal(alu_1_equal), .Result(calc),
    .out_6(alu_1_out_6));  // open: Result_2, out_4
  Multiplexer #(.select(1), .width(32), .disabled("Z"), .enable("false")) multiplexer_9 (
    .in0(R2), .in1(SB), .out(MDin), .sel(DASB));
  nand nand_1 (nand_1_out, d_ff_8_q, comparator_1_eq);
  and and_4 (and_4_out, \单周期硬布线控制器_1_blt , ~alu_1_out_6);  // AND_Gate
  and and_5 (and_5_out, \单周期硬布线控制器_1_beq , alu_1_equal);
  and and_6 (and_6_out, \单周期硬布线控制器_1_bne , ~alu_1_equal);  // AND_Gate
  assign CLK = nand_1_out ? clock_1_out : 1'bz;  // Controlled_Buffer controlled_buffer_1
  Pull_Resistor #(.pull(1)) pull_resistor_1 (.node(CLK));
  or or_12 (branch, and_4_out, and_5_out, and_6_out);
  RAM #(.addrWidth(10), .dataWidth(32), .bus("separate"), .Select("high")) ram_1 (
    .addr(calc[11:2]), .din(MDin), .data(LH_DIN), .str(MemWrite), .clk(CLK), .ld(undriven));  // open: sel, clr
  assign bit_extender_5_out = {{24{1'b0}}, R2[7:0]};  // Bit_Extender bit_extender_5
  Shifter #(.width(32), .shift("ll")) shifter_3 (.in(bit_extender_5_out), .\dist (5'b01000), .out(shifter_3_out));
  Shifter #(.width(32), .shift("ll")) shifter_4 (.in(bit_extender_5_out), .\dist (5'b10000), .out(shifter_4_out));
  Shifter #(.width(32), .shift("ll")) shifter_5 (.in(bit_extender_5_out), .\dist (5'b11000), .out(shifter_5_out));
  Comparator #(.width(32), .mode("twosComplement")) comparator_2 (
    .a(R1), .b(32'h22), .eq(comparator_2_eq));  // open: gt, lt
  Comparator #(.width(16), .mode("twosComplement")) comparator_3 (
    .a(\总周期数 ), .b(16'h7), .eq(comparator_3_eq));  // open: gt, lt
  Comparator #(.width(16), .mode("twosComplement")) comparator_4 (
    .a(\总周期数 ), .b(16'h241), .eq(comparator_4_eq));  // open: gt, lt
  Multiplexer #(.select(2), .width(32), .disabled("Z"), .enable("false")) multiplexer_10 (
    .in0(bit_extender_5_out), .in1(shifter_3_out), .in2(shifter_4_out), .in3(shifter_5_out),
    .out(multiplexer_10_out), .sel(calc[1:0]));
  and and_7 (and_7_out, ecall, ~comparator_2_eq);  // AND_Gate
  and and_8 (and_8_out, comparator_2_eq, ecall);
  Comparator #(.width(16), .mode("twosComplement")) comparator_5 (
    .a(16'h258), .b(\总周期数 ), .eq(comparator_5_eq));  // open: gt, lt
  or or_13 (or_13_out, comparator_5_eq, comparator_6_eq);
  Comparator #(.width(16), .mode("twosComplement")) comparator_6 (
    .a(\总周期数 ), .b(16'h1), .eq(comparator_6_eq));  // open: gt, lt
  Comparator #(.width(16), .mode("twosComplement")) comparator_7 (
    .a(\总周期数 ), .b(16'h4), .eq(comparator_7_eq));  // open: gt, lt
  or or_14 (or_14_out, comparator_3_eq, comparator_4_eq);
  assign SB = multiplexer_10_out | LH_DIN;  // OR_Gate or_15, 32 bits wide
  Multiplexer #(.select(1), .width(1), .disabled("Z"), .enable("false")) multiplexer_11 (
    .in0(and_7_out), .in1(1'b0), .out(halt), .sel(Go));
  Register #(.width(32), .trigger("rising"), .Select("low")) register_1 (
    .D(R2), .en(and_8_out), .Q(LedData), .clk(CLK), .clr(RST));
  Pull_Resistor #(.pull(0)) pull_resistor_2 (.node(AUTO_IRQ1));
  assign AUTO_IRQ1 = or_13_out ? ~CLK : 1'bz;  // Controlled_Inverter controlled_inverter_1
  Pull_Resistor #(.pull(0)) pull_resistor_3 (.node(AUTO_IRQ2));
  assign AUTO_IRQ2 = comparator_7_eq ? ~CLK : 1'bz;  // Controlled_Inverter controlled_inverter_2
  Pull_Resistor #(.pull(0)) pull_resistor_4 (.node(AUTO_IRQ3));
  assign AUTO_IRQ3 = or_14_out ? ~CLK : 1'bz;  // Controlled_Inverter controlled_inverter_3
  Pull_Resistor #(.pull(0)) pull_resistor_5 (.node(AUTO_IRQ_EN));
  // Switch #(.width(1)) AUTO_IRQ_EN: pin names not known; wires that end beside it: 1'b1, AUTO_IRQ_EN
  Multiplexer #(.select(1), .width(1), .disabled("Z"), .enable("false")) multiplexer_12 (
    .in0(MAN_IRQ1), .in1(AUTO_IRQ1), .out(LOCAL_IRQ1), .sel(AUTO_IRQ_EN));
  Multiplexer #(.select(1), .width(1), .disabled("Z"), .enable("false")) multiplexer_13 (
    .in0(MAN_IRQ2), .in1(AUTO_IRQ2), .out(LOCAL_IRQ2), .sel(AUTO_IRQ_EN));
  Multiplexer #(.select(1), .width(1), .disabled("Z"), .enable("false")) multiplexer_14 (
    .in0(MAN_IRQ3), .in1(AUTO_IRQ3), .out(LOCAL_IRQ3), .sel(AUTO_IRQ_EN));
  Demultiplexer #(.select(2), .width(1), .tristate("false"), .disabled("Z"), .enable("false")) demultiplexer_2 (
    .out0(EPC_WE0), .out1(EPC_WE1), .out2(EPC_WE2), .in(INT), .sel(DEPTH));  // open: out3
  Demultiplexer #(.select(2), .width(1), .tristate("false"), .disabled("Z"), .enable("false")) demultiplexer_3 (
    .out0(IRQ_WE0), .out1(IRQ_WE1), .out2(IRQ_WE2), .in(INT), .sel(DEPTH));  // open: out3
  Multiplexer #(.select(1), .width(2), .disabled("Z"), .enable("false")) multiplexer_15 (
    .in0(2'b11), .in1(2'b01), .out(multiplexer_15_out), .sel(INT));
  or or_16 (DEPTH_WE, INT, DO_URET);
  Register #(.width(2), .trigger("rising"), .Select("low")) u_DEPTH (
    .D(adder_4_out), .en(DEPTH_WE), .Q(DEPTH), .clk(CLK), .clr(RST));
  Adder #(.width(2)) adder_4 (.a(DEPTH), .b(multiplexer_15_out), .out(adder_4_out));  // open: cin, cout
  Register #(.width(32), .trigger("rising"), .Select("low")) u_EPC1 (
    .D(EPC_CAPTURE), .en(EPC_WE1), .Q(EPC1), .clk(CLK), .clr(RST));
  Register #(.width(32), .trigger("rising"), .Select("low")) u_EPC2 (
    .D(EPC_CAPTURE), .en(EPC_WE2), .Q(EPC2), .clk(CLK), .clr(RST));
  Register #(.width(2), .trigger("rising"), .Select("low")) u_IRQ1 (
    .D(IRQ_ID), .en(IRQ_WE1), .Q(IRQ1), .clk(CLK), .clr(RST));
  Register #(.width(2), .trigger("rising"), .Select("low")) u_IRQ2 (
    .D(IRQ_ID), .en(IRQ_WE2), .Q(IRQ2), .clk(CLK), .clr(RST));
  Multiplexer #(.select(2), .width(32), .disabled("Z"), .enable("false")) multiplexer_16 (
    .in0({32{1'b0}}), .in1(EPC0), .in2(EPC1), .in3(EPC2), .out(EPC_TOP), .sel(DEPTH));
  Multiplexer #(.select(2), .width(2), .disabled("Z"), .enable("false")) multiplexer_17 (
    .in0(2'b00), .in1(IRQ0), .in2(IRQ1), .in3(IRQ2), .out(CUR_PRIO), .sel(DEPTH));
  Comparator #(.width(2), .mode("unsigned")) comparator_8 (.a(IRQ_ID), .b(CUR_PRIO), .gt(HIGHER_OK));  // open: eq, lt
  Comparator #(.width(2), .mode("unsigned")) comparator_9 (.a(DEPTH), .b(2'b11), .eq(comparator_9_eq));  // open: gt, lt
  Comparator #(.width(2), .mode("unsigned")) comparator_10 (.a(DEPTH), .b(2'b00), .eq(DEPTH_ZERO));  // open: gt, lt
  not not_3 (DEPTH_LT3, comparator_9_eq);
  not not_4 (DEPTH_NONZERO, DEPTH_ZERO);
  and and_9 (IRQ_GATE1, IRQ_VALID, IE);
  not not_5 (NOT_URET, URET_RAW);
  and and_10 (DO_URET, URET_RAW, DEPTH_NONZERO);
  and and_11 (IRQ_GATE2, IRQ_GATE1, PRIO_OK);
  or or_17 (PRIO_OK, HIGHER_OK, DEPTH_ZERO);
  or or_18 (IE_CLEAR, INT, CSRRCI);
  or or_19 (IE_SET, CSRRSI, DO_URET);
  and and_12 (IRQ_GATE3, IRQ_GATE2, DEPTH_LT3);
  not not_6 (NOT_CSRRCI, CSRRCI);
  not not_7 (IE_KEEP, IE_CLEAR);
  or or_20 (IE_SET_OR_OLD, IE_SET, IE);
  and and_13 (IRQ_GATE4, IRQ_GATE3, NOT_URET);
  and and_14 (IE_MID, IE_KEEP, IE_SET_OR_OLD);
  and and_15 (INT, IRQ_GATE4, NOT_CSRRCI);
  or or_21 (IE_D, RST, IE_MID);
  not not_8 (not_8_out, IR[13]);
  not not_9 (not_9_out, IR[14]);
  and and_16 (and_16_out, IR[12], not_8_out, not_9_out, MemToReg);
  Multiplexer #(.select(1), .width(16), .disabled("Z"), .enable("false")) multiplexer_18 (
    .in0(LH_DIN[15:0]), .in1(LH_DIN[31:16]), .out(multiplexer_18_out), .sel(calc[1]));
  assign bit_extender_6_out = {{16{multiplexer_18_out[15]}}, multiplexer_18_out};  // Bit_Extender bit_extender_6
  Multiplexer #(.select(1), .width(32), .disabled("Z"), .enable("false")) multiplexer_19 (
    .in0(LH_DIN), .in1(bit_extender_6_out), .out(LH_DOUT), .sel(and_16_out));

  // Other names for the same wires on the sheet: TAKE_IRQ = INT

  // Notes on the sheet:
  //   中断源
  //   中断等待指示
  //   总复位信号应将除ROM以外所有存储组件全部清零
  //   数码管输出
  //   数码管输出应该用寄存器锁存，否则显示数据只能一闪而过
  //   指令存储器
  //   contents of rom_1 (hex, n*v repeats v):
  //   7d000113 100413 1f41993 41f9d993 433 c00913 800b13 140413 f47413 800293 100313 499993 89e9b3 1300533
  //   2200893 73 406282b3 fe0294e3 140413 f00f93 1f47433 1c41413 800293 100313 49d993 89e9b3 1300533
  //   2200893 73 406282b3 fe0294e3 1c45413 406b0b33 b0463 f95ff06f 2b3 fff2c293 1029293 fff2e293 500533
  //   2200893 73 f5dff06f 1112023 410113 a12023 410113 812023 410113 1312023 410113 1412023 410113 1512023
  //   410113 1612023 410113 40e073 100b13 300a13 100a93 1600433 441413 14469b3 1300533 2200893 73 fe0416e3
  //   415a0a33 fe0a10e3 40f073 ffc10113 12b03 ffc10113 12a83 ffc10113 12a03 ffc10113 12983 ffc10113 12403
  //   ffc10113 12503 ffc10113 12883 1e80006f 1112023 410113 a12023 410113 812023 410113 1312023 410113
  //   1412023 410113 1512023 410113 1612023 410113 40e073 200b13 300a13 100a93 1600433 441413 14469b3
  //   1300533 2200893 73 fe0416e3 415a0a33 fe0a10e3 40f073 ffc10113 12b03 ffc10113 12a83 ffc10113 12a03
  //   ffc10113 12983 ffc10113 12403 ffc10113 12503 ffc10113 12883 1f40006f 1112023 410113 a12023 410113
  //   812023 410113 1312023 410113 1412023 410113 1512023 410113 1612023 410113 40e073 300b13 300a13
  //   100a93 1600433 441413 14469b3 1300533 2200893 73 fe0416e3 415a0a33 fe0a10e3 40f073 ffc10113 12b03
  //   ffc10113 12a83 ffc10113 12a03 ffc10113 12983 ffc10113 12403 ffc10113 12503 ffc10113 12883 40006f
  //   1112023 410113 a12023 410113 812023 410113 1312023 410113 1412023 410113 1512023 410113 1612023
  //   410113 f00a13 1400533 2200893 73 fffa0a13 fe0a58e3 ffc10113 12b03 ffc10113 12a83 ffc10113 12a03
  //   ffc10113 12983 ffc10113 12403 ffc10113 12503 ffc10113 12883 200073 1112023 410113 a12023 410113
  //   812023 410113 1312023 410113 1412023 410113 1512023 410113 1612023 410113 100a93 300b13 800413
  //   841413 7640413 1441413 800533 2200893 73 800a13 41545433 41645433 800533 2200893 73 fffa0a13
  //   fe0a14e3 ffc10113 12b03 ffc10113 12a83 ffc10113 12a03 ffc10113 12983 ffc10113 12403 ffc10113 12503
  //   ffc10113 12883 200073 1112023 410113 a12023 410113 812023 410113 1312023 410113 1412023 410113
  //   1512023 410113 1612023 410113 413 1000a13 8400a93 8a9a93 83a8a93 400b13 8b1b13 4b0b13 8a9a93 82a8a93
  //   8a9a93 81a8a93 8b1b13 4b0b13 8b1b13 4b0b13 1542023 16a8ab3 440413 fffa0a13 fe0a18e3 2000a13 413
  //   41a83 1500533 2200893 73 240413 fffa0a13 fe0a14e3 ffc10113 12b03 ffc10113 12a83 ffc10113 12a03
  //   ffc10113 12983 ffc10113 12403 ffc10113 12503 ffc10113 12883 200073
  //   为方便自动评测，需要输出PC，IR，寄存器堆写如数据RDin
  //   指令字
  //   RAM写使能MemWrite、RAM写入数据MDin等信号
  //   JAL
  //   JALR
  //   URET
  //   BGEU
  //   CSR
  //   DASB
  //   Beq
  //   Bne
  //   MemToReg
  //   MemWrite
  //   AluOP
  //   AluSrcB
  //   RegWrite
  //   控制位
  //   暂停节拍，不能为0
  //   戳工具置1进入计数暂停模式，ctrl+k时钟自动运行到对应节拍暂停
  //   ctrl+k关闭时钟连续运行，将控制位置零，进入单步调试模式调试
  //   可计数暂停的时钟源
  //   数据存储器
  //   多级中断测试信号模拟器
  //   AUTO_IRQ_EN: 0=手动，1=自动
endmodule

module \封装正确性测试  (
);

  wire IR1, IR2, IR3, MemW, RegW;
  wire [31:0] EX_PC, ID_PC, IF_PC, IR, LED, MDin, MDinr, MEM_PC, PC, RDin, RDinr, WB_PC;

  \单周期RISC_V  \u_单周期risc_v_1  (
    .IR1(IR1), .IR2(IR2), .IR3(IR3), .RegWrite(RegW), .MemWrite(MemW), .PC(PC), .IR(IR), .RDin(RDin),
    .MDin(MDin), .LedData(LED));
  \气泡流水线  \u_气泡流水线_1  (
    .RegWrite(RegW), .MemWrite(MemW), .IF_PC(IF_PC), .ID_PC(ID_PC), .EX_PC(EX_PC), .M_PC(MEM_PC),
    .WB_PC(WB_PC), .RDin(RDinr), .MDin(MDinr), .LedData(LED));
  \单周期_单级中断  \u_单周期_单级中断_1  (
    .IR1(IR1), .IR2(IR2), .IR3(IR3), .RegWrite(RegW), .MemWrite(MemW), .PC(PC), .IR(IR), .RDin(RDin),
    .MDin(MDin), .LedData(LED));
  \理想流水线  \u_理想流水线_1  (
    .RegWrite(RegW), .MemWrite(MemW), .IF_PC(IF_PC), .ID_PC(ID_PC), .EX_PC(EX_PC), .M_PC(MEM_PC),
    .WB_PC(WB_PC), .RDin(RDinr), .MDin(MDinr), .LedData(LED));
  \重定向流水线  \u_重定向流水线_1  (
    .RegWrite(RegW), .MemWrite(MemW), .IF_PC(IF_PC), .ID_PC(ID_PC), .EX_PC(EX_PC), .M_PC(MEM_PC),
    .WB_PC(WB_PC), .RDin(RDinr), .MDin(MDinr), .LedData(LED));
  \单周期_多级中断  \u_单周期_多级中断_1  (
    .IR1(IR1), .IR2(IR2), .IR3(IR3), .RegWrite(RegW), .MemWrite(MemW), .PC(PC), .IR(IR), .RDin(RDin),
    .MDin(MDin), .LedData(LED));

  // Notes on the sheet:
  //   单周期封装测试
  //   气泡流水封装测试
  //   单周期+单级中断封装测试
  //   请检查上面封装有无位宽不匹配，引脚标签是否和连接的标签相对应，否则无法在educoder平台上正确测试
  //   理想流水封装测试
  //   重定向流水封装测试
  //   单周期+多级中断封装测试
endmodule

module \数据相关监测  (
  input  [4:0] rs1_id,
  input  [4:0] rs2_id,
  input  rs1_used,
  input  rs2_used,
  input  EX_RegWrite,
  input  MEM_RegWrite,
  input  EX_MemToReg,
  input  [4:0] EX_rd,
  input  [4:0] MEM_rd,
  output [1:0] rs1Fwd,
  output DataCorrelate,
  output [1:0] rs2Fwd,
  output LoadUse
);

  wire and_1_out, and_2_out, and_3_out, and_4_out, and_5_out, and_6_out, and_7_out, and_8_out, and_9_out,
       and_10_out, and_12_out, and_14_out, and_15_out, and_16_out, and_17_out, and_18_out, comparator_1_eq,
       comparator_2_eq, comparator_3_eq, comparator_4_eq, comparator_5_eq, comparator_6_eq, comparator_7_eq,
       comparator_8_eq, comparator_9_eq, comparator_10_eq, comparator_11_eq, comparator_12_eq, not_1_out,
       not_2_out, not_3_out, not_4_out, not_5_out, not_6_out, not_7_out, not_8_out;

  Comparator #(.width(5), .mode("twosComplement")) comparator_1 (
    .a(rs1_id), .b(EX_rd), .eq(comparator_1_eq));  // open: gt, lt
  Comparator #(.width(5), .mode("twosComplement")) comparator_2 (
    .a(rs1_id), .b(MEM_rd), .eq(comparator_2_eq));  // open: gt, lt
  Comparator #(.width(5), .mode("twosComplement")) comparator_3 (
    .a(rs2_id), .b(EX_rd), .eq(comparator_3_eq));  // open: gt, lt
  Comparator #(.width(5), .mode("twosComplement")) comparator_4 (
    .a(rs2_id), .b(MEM_rd), .eq(comparator_4_eq));  // open: gt, lt
  Comparator #(.width(5), .mode("twosComplement")) comparator_5 (
    .a(rs1_id), .b(EX_rd), .eq(comparator_5_eq));  // open: gt, lt
  Comparator #(.width(5), .mode("twosComplement")) comparator_6 (
    .a(rs2_id), .b(EX_rd), .eq(comparator_6_eq));  // open: gt, lt
  Comparator #(.width(5), .mode("twosComplement")) comparator_7 (
    .a({5{1'b0}}), .b(rs1_id), .eq(comparator_7_eq));  // open: gt, lt
  and and_1 (and_1_out, comparator_1_eq, EX_RegWrite);
  Comparator #(.width(5), .mode("twosComplement")) comparator_8 (
    .a({5{1'b0}}), .b(rs1_id), .eq(comparator_8_eq));  // open: gt, lt
  and and_2 (and_2_out, comparator_2_eq, MEM_RegWrite);
  Comparator #(.width(5), .mode("twosComplement")) comparator_9 (
    .a({5{1'b0}}), .b(rs2_id), .eq(comparator_9_eq));  // open: gt, lt
  and and_3 (and_3_out, comparator_3_eq, EX_RegWrite);
  Comparator #(.width(5), .mode("twosComplement")) comparator_10 (
    .a({5{1'b0}}), .b(rs2_id), .eq(comparator_10_eq));  // open: gt, lt
  and and_4 (and_4_out, comparator_4_eq, MEM_RegWrite);
  Comparator #(.width(5), .mode("twosComplement")) comparator_11 (
    .a({5{1'b0}}), .b(rs1_id), .eq(comparator_11_eq));  // open: gt, lt
  and and_5 (and_5_out, comparator_5_eq, EX_MemToReg);
  Comparator #(.width(5), .mode("twosComplement")) comparator_12 (
    .a({5{1'b0}}), .b(rs2_id), .eq(comparator_12_eq));  // open: gt, lt
  and and_6 (and_6_out, comparator_6_eq, EX_MemToReg);
  not not_1 (not_1_out, comparator_7_eq);
  and and_7 (and_7_out, not_1_out, and_1_out);
  not not_2 (not_2_out, comparator_8_eq);
  and and_8 (and_8_out, not_2_out, and_2_out);
  not not_3 (not_3_out, comparator_9_eq);
  and and_9 (and_9_out, not_3_out, and_3_out);
  not not_4 (not_4_out, comparator_10_eq);
  and and_10 (and_10_out, not_4_out, and_4_out);
  not not_5 (not_5_out, comparator_11_eq);
  not not_6 (not_6_out, comparator_12_eq);
  and and_11 (rs1Fwd[0], and_7_out, rs1_used);
  and and_12 (and_12_out, and_8_out, rs1_used);
  and and_13 (rs2Fwd[0], and_9_out, rs2_used);
  and and_14 (and_14_out, and_10_out, rs2_used);
  and and_15 (and_15_out, not_5_out, and_5_out);
  and and_16 (and_16_out, and_15_out, rs1_used);
  and and_17 (and_17_out, not_6_out, and_6_out);
  and and_18 (and_18_out, and_17_out, rs2_used);
  not not_7 (not_7_out, rs1Fwd[0]);
  or or_1 (DataCorrelate, rs1Fwd[0], and_12_out, rs2Fwd[0], and_14_out);
  not not_8 (not_8_out, rs2Fwd[0]);
  or or_2 (LoadUse, and_16_out, and_18_out);
  and and_19 (rs1Fwd[1], not_7_out, and_12_out);
  and and_20 (rs2Fwd[1], not_8_out, and_14_out);
endmodule

module \寄存器使用情况  (
  input  [4:0] OP,
  input  [4:0] Funct,
  output rs1_used,
  output rs2_used
);

  wire and_1_out, and_2_out, and_3_out, and_4_out, and_5_out, and_6_out, and_7_out, and_8_out, and_9_out,
       and_10_out, and_11_out, and_12_out, and_13_out, and_14_out, and_15_out, and_16_out, and_17_out,
       and_18_out, and_19_out, and_20_out, and_21_out, and_22_out, and_23_out, and_24_out, and_25_out,
       and_26_out, and_27_out, and_28_out, and_29_out, and_30_out, and_31_out, and_32_out, and_33_out,
       and_34_out, and_35_out, and_36_out, and_37_out, comparator_1_eq, comparator_2_eq, not_1_out,
       not_2_out, not_3_out, not_4_out, not_5_out, not_6_out, not_7_out, not_8_out, not_9_out, not_10_out,
       not_11_out, not_12_out, not_13_out, not_14_out, not_15_out, not_16_out, not_17_out, not_18_out,
       not_19_out, not_20_out, not_21_out, not_22_out, not_23_out, not_24_out, not_25_out, not_26_out,
       not_27_out, not_28_out, not_29_out, not_30_out, not_31_out, not_32_out, not_33_out, not_34_out,
       not_35_out, not_36_out, not_37_out, not_38_out, not_39_out, not_40_out, not_41_out, not_42_out,
       not_43_out, not_44_out, not_45_out, not_46_out, not_47_out, not_48_out, not_49_out, not_50_out,
       not_51_out, not_52_out, not_53_out, not_54_out, not_55_out, not_56_out, not_57_out, not_58_out,
       not_59_out, not_60_out, not_61_out, not_62_out, not_63_out, not_64_out, not_65_out, not_66_out,
       not_67_out, not_68_out, not_69_out, not_70_out, not_71_out, not_72_out, not_73_out, not_74_out,
       not_75_out, not_76_out, not_77_out, not_78_out, not_79_out, not_80_out, not_81_out, not_82_out,
       not_83_out, not_84_out, not_85_out, not_86_out, not_87_out, not_88_out, not_89_out, not_90_out,
       not_91_out, not_92_out, not_93_out, not_94_out, not_95_out, not_96_out, not_97_out, not_98_out,
       not_99_out, not_100_out, not_101_out, not_102_out, not_103_out, not_104_out, not_105_out, not_106_out,
       not_107_out, not_108_out, not_109_out, not_110_out, not_111_out, not_112_out, not_113_out,
       not_114_out, not_115_out, not_116_out, not_117_out, not_118_out, not_119_out, not_120_out,
       not_121_out, not_122_out, not_123_out, not_124_out, not_125_out, not_126_out, not_127_out,
       not_128_out, not_129_out, not_130_out, not_131_out, not_132_out, not_133_out, not_134_out,
       not_135_out, not_136_out, not_137_out, not_138_out, not_139_out, not_140_out, not_141_out,
       not_142_out, not_143_out, not_144_out, not_145_out, not_146_out, not_147_out, not_148_out,
       not_149_out, not_150_out, not_151_out, not_152_out, not_153_out, not_154_out, not_155_out,
       not_156_out, not_157_out, not_158_out, not_159_out, not_160_out, not_161_out, not_162_out,
       not_163_out, not_164_out, not_165_out, not_166_out, not_167_out, not_168_out, not_169_out,
       not_170_out, not_171_out, not_172_out, not_173_out, not_174_out, not_175_out, not_176_out,
       not_177_out, not_178_out, not_179_out, not_180_out, not_181_out, not_182_out, not_183_out,
       not_184_out, not_185_out, not_186_out, not_187_out, not_188_out, not_189_out, not_190_out,
       not_191_out, not_192_out, not_193_out, not_194_out, not_195_out, not_196_out, not_197_out,
       not_198_out, not_199_out, not_200_out, not_201_out, not_202_out, not_203_out, not_204_out,
       not_205_out, not_206_out, not_207_out, not_208_out, not_209_out, not_210_out, not_211_out,
       not_212_out, not_213_out, not_214_out, not_215_out, not_216_out, not_217_out, not_218_out,
       not_219_out, not_220_out, not_221_out, RegUse_IType, RegUse_Rs1Base, RegUse_Rs2Base, RegUse_Store,
       RegUse_UsesBoth, RegUse_UsesRs1Extra;

  not not_1 (not_1_out, Funct[4]);
  not not_2 (not_2_out, Funct[3]);
  not not_3 (not_3_out, Funct[2]);
  not not_4 (not_4_out, Funct[1]);
  not not_5 (not_5_out, Funct[0]);
  not not_6 (not_6_out, OP[4]);
  not not_7 (not_7_out, OP[1]);
  not not_8 (not_8_out, OP[0]);
  not not_9 (not_9_out, Funct[3]);
  not not_10 (not_10_out, Funct[2]);
  not not_11 (not_11_out, Funct[1]);
  not not_12 (not_12_out, Funct[0]);
  not not_13 (not_13_out, OP[4]);
  not not_14 (not_14_out, OP[1]);
  not not_15 (not_15_out, OP[0]);
  not not_16 (not_16_out, Funct[4]);
  not not_17 (not_17_out, Funct[3]);
  not not_18 (not_18_out, OP[4]);
  not not_19 (not_19_out, OP[1]);
  not not_20 (not_20_out, OP[0]);
  not not_21 (not_21_out, Funct[4]);
  not not_22 (not_22_out, Funct[3]);
  not not_23 (not_23_out, Funct[0]);
  not not_24 (not_24_out, OP[4]);
  not not_25 (not_25_out, OP[1]);
  not not_26 (not_26_out, OP[0]);
  not not_27 (not_27_out, Funct[4]);
  not not_28 (not_28_out, Funct[3]);
  not not_29 (not_29_out, Funct[2]);
  not not_30 (not_30_out, Funct[0]);
  not not_31 (not_31_out, OP[4]);
  not not_32 (not_32_out, OP[1]);
  not not_33 (not_33_out, OP[0]);
  not not_34 (not_34_out, Funct[4]);
  not not_35 (not_35_out, Funct[3]);
  not not_36 (not_36_out, Funct[2]);
  not not_37 (not_37_out, OP[4]);
  not not_38 (not_38_out, OP[1]);
  not not_39 (not_39_out, OP[0]);
  not not_40 (not_40_out, Funct[2]);
  not not_41 (not_41_out, Funct[1]);
  not not_42 (not_42_out, Funct[0]);
  not not_43 (not_43_out, OP[4]);
  not not_44 (not_44_out, OP[3]);
  not not_45 (not_45_out, OP[1]);
  not not_46 (not_46_out, OP[0]);
  not not_47 (not_47_out, OP[4]);
  not not_48 (not_48_out, OP[3]);
  not not_49 (not_49_out, OP[1]);
  not not_50 (not_50_out, OP[0]);
  not not_51 (not_51_out, Funct[0]);
  not not_52 (not_52_out, OP[4]);
  not not_53 (not_53_out, OP[3]);
  not not_54 (not_54_out, OP[1]);
  not not_55 (not_55_out, OP[0]);
  not not_56 (not_56_out, Funct[1]);
  not not_57 (not_57_out, Funct[0]);
  not not_58 (not_58_out, OP[4]);
  not not_59 (not_59_out, OP[3]);
  not not_60 (not_60_out, OP[1]);
  not not_61 (not_61_out, OP[0]);
  not not_62 (not_62_out, Funct[2]);
  not not_63 (not_63_out, Funct[0]);
  not not_64 (not_64_out, OP[4]);
  not not_65 (not_65_out, OP[3]);
  not not_66 (not_66_out, OP[1]);
  not not_67 (not_67_out, OP[0]);
  not not_68 (not_68_out, Funct[4]);
  not not_69 (not_69_out, Funct[3]);
  not not_70 (not_70_out, Funct[2]);
  not not_71 (not_71_out, Funct[1]);
  not not_72 (not_72_out, OP[4]);
  not not_73 (not_73_out, OP[3]);
  not not_74 (not_74_out, OP[1]);
  not not_75 (not_75_out, OP[0]);
  not not_76 (not_76_out, Funct[4]);
  not not_77 (not_77_out, Funct[3]);
  not not_78 (not_78_out, Funct[1]);
  not not_79 (not_79_out, OP[4]);
  not not_80 (not_80_out, OP[3]);
  not not_81 (not_81_out, OP[1]);
  not not_82 (not_82_out, OP[0]);
  not not_83 (not_83_out, Funct[3]);
  not not_84 (not_84_out, Funct[1]);
  not not_85 (not_85_out, OP[4]);
  not not_86 (not_86_out, OP[3]);
  not not_87 (not_87_out, OP[1]);
  not not_88 (not_88_out, OP[0]);
  not not_89 (not_89_out, Funct[2]);
  not not_90 (not_90_out, Funct[0]);
  not not_91 (not_91_out, OP[4]);
  not not_92 (not_92_out, OP[3]);
  not not_93 (not_93_out, OP[2]);
  not not_94 (not_94_out, OP[1]);
  not not_95 (not_95_out, OP[0]);
  not not_96 (not_96_out, Funct[2]);
  not not_97 (not_97_out, Funct[0]);
  not not_98 (not_98_out, OP[4]);
  not not_99 (not_99_out, OP[2]);
  not not_100 (not_100_out, OP[1]);
  not not_101 (not_101_out, OP[0]);
  not not_102 (not_102_out, Funct[4]);
  not not_103 (not_103_out, Funct[3]);
  not not_104 (not_104_out, Funct[2]);
  not not_105 (not_105_out, Funct[1]);
  not not_106 (not_106_out, Funct[0]);
  not not_107 (not_107_out, OP[1]);
  not not_108 (not_108_out, OP[0]);
  not not_109 (not_109_out, Funct[2]);
  not not_110 (not_110_out, Funct[1]);
  not not_111 (not_111_out, Funct[0]);
  not not_112 (not_112_out, OP[2]);
  not not_113 (not_113_out, OP[1]);
  not not_114 (not_114_out, OP[0]);
  not not_115 (not_115_out, Funct[2]);
  not not_116 (not_116_out, Funct[1]);
  not not_117 (not_117_out, OP[2]);
  not not_118 (not_118_out, OP[1]);
  not not_119 (not_119_out, OP[0]);
  not not_120 (not_120_out, Funct[2]);
  not not_121 (not_121_out, Funct[1]);
  not not_122 (not_122_out, Funct[0]);
  not not_123 (not_123_out, OP[2]);
  not not_124 (not_124_out, OP[1]);
  not not_125 (not_125_out, Funct[4]);
  not not_126 (not_126_out, Funct[3]);
  not not_127 (not_127_out, Funct[1]);
  not not_128 (not_128_out, OP[4]);
  not not_129 (not_129_out, OP[1]);
  not not_130 (not_130_out, OP[0]);
  not not_131 (not_131_out, OP[4]);
  not not_132 (not_132_out, OP[1]);
  not not_133 (not_133_out, Funct[2]);
  not not_134 (not_134_out, Funct[1]);
  not not_135 (not_135_out, OP[4]);
  not not_136 (not_136_out, OP[2]);
  not not_137 (not_137_out, OP[1]);
  not not_138 (not_138_out, OP[0]);
  not not_139 (not_139_out, Funct[0]);
  not not_140 (not_140_out, OP[2]);
  not not_141 (not_141_out, OP[1]);
  not not_142 (not_142_out, OP[0]);
  not not_143 (not_143_out, Funct[4]);
  not not_144 (not_144_out, Funct[3]);
  not not_145 (not_145_out, Funct[2]);
  not not_146 (not_146_out, Funct[1]);
  not not_147 (not_147_out, Funct[0]);
  not not_148 (not_148_out, OP[4]);
  not not_149 (not_149_out, OP[1]);
  not not_150 (not_150_out, OP[0]);
  not not_151 (not_151_out, Funct[3]);
  not not_152 (not_152_out, Funct[2]);
  not not_153 (not_153_out, Funct[1]);
  not not_154 (not_154_out, Funct[0]);
  not not_155 (not_155_out, OP[4]);
  not not_156 (not_156_out, OP[1]);
  not not_157 (not_157_out, OP[0]);
  not not_158 (not_158_out, Funct[4]);
  not not_159 (not_159_out, Funct[3]);
  not not_160 (not_160_out, OP[4]);
  not not_161 (not_161_out, OP[1]);
  not not_162 (not_162_out, OP[0]);
  not not_163 (not_163_out, Funct[4]);
  not not_164 (not_164_out, Funct[3]);
  not not_165 (not_165_out, Funct[0]);
  not not_166 (not_166_out, OP[4]);
  not not_167 (not_167_out, OP[1]);
  not not_168 (not_168_out, OP[0]);
  not not_169 (not_169_out, Funct[4]);
  not not_170 (not_170_out, Funct[3]);
  not not_171 (not_171_out, Funct[2]);
  not not_172 (not_172_out, Funct[0]);
  not not_173 (not_173_out, OP[4]);
  not not_174 (not_174_out, OP[1]);
  not not_175 (not_175_out, OP[0]);
  not not_176 (not_176_out, Funct[4]);
  not not_177 (not_177_out, Funct[3]);
  not not_178 (not_178_out, Funct[2]);
  not not_179 (not_179_out, OP[4]);
  not not_180 (not_180_out, OP[1]);
  not not_181 (not_181_out, OP[0]);
  not not_182 (not_182_out, Funct[2]);
  not not_183 (not_183_out, Funct[0]);
  not not_184 (not_184_out, OP[4]);
  not not_185 (not_185_out, OP[2]);
  not not_186 (not_186_out, OP[1]);
  not not_187 (not_187_out, OP[0]);
  not not_188 (not_188_out, Funct[4]);
  not not_189 (not_189_out, Funct[3]);
  not not_190 (not_190_out, Funct[2]);
  not not_191 (not_191_out, Funct[1]);
  not not_192 (not_192_out, Funct[0]);
  not not_193 (not_193_out, OP[1]);
  not not_194 (not_194_out, OP[0]);
  not not_195 (not_195_out, Funct[2]);
  not not_196 (not_196_out, Funct[1]);
  not not_197 (not_197_out, Funct[0]);
  not not_198 (not_198_out, OP[2]);
  not not_199 (not_199_out, OP[1]);
  not not_200 (not_200_out, OP[0]);
  not not_201 (not_201_out, Funct[2]);
  not not_202 (not_202_out, Funct[1]);
  not not_203 (not_203_out, OP[2]);
  not not_204 (not_204_out, OP[1]);
  not not_205 (not_205_out, OP[0]);
  not not_206 (not_206_out, Funct[4]);
  not not_207 (not_207_out, Funct[3]);
  not not_208 (not_208_out, Funct[1]);
  not not_209 (not_209_out, OP[4]);
  not not_210 (not_210_out, OP[1]);
  not not_211 (not_211_out, OP[0]);
  not not_212 (not_212_out, Funct[2]);
  not not_213 (not_213_out, Funct[1]);
  not not_214 (not_214_out, OP[4]);
  not not_215 (not_215_out, OP[2]);
  not not_216 (not_216_out, OP[1]);
  not not_217 (not_217_out, OP[0]);
  not not_218 (not_218_out, Funct[0]);
  not not_219 (not_219_out, OP[2]);
  not not_220 (not_220_out, OP[1]);
  not not_221 (not_221_out, OP[0]);
  and and_1 (and_1_out, not_1_out, not_2_out, not_3_out, not_4_out, not_5_out, not_6_out, OP[3], OP[2], not_7_out, not_8_out);
  and and_2 (and_2_out, Funct[4], not_9_out, not_10_out, not_11_out, not_12_out, not_13_out, OP[3], OP[2], not_14_out, not_15_out);
  and and_3 (and_3_out, not_16_out, not_17_out, Funct[2], Funct[1], Funct[0], not_18_out, OP[3], OP[2], not_19_out, not_20_out);
  and and_4 (and_4_out, not_21_out, not_22_out, Funct[2], Funct[1], not_23_out, not_24_out, OP[3], OP[2], not_25_out, not_26_out);
  and and_5 (and_5_out, not_27_out, not_28_out, not_29_out, Funct[1], not_30_out, not_31_out, OP[3], OP[2], not_32_out, not_33_out);
  and and_6 (and_6_out, not_34_out, not_35_out, not_36_out, Funct[1], Funct[0], not_37_out, OP[3], OP[2], not_38_out, not_39_out);
  and and_7 (and_7_out, not_40_out, not_41_out, not_42_out, not_43_out, not_44_out, OP[2], not_45_out, not_46_out);
  and and_8 (and_8_out, Funct[2], Funct[1], Funct[0], not_47_out, not_48_out, OP[2], not_49_out, not_50_out);
  and and_9 (and_9_out, Funct[2], Funct[1], not_51_out, not_52_out, not_53_out, OP[2], not_54_out, not_55_out);
  and and_10 (and_10_out, Funct[2], not_56_out, not_57_out, not_58_out, not_59_out, OP[2], not_60_out, not_61_out);
  and and_11 (and_11_out, not_62_out, Funct[1], not_63_out, not_64_out, not_65_out, OP[2], not_66_out, not_67_out);
  and and_12 (and_12_out, not_68_out, not_69_out, not_70_out, not_71_out, Funct[0], not_72_out, not_73_out, OP[2], not_74_out, not_75_out);
  and and_13 (and_13_out, not_76_out, not_77_out, Funct[2], not_78_out, Funct[0], not_79_out, not_80_out, OP[2], not_81_out, not_82_out);
  and and_14 (and_14_out, Funct[4], not_83_out, Funct[2], not_84_out, Funct[0], not_85_out, not_86_out, OP[2], not_87_out, not_88_out);
  and and_15 (and_15_out, not_89_out, Funct[1], not_90_out, not_91_out, not_92_out, not_93_out, not_94_out, not_95_out);
  and and_16 (and_16_out, not_96_out, Funct[1], not_97_out, not_98_out, OP[3], not_99_out, not_100_out, not_101_out);
  and and_17 (and_17_out, not_102_out, not_103_out, not_104_out, not_105_out, not_106_out, OP[4], OP[3], OP[2], not_107_out, not_108_out);
  and and_18 (and_18_out, not_109_out, not_110_out, not_111_out, OP[4], OP[3], not_112_out, not_113_out, not_114_out);
  and and_19 (and_19_out, not_115_out, not_116_out, Funct[0], OP[4], OP[3], not_117_out, not_118_out, not_119_out);
  and and_20 (and_20_out, not_120_out, not_121_out, not_122_out, OP[4], OP[3], not_123_out, not_124_out, OP[0]);
  and and_21 (and_21_out, not_125_out, not_126_out, Funct[2], not_127_out, Funct[0], not_128_out, OP[3], OP[2], not_129_out, not_130_out);
  and and_22 (and_22_out, not_131_out, OP[3], OP[2], not_132_out, OP[0]);
  and and_23 (and_23_out, not_133_out, not_134_out, Funct[0], not_135_out, OP[3], not_136_out, not_137_out, not_138_out);
  and and_24 (and_24_out, Funct[2], Funct[1], not_139_out, OP[4], OP[3], not_140_out, not_141_out, not_142_out);
  and and_25 (and_25_out, not_143_out, not_144_out, not_145_out, not_146_out, not_147_out, not_148_out, OP[3], OP[2], not_149_out, not_150_out);
  and and_26 (and_26_out, Funct[4], not_151_out, not_152_out, not_153_out, not_154_out, not_155_out, OP[3], OP[2], not_156_out, not_157_out);
  and and_27 (and_27_out, not_158_out, not_159_out, Funct[2], Funct[1], Funct[0], not_160_out, OP[3], OP[2], not_161_out, not_162_out);
  and and_28 (and_28_out, not_163_out, not_164_out, Funct[2], Funct[1], not_165_out, not_166_out, OP[3], OP[2], not_167_out, not_168_out);
  and and_29 (and_29_out, not_169_out, not_170_out, not_171_out, Funct[1], not_172_out, not_173_out, OP[3], OP[2], not_174_out, not_175_out);
  and and_30 (and_30_out, not_176_out, not_177_out, not_178_out, Funct[1], Funct[0], not_179_out, OP[3], OP[2], not_180_out, not_181_out);
  and and_31 (and_31_out, not_182_out, Funct[1], not_183_out, not_184_out, OP[3], not_185_out, not_186_out, not_187_out);
  and and_32 (and_32_out, not_188_out, not_189_out, not_190_out, not_191_out, not_192_out, OP[4], OP[3], OP[2], not_193_out, not_194_out);
  and and_33 (and_33_out, not_195_out, not_196_out, not_197_out, OP[4], OP[3], not_198_out, not_199_out, not_200_out);
  and and_34 (and_34_out, not_201_out, not_202_out, Funct[0], OP[4], OP[3], not_203_out, not_204_out, not_205_out);
  and and_35 (and_35_out, not_206_out, not_207_out, Funct[2], not_208_out, Funct[0], not_209_out, OP[3], OP[2], not_210_out, not_211_out);
  and and_36 (and_36_out, not_212_out, not_213_out, Funct[0], not_214_out, OP[3], not_215_out, not_216_out, not_217_out);
  and and_37 (and_37_out, Funct[2], Funct[1], not_218_out, OP[4], OP[3], not_219_out, not_220_out, not_221_out);
  or or_1 (RegUse_Rs2Base, and_25_out, and_26_out, and_27_out, and_28_out, and_29_out, and_30_out, and_31_out, and_32_out, and_33_out, and_34_out, and_35_out, and_36_out, and_37_out);
  or or_2 (RegUse_Rs1Base, and_1_out, and_2_out, and_3_out, and_4_out, and_5_out, and_6_out, and_7_out, and_8_out, and_9_out, and_10_out, and_11_out, and_12_out, and_13_out, and_14_out, and_15_out, and_16_out, and_17_out, and_18_out, and_19_out, and_20_out, and_21_out, and_22_out, and_23_out, and_24_out);
  Comparator #(.width(5), .mode("unsigned")) comparator_1 (.a(OP), .b(5'b01100), .eq(comparator_1_eq));  // open: gt, lt
  Comparator #(.width(5), .mode("unsigned")) comparator_2 (.a(OP), .b(5'b11000), .eq(comparator_2_eq));  // open: gt, lt
  Comparator #(.width(5), .mode("unsigned")) comparator_3 (.a(OP), .b(5'b00100), .eq(RegUse_IType));  // open: gt, lt
  Comparator #(.width(5), .mode("unsigned")) comparator_4 (.a(OP), .b(5'b01000), .eq(RegUse_Store));  // open: gt, lt
  or or_3 (RegUse_UsesBoth, comparator_1_eq, comparator_2_eq);
  or or_4 (RegUse_UsesRs1Extra, RegUse_IType, RegUse_Store);
  or or_5 (rs1_used, RegUse_Rs1Base, RegUse_UsesRs1Extra, RegUse_UsesBoth);
  or or_6 (rs2_used, RegUse_Rs2Base, RegUse_Store, RegUse_UsesBoth);

  // Other names for the same wires on the sheet: RegUse_OP[4:0] = OP; RegUse_Rs1Final = rs1_used;
  //   RegUse_Rs2Final = rs2_used
endmodule
module \中断地址保存  (
  input  [1:0] IRIN,
  input  URET,
  input  INT,
  input  CLK,
  output [1:0] IROUT
);

  wire or_1_out;
  wire [1:0] multiplexer_1_out, multiplexer_2_out, multiplexer_3_out, register_2_q, register_3_q;

  or or_1 (or_1_out, URET, INT);
  Multiplexer #(.select(1), .width(2), .disabled("Z"), .enable("false")) multiplexer_1 (
    .in0(IRIN), .in1(register_2_q), .out(multiplexer_1_out), .sel(URET));
  Register #(.width(2), .trigger("rising"), .Select("low")) register_1 (
    .D(multiplexer_1_out), .en(or_1_out), .Q(IROUT), .clk(CLK));  // open: clr
  Multiplexer #(.select(1), .width(2), .disabled("Z"), .enable("false")) multiplexer_2 (
    .in0(IROUT), .in1(register_3_q), .out(multiplexer_2_out), .sel(URET));
  Register #(.width(2), .trigger("rising"), .Select("low")) register_2 (
    .D(multiplexer_2_out), .en(or_1_out), .Q(register_2_q), .clk(CLK));  // open: clr
  Multiplexer #(.select(1), .width(2), .disabled("Z"), .enable("false")) multiplexer_3 (
    .in0(register_2_q), .in1(2'b00), .out(multiplexer_3_out), .sel(URET));
  Register #(.width(2), .trigger("rising"), .Select("low")) register_3 (
    .D(multiplexer_3_out), .en(or_1_out), .Q(register_3_q), .clk(CLK));  // open: clr
endmodule

module \断点地址保存  (
  input  [31:0] IRIN,
  input  URET,
  input  INT,
  input  CLK,
  output [31:0] IROUT
);

  wire or_1_out;
  wire [31:0] multiplexer_1_out, multiplexer_2_out, multiplexer_3_out, register_2_q, register_3_q;

  or or_1 (or_1_out, URET, INT);
  Multiplexer #(.select(1), .width(32), .disabled("Z"), .enable("false")) multiplexer_1 (
    .in0(IRIN), .in1(register_2_q), .out(multiplexer_1_out), .sel(URET));
  Register #(.width(32), .trigger("rising"), .Select("low")) register_1 (
    .D(multiplexer_1_out), .en(or_1_out), .Q(IROUT), .clk(CLK));  // open: clr
  Multiplexer #(.select(1), .width(32), .disabled("Z"), .enable("false")) multiplexer_2 (
    .in0(IROUT), .in1(register_3_q), .out(multiplexer_2_out), .sel(URET));
  Register #(.width(32), .trigger("rising"), .Select("low")) register_2 (
    .D(multiplexer_2_out), .en(or_1_out), .Q(register_2_q), .clk(CLK));  // open: clr
  Multiplexer #(.select(1), .width(32), .disabled("Z"), .enable("false")) multiplexer_3 (
    .in0(register_2_q), .in1({32{1'b0}}), .out(multiplexer_3_out), .sel(URET));
  Register #(.width(32), .trigger("rising"), .Select("low")) register_3 (
    .D(multiplexer_3_out), .en(or_1_out), .Q(register_3_q), .clk(CLK));  // open: clr
endmodule

module \动态分支预测流水线  (
  output RegWrite,
  output MemWrite,
  output [31:0] IF_PC,
  output [31:0] ID_PC,
  output [31:0] EX_PC,
  output [31:0] M_PC,
  output [31:0] WB_PC,
  output [31:0] RDin,
  output [31:0] MDin,
  output [31:0] LedData
);

  wire alu_1_equal, alu_1_out_6, and_1_out, and_2_out, and_5_out, and_6_out, and_7_out, and_8_out, and_9_out,
       and_10_out, and_11_out, and_12_out, and_13_out, BGEU, Branch, branch_conf, branchTaken, CLK,
       clock_1_out, comparator_1_eq, comparator_1_lt, comparator_2_eq, CSR, d_ff_1_q, DASB, ecall,
       ex_mem_1_halt_2, ex_mem_1_memtoreg_2, ex_mem_1_regwrite_2, EX_PredictErr, EX_PredictJump, Go, halt,
       id_ex_1_alusrc_2, id_ex_1_memtoreg_2, id_ex_1_memwrite_2, id_ex_1_regwrite_2, if_id_1_predictjump_2,
       IR1, IR2, IR3, JAL, Jal_t, JALR, Jalr_t, jump, LoadUse, mem_wb_1_out_24, nand_1_out, not_1_out,
       not_2_out, not_3_out, not_4_out, not_5_out, or_1_out, or_2_out, or_3_out, or_4_out, or_5_out,
       or_6_out, or_9_out, PredictJump, RST, S_type, URET, W1, W2, W3, \单周期硬布线控制器_1_alu_src ,
       \单周期硬布线控制器_1_memtoreg , \单周期硬布线控制器_1_memwrite , \单周期硬布线控制器_1_regwrite , \寄存器使用情况_1_rs1_used ,
       \寄存器使用情况_1_rs2_used ;
  wire [0:0] mem_wb_1_memtoreg_2;
  wire [1:0] id_ex_1_rs1fwd_2, id_ex_1_rs2fwd_2, \数据相关监测_1_rs1fwd , \数据相关监测_1_rs2fwd ;
  wire [3:0] id_ex_1_aluop_2, \单周期硬布线控制器_1_alu_op ;
  wire [4:0] ex_mem_1_writereg_num_2, id_ex_1_writereg_num_2, mem_wb_1_writereg_num_2, multiplexer_4_out,
       multiplexer_5_out;
  wire [8:0] \单周期硬布线控制器_1_beq ;
  wire [9:0] \ex_mem_1_指令译码信号_2 , \id_ex_1_指令译码信号_2 , \mem_wb_1_指令译码信号_2 ;
  wire [11:0] multiplexer_6_out;
  wire [12:0] CNT_num;
  wire [15:0] \LoadUse次数 , \总周期数 , \插入气泡数 , \无条件分支数 , \条件分支成功数 ;
  wire [31:0] adder_1_out, adder_3_out, adder_4_out, adder_5_out, and_3_out, and_4_out, bit_extender_1_out,
       bit_extender_2_out, bit_extender_3_out, bit_extender_4_out, BranchAddr, calc, EX_IR,
       ex_mem_1_aluresult_2, ex_mem_1_reserved1_2, ex_mem_1_reserved2_2, ex_mem_1_writedata_2,
       id_ex_1_imm32_2, id_ex_1_immb_2, id_ex_1_immj_2, id_ex_1_rs1_2, id_ex_1_rs2_2, ID_IR, IF_IR, IF_PC_4,
       IR, MEM_IR, mem_wb_1_aluresult_2, mem_wb_1_memdata_2, multiplexer_1_out, multiplexer_2_out,
       multiplexer_7_out, multiplexer_8_out, multiplexer_9_out, multiplexer_11_out, PCout, R1, ram_1_data,
       regifile_1_r2, SB, shifter_1_out, shifter_2_out, shifter_3_out, shifter_4_out, shifter_5_out, WB_IR;

  Button \u_总复位  (.out(RST));
  Button _1 (.out(IR1));
  Button _2 (.out(IR2));
  Button _3 (.out(IR3));
  // Probe on \总周期数 
  // Probe on \总周期数 
  Button \u_继续运行  (.out(Go));
  LED #(.active("true")) led_1 (.in(W1));
  LED #(.active("true")) led_2 (.in(W2));
  LED #(.active("true")) led_3 (.in(W3));
  Hex_Digit_Display hex_digit_display_1 (.value(LedData[31:28]));  // open: dp
  // Probe on IF_PC[19:0]
  // RiscV_Probe riscv_probe_1: pin names not known; wires that end beside it: IF_IR
  Hex_Digit_Display hex_digit_display_2 (.value(LedData[23:20]));  // open: dp
  Hex_Digit_Display hex_digit_display_3 (.value(LedData[27:24]));  // open: dp
  // Probe on ID_PC[19:0]
  // RiscV_Probe riscv_probe_2: pin names not known; wires that end beside it: ID_IR
  Adder #(.width(32)) adder_1 (.a(EX_PC), .b(32'h4), .out(adder_1_out));  // open: cin, cout
  or or_1 (or_1_out, branchTaken, and_1_out);
  and and_1 (and_1_out, Jal_t, ~Jalr_t);  // AND_Gate
  and and_2 (and_2_out, Jal_t, ~Jalr_t);  // AND_Gate
  Hex_Digit_Display hex_digit_display_4 (.value(LedData[15:12]));  // open: dp
  Hex_Digit_Display hex_digit_display_5 (.value(LedData[19:16]));  // open: dp
  assign and_3_out = calc & 32'hfffffffe;  // AND_Gate and_3, 32 bits wide
  or or_2 (or_2_out, Branch, and_2_out);
  Hex_Digit_Display hex_digit_display_6 (.value(LedData[7:4]));  // open: dp
  Hex_Digit_Display hex_digit_display_7 (.value(LedData[11:8]));  // open: dp
  // Probe on EX_PC[19:0]
  // RiscV_Probe riscv_probe_3: pin names not known; wires that end beside it: EX_IR
  \分支预测  \u_分支预测_1  (
    .CLK(CLK), .EX_Jalr(Jalr_t), .PC(IF_PC), .EX_PC(EX_PC), .EX_jalrAddr(and_3_out), .en(not_1_out),
    .EX_GuessJ(EX_PredictJump), .PC_4(IF_PC_4), .EX_PC_4(adder_1_out), .EX_JumpAddr(BranchAddr),
    .EX_BranchTaken(or_1_out), .EX_Branch(or_2_out), .IR(IF_IR), .PCout(PCout), .GuessJ(PredictJump),
    .Ex_PredictErr(EX_PredictErr));
  not not_1 (not_1_out, halt);
  Hex_Digit_Display hex_digit_display_8 (.value(LedData[3:0]));  // open: dp
  // Probe on \总周期数 
  // Probe on M_PC[19:0]
  // RiscV_Probe riscv_probe_4: pin names not known; wires that end beside it: MEM_IR
  // Probe on \总周期数 
  // Probe on \无条件分支数 
  // Probe on \条件分支成功数 
  // Probe on \插入气泡数 
  // Probe on \LoadUse次数 
  // Probe on IF_PC[11:0]
  // Probe on WB_PC[19:0]
  // RiscV_Probe riscv_probe_5: pin names not known; wires that end beside it: WB_IR
  // Probe on EX_PC[11:0]
  // Probe on ID_PC[11:0]
  Multiplexer #(.select(1), .width(32), .disabled("Z"), .enable("false")) multiplexer_1 (
    .in0(IF_PC_4), .in1(adder_4_out), .out(multiplexer_1_out), .sel(Jal_t));
  assign and_4_out = calc & 32'hfffffffe;  // AND_Gate and_4, 32 bits wide
  // Probe on M_PC[11:0]
  D_Flip_Flop #(.trigger("high"), .Pre_Clr_Positions("LEGACY"), .NegatePresetClear("false"), .enable("true"), .NewFFLayout("false")) d_ff_1 (.Q(d_ff_1_q));  // open: clk, D, Qn, preset, en, reset
  // Probe on 13'hc
  Multiplexer #(.select(1), .width(32), .disabled("Z"), .enable("false")) multiplexer_2 (
    .in0(multiplexer_1_out), .in1(and_4_out), .out(multiplexer_2_out), .sel(Jalr_t));
  Multiplexer #(.select(1), .width(32), .disabled("Z"), .enable("false")) multiplexer_3 (
    .in0(multiplexer_2_out), .in1(adder_3_out), .out(BranchAddr), .sel(Branch));
  // Probe on WB_PC[11:0]
  Comparator #(.width(13), .mode("twosComplement")) comparator_1 (
    .a(CNT_num), .b(13'hc), .eq(comparator_1_eq), .lt(comparator_1_lt));  // open: gt
  Clock #(.highDuration(1), .lowDuration(1)) clock_1 (.out(clock_1_out));
  nand nand_1 (nand_1_out, d_ff_1_q, comparator_1_eq);
  Counter #(.width(13), .max('h1fff), .ongoal("stay"), .trigger("rising"), .behavior("old")) counter_1 (
    .count(comparator_1_lt), .Q(CNT_num), .clk(clock_1_out));  // open: load, D, carry, clr, preset
  assign CLK = nand_1_out ? clock_1_out : 1'bz;  // Controlled_Buffer controlled_buffer_1
  Pull_Resistor #(.pull(1)) pull_resistor_1 (.node(CLK));
  not not_2 (not_2_out, or_3_out);
  or or_3 (or_3_out, LoadUse, halt);
  not not_3 (not_3_out, halt);
  Register #(.width(32), .trigger("rising"), .Select("low")) PC (
    .D(PCout), .en(not_2_out), .Q(IF_PC), .clk(CLK), .clr(RST));
  Counter #(.width(16), .max('hffff), .ongoal("wrap"), .trigger("rising"), .behavior("old")) counter_2 (
    .count(not_3_out), .Q(\总周期数 ), .clk(CLK));  // open: load, D, carry, clr, preset
  and and_5 (and_5_out, not_3_out, jump);
  or or_4 (or_4_out, EX_PredictErr, Jalr_t);
  Adder #(.width(32)) adder_2 (.a(IF_PC), .b(32'h4), .out(IF_PC_4));  // open: cin, cout
  Counter #(.width(16), .max('hffff), .ongoal("wrap"), .trigger("rising"), .behavior("old")) counter_3 (
    .count(and_5_out), .Q(\无条件分支数 ), .clk(CLK));  // open: load, D, carry, clr, preset
  or or_5 (or_5_out, halt, LoadUse);
  ROM #(.addrWidth(10), .dataWidth(32), .Select("low")) rom_1 (.addr(IF_PC[11:2]), .data(IF_IR));
  and and_6 (and_6_out, not_3_out, and_7_out);
  or or_6 (or_6_out, Branch, Jal_t);
  and and_7 (and_7_out, or_6_out, ~EX_PredictErr);  // AND_Gate
  IF_ID if_id_1 (
    .PredictJump(PredictJump), .IR(IF_IR), .\气泡 (or_4_out), .PredictJump_2(if_id_1_predictjump_2), .IR_2(IR),
    .\EN_低电平有效 (or_5_out), .CLK(CLK), .PC_2(ID_PC), .PC(IF_PC), .IR_3(ID_IR));
  Counter #(.width(16), .max('hffff), .ongoal("wrap"), .trigger("rising"), .behavior("old")) counter_4 (
    .count(and_6_out), .Q(\条件分支成功数 ), .clk(CLK));  // open: load, D, carry, clr, preset
  \数据相关监测  \u_数据相关监测_1  (
    .rs1_id(multiplexer_4_out), .rs2_id(multiplexer_5_out), .rs1_used(\寄存器使用情况_1_rs1_used ),
    .rs2_used(\寄存器使用情况_1_rs2_used ), .EX_RegWrite(id_ex_1_regwrite_2), .MEM_RegWrite(ex_mem_1_regwrite_2),
    .EX_MemToReg(id_ex_1_memtoreg_2), .EX_rd(id_ex_1_writereg_num_2), .MEM_rd(ex_mem_1_writereg_num_2),
    .rs1Fwd(\数据相关监测_1_rs1fwd ), .rs2Fwd(\数据相关监测_1_rs2fwd ), .LoadUse(LoadUse));  // open: DataCorrelate
  \寄存器使用情况  \u_寄存器使用情况_1  (
    .OP(IR[6:2]), .Funct({IR[30], IR[25], IR[14:12]}), .rs1_used(\寄存器使用情况_1_rs1_used ),
    .rs2_used(\寄存器使用情况_1_rs2_used ));
  and and_8 (and_8_out, not_3_out, LoadUse);
  Counter #(.width(16), .max('hffff), .ongoal("wrap"), .trigger("rising"), .behavior("old")) counter_5 (
    .count(and_8_out), .Q(\LoadUse次数 ), .clk(CLK));  // open: load, D, carry, clr, preset
  \单周期硬布线控制器  \u_单周期硬布线控制器_1  (
    .OP(IR[6:2]), .Funct({IR[30], IR[25], IR[14:12]}), .ALU_OP(\单周期硬布线控制器_1_alu_op ), .in_3(IR[21]),
    .uret(URET), .MemToReg(\单周期硬布线控制器_1_memtoreg ), .ecall(ecall), .MemWrite(\单周期硬布线控制器_1_memwrite ),
    .ALU_SRC(\单周期硬布线控制器_1_alu_src ), .RegWrite(\单周期硬布线控制器_1_regwrite ), .S_type(S_type),
    .Beq(\单周期硬布线控制器_1_beq [0]), .Bne(\单周期硬布线控制器_1_beq [1]), .Jalr(JALR), .JAL(JAL), .blt(BGEU), .csrrsi(CSR),
    .dasb(DASB));  // open: U_type, csrrci
  Multiplexer #(.select(1), .width(5), .disabled("Z"), .enable("false")) multiplexer_4 (
    .in0(IR[19:15]), .in1(5'b10001), .out(multiplexer_4_out), .sel(ecall));
  Multiplexer #(.select(1), .width(5), .disabled("Z"), .enable("false")) multiplexer_5 (
    .in0(IR[24:20]), .in1(5'b01010), .out(multiplexer_5_out), .sel(ecall));
  Multiplexer #(.select(1), .width(12), .disabled("Z"), .enable("false")) multiplexer_6 (
    .in0(IR[31:20]), .in1({IR[31:25], IR[11:7]}), .out(multiplexer_6_out), .sel(S_type));
  assign bit_extender_1_out = {{20{IR[31]}}, {IR[31], IR[7], IR[30:25], IR[11:8]}};  // Bit_Extender bit_extender_1
  assign bit_extender_2_out = {{12{IR[31]}}, {IR[31], IR[19:12], IR[20], IR[30:21]}};  // Bit_Extender bit_extender_2
  not not_4 (not_4_out, CLK);
  Regifile regifile_1 (
    .Din(RDin), .Clk(not_4_out), .R1(R1), .R2(regifile_1_r2), .WE(RegWrite), .W_num(mem_wb_1_writereg_num_2),
    .R1_num(multiplexer_4_out), .R2_num(multiplexer_5_out));
  assign bit_extender_3_out = {{20{multiplexer_6_out[11]}}, multiplexer_6_out};  // Bit_Extender bit_extender_3
  Shifter #(.width(32), .shift("ll")) shifter_1 (.in(bit_extender_1_out), .\dist (5'b00001), .out(shifter_1_out));
  Shifter #(.width(32), .shift("ll")) shifter_2 (.in(bit_extender_2_out), .\dist (5'b00001), .out(shifter_2_out));
  Priority_Encoder #(.select(2), .disabled("Z")) priority_encoder_1 (
    .in0(1'b1), .in1(Jalr_t), .in2(branchTaken), .in3(Jal_t));  // open: out, gs, en_out, en_in
  or or_7 (branch_conf, Jalr_t, Jal_t, branchTaken);
  or or_8 (branchTaken, and_9_out, and_10_out, and_11_out);
  and and_9 (and_9_out, \id_ex_1_指令译码信号_2 [5], ~alu_1_out_6);  // AND_Gate
  and and_10 (and_10_out, \id_ex_1_指令译码信号_2 [0], alu_1_equal);
  and and_11 (and_11_out, \id_ex_1_指令译码信号_2 [1], ~alu_1_equal);  // AND_Gate
  or or_9 (or_9_out, LoadUse, or_4_out);
  ID_EX id_ex_1 (
    .PC(ID_PC), .RS1(R1), .RS2(regifile_1_r2), .IR(IR), .WriteReg_num(IR[11:7]),
    .ALUOP(\单周期硬布线控制器_1_alu_op ), .\气泡 (or_9_out), .PC_2(EX_PC), .RS1_2(id_ex_1_rs1_2),
    .RS2_2(id_ex_1_rs2_2), .IR_2(EX_IR), .RegWrite_2(id_ex_1_regwrite_2), .MemToReg_2(id_ex_1_memtoreg_2),
    .MemWrite_2(id_ex_1_memwrite_2), .ALuSrc_2(id_ex_1_alusrc_2), .WriteReg_num_2(id_ex_1_writereg_num_2),
    .RegWrite(\单周期硬布线控制器_1_regwrite ), .MemToReg(\单周期硬布线控制器_1_memtoreg ), .MemWrite(\单周期硬布线控制器_1_memwrite ),
    .ALuSrc(\单周期硬布线控制器_1_alu_src ), .ALUOP_2(id_ex_1_aluop_2), .CLK(CLK), .immb_2(id_ex_1_immb_2),
    .immb(shifter_1_out), .Imm32_2(id_ex_1_imm32_2), .Imm32(bit_extender_3_out), .rs2Fwd_2(id_ex_1_rs2fwd_2),
    .rs1Fwd_2(id_ex_1_rs1fwd_2), .PredictJump_2(EX_PredictJump), .rs2Fwd(\数据相关监测_1_rs2fwd ),
    .rs1Fwd(\数据相关监测_1_rs1fwd ), .PredictJump(if_id_1_predictjump_2),
    .\指令译码信号 ({ecall, \单周期硬布线控制器_1_beq [8], DASB, CSR, BGEU, URET, JALR, JAL, \单周期硬布线控制器_1_beq [1:0]}),
    .\指令译码信号_2 ({\id_ex_1_指令译码信号_2 [9:4], Jalr_t, Jal_t, \id_ex_1_指令译码信号_2 [1:0]}), .immj(shifter_2_out),
    .immj_2(id_ex_1_immj_2), .\EN_低电平有效 (halt));
  Multiplexer #(.select(2), .width(32), .disabled("Z"), .enable("false")) multiplexer_7 (
    .in0(id_ex_1_rs1_2), .in1(ex_mem_1_aluresult_2), .in2(RDin), .out(multiplexer_7_out),
    .sel(id_ex_1_rs1fwd_2));  // open: in3
  Multiplexer #(.select(2), .width(32), .disabled("Z"), .enable("false")) multiplexer_8 (
    .in0(id_ex_1_rs2_2), .in1(ex_mem_1_aluresult_2), .in2(RDin), .out(multiplexer_8_out),
    .sel(id_ex_1_rs2fwd_2));  // open: in3
  Multiplexer #(.select(1), .width(32), .disabled("Z"), .enable("false")) multiplexer_9 (
    .in0(multiplexer_8_out), .in1(id_ex_1_imm32_2), .out(multiplexer_9_out), .sel(id_ex_1_alusrc_2));
  ALU alu_1 (
    .X(multiplexer_7_out), .Y(multiplexer_9_out), .AluOP(id_ex_1_aluop_2), .Equal(alu_1_equal),
    .Result(calc), .out_6(alu_1_out_6));  // open: Result_2, out_4
  not not_5 (not_5_out, comparator_2_eq);
  and and_12 (and_12_out, comparator_2_eq, \id_ex_1_指令译码信号_2 [9]);
  Adder #(.width(32)) adder_3 (.a(id_ex_1_immb_2), .b(EX_PC), .out(adder_3_out));  // open: cin, cout
  Adder #(.width(32)) adder_4 (.a(EX_PC), .b(id_ex_1_immj_2), .out(adder_4_out));  // open: cin, cout
  or or_10 (Branch, \id_ex_1_指令译码信号_2 [0], \id_ex_1_指令译码信号_2 [1], \id_ex_1_指令译码信号_2 [5]);
  and and_13 (and_13_out, not_5_out, \id_ex_1_指令译码信号_2 [9]);
  Register #(.width(32), .trigger("rising"), .Select("low")) register_1 (
    .D(multiplexer_8_out), .en(and_12_out), .Q(LedData), .clk(CLK));  // open: clr
  Comparator #(.width(32), .mode("twosComplement")) comparator_2 (
    .a(multiplexer_7_out), .b(32'h22), .eq(comparator_2_eq));  // open: gt, lt
  EX_MEM ex_mem_1 (
    .PC(EX_PC), .IR(EX_IR), .WriteReg_num(id_ex_1_writereg_num_2), .\气泡 (1'b0), .PC_2(M_PC), .IR_2(MEM_IR),
    .RegWrite_2(ex_mem_1_regwrite_2), .MemToReg_2(ex_mem_1_memtoreg_2), .MemWrite_2(MemWrite),
    .WriteReg_num_2(ex_mem_1_writereg_num_2), .RegWrite(id_ex_1_regwrite_2), .MemToReg(id_ex_1_memtoreg_2),
    .MemWrite(id_ex_1_memwrite_2), .\EN_低电平有效 (halt), .CLK(CLK), .Reserved1_2(ex_mem_1_reserved1_2),
    .Reserved1(id_ex_1_immb_2), .\指令译码信号 ({\id_ex_1_指令译码信号_2 [9:4], Jalr_t, Jal_t, \id_ex_1_指令译码信号_2 [1:0]}),
    .\指令译码信号_2 (\ex_mem_1_指令译码信号_2 ), .Reserved2(id_ex_1_immj_2), .Reserved2_2(ex_mem_1_reserved2_2),
    .WriteData(multiplexer_8_out), .WriteData_2(ex_mem_1_writedata_2), .AluResult(calc),
    .AluResult_2(ex_mem_1_aluresult_2), .halt(and_13_out), .halt_2(ex_mem_1_halt_2));
  Multiplexer #(.select(1), .width(32), .disabled("Z"), .enable("false")) multiplexer_10 (
    .in0(ex_mem_1_writedata_2), .in1(SB), .out(MDin), .sel(\ex_mem_1_指令译码信号_2 [7]));
  assign bit_extender_4_out = {{24{1'b0}}, ex_mem_1_writedata_2[7:0]};  // Bit_Extender bit_extender_4
  Shifter #(.width(32), .shift("ll")) shifter_3 (.in(bit_extender_4_out), .\dist (5'b01000), .out(shifter_3_out));
  Shifter #(.width(32), .shift("ll")) shifter_4 (.in(bit_extender_4_out), .\dist (5'b10000), .out(shifter_4_out));
  Shifter #(.width(32), .shift("ll")) shifter_5 (.in(bit_extender_4_out), .\dist (5'b11000), .out(shifter_5_out));
  RAM #(.addrWidth(10), .dataWidth(32), .bus("separate"), .Select("low")) ram_1 (
    .addr(ex_mem_1_aluresult_2[11:2]), .din(MDin), .data(ram_1_data), .str(MemWrite), .sel(1'b0), .clk(CLK),
    .ld(1'b1));  // open: clr
  Multiplexer #(.select(2), .width(32), .disabled("Z"), .enable("false")) multiplexer_11 (
    .in0(bit_extender_4_out), .in1(shifter_3_out), .in2(shifter_4_out), .in3(shifter_5_out),
    .out(multiplexer_11_out), .sel(ex_mem_1_aluresult_2[1:0]));
  MEM_WB mem_wb_1 (
    .PC(M_PC), .IR(MEM_IR), .WriteReg_num(ex_mem_1_writereg_num_2), .\气泡 (1'b0), .PC_2(WB_PC), .IR_2(WB_IR),
    .RegWrite_2(RegWrite), .MemToReg_2(mem_wb_1_memtoreg_2[0]), .WriteReg_num_2(mem_wb_1_writereg_num_2),
    .RegWrite(ex_mem_1_regwrite_2), .MemToReg(ex_mem_1_memtoreg_2), .\EN_低电平有效 (halt), .CLK(CLK),
    .Reserved1(ex_mem_1_reserved1_2), .\指令译码信号 (\ex_mem_1_指令译码信号_2 ), .\指令译码信号_2 (\mem_wb_1_指令译码信号_2 ),
    .Reserved2(ex_mem_1_reserved2_2), .MemData(ram_1_data), .MemData_2(mem_wb_1_memdata_2),
    .AluResult(ex_mem_1_aluresult_2), .AluResult_2(mem_wb_1_aluresult_2), .halt(ex_mem_1_halt_2),
    .out_24(mem_wb_1_out_24));  // open: Reserved1_2, Reserved2_2
  assign SB = multiplexer_11_out | ram_1_data;  // OR_Gate or_11, 32 bits wide
  Multiplexer #(.select(1), .width(1), .disabled("Z"), .enable("false")) multiplexer_12 (
    .in0(mem_wb_1_out_24), .in1(1'b0), .out(halt), .sel(Go));
  or or_12 (jump, \mem_wb_1_指令译码信号_2 [2], \mem_wb_1_指令译码信号_2 [3]);
  Adder #(.width(32)) adder_5 (.a(32'h4), .b(WB_PC), .out(adder_5_out));  // open: cin, cout
  Multiplexer #(.select(2), .width(32), .disabled("Z"), .enable("false")) multiplexer_13 (
    .in0(mem_wb_1_aluresult_2), .in1(mem_wb_1_memdata_2), .in2(adder_5_out), .out(RDin),
    .sel({jump, mem_wb_1_memtoreg_2[0]}));  // open: in3
  Multiplexer #(.select(1), .width(32), .disabled("Z"), .enable("false")) multiplexer_14 (
    .in0(mem_wb_1_aluresult_2), .in1(adder_5_out), .sel(\mem_wb_1_指令译码信号_2 [2]));  // open: out

  // Other names for the same wires on the sheet: rd[4:0] = IR[11:7]; MEM_PC[31:0] = M_PC

  // Notes on the sheet:
  //   中断源
  //   时空图监测，可删除
  //   中断等待指示
  //   数码管输出
  //   控制位
  //   流水调试日志用
  //   暂停节拍，不能为0
  //   戳工具置1进入计数暂停模式，ctrl+k时钟自动运行到对应节拍暂停
  //   ctrl+k关闭时钟连续运行，将控制位置零，进入单步调试模式调试
  //   可计数暂停的时钟源
  //   为方便自动评测，需要输出流水线各段保存的PC值，注意是PC不是PC+4，另外ID段寄存器写入信息，Mem段内存写入信息也要输出
  //   contents of rom_1 (hex, n*v repeats v):
  //   100493 100006f 100493 200913 300993 100006f 100493 200913 300993 100006f 100493 200913 300993
  //   100006f 100493 200913 300993 3c8000ef 100413 100493 1f49493 900533 2200893 73 24d493 48463 fedff06f
  //   900533 2200893 73 100493 249493 900533 2200893 73 48463 fedff06f 100493 1f49493 900533 2200893 73
  //   4034d493 900533 2200893 73 4044d493 900533 2200893 73 4044d493 900533 2200893 73 4044d493 900533
  //   2200893 73 4044d493 900533 2200893 73 4044d493 900533 2200893 73 4044d493 900533 2200893 73 4044d493
  //   900533 2200893 73 100413 1f41993 41f9d993 433 c00913 300b13 140413 f47413 800293 100313 499993
  //   89e9b3 1300533 2200893 73 406282b3 fe0294e3 140413 f00f93 1f47433 1c41413 800293 100313 49d993
  //   89e9b3 1300533 2200893 73 406282b3 fe0294e3 1c45413 406b0b33 b0463 f95ff06f 2b3 fff2c293 829293
  //   ff2e293 500533 2200893 73 fff00413 493 84a023 140413 448493 84a023 140413 448493 84a023 140413
  //   448493 84a023 140413 448493 84a023 140413 448493 84a023 140413 448493 84a023 140413 448493 84a023
  //   140413 448493 84a023 140413 448493 84a023 140413 448493 84a023 140413 448493 84a023 140413 448493
  //   84a023 140413 448493 84a023 140413 448493 84a023 140413 448493 84a023 140413 448493 140413 433
  //   3c00493 42983 4aa03 149a2b3 28663 134a023 1442023 ffc48493 fe9412e3 800533 2200893 73 440413 3c00493
  //   fc9416e3 a00893 73 100293 300313 800493 849493 7648493 1449493 900533 2200893 73 800e13 4054d4b3
  //   4064d4b3 900533 2200893 73 fffe0e13 fe0e14e3 a00893 73 fff00293 7700493 849493 7748493 900533
  //   2200893 73 1000e13 54c4b3 900533 2200893 73 fffe0e13 fe0e16e3 a00893 73 313 1000e13 8400493 849493
  //   8348493 400913 891913 490913 849493 8248493 849493 8148493 891913 490913 891913 490913 932023
  //   12484b3 430313 fffe0e13 fe0e18e3 2000e13 313 31483 900533 2200893 73 230313 fffe0e13 fe0e14e3 a00893
  //   73 f00493 900533 2200893 73 fff48493 fe04d8e3 a00893 73 413 140413 800533 2200893 73 240413 800533
  //   2200893 73 340413 800533 2200893 73 440413 800533 2200893 73 540413 800533 2200893 73 640413 800533
  //   2200893 73 740413 800533 2200893 73 840413 800533 2200893 2200893 73 8067
  //   指令字
  //   JALR
  //   URET
  //   b型
  //   j型
  //   Beq
  //   Bne
  //   MemToReg
  //   MemWrite
  //   AluOP
  //   AluSrcB
  //   RegWrite
endmodule

module BTB (
  input  [31:0] EX_PC,
  input  [1:0] NewJumpState,
  input  [1:0] JumpState,
  input  [31:0] PC,
  input  [31:0] BranchAddr,
  input  CLK,
  input  en,
  input  PCReady,
  input  StateReady,
  output [1:0] PredictJump,
  output [1:0] EX_PredictJump,
  output [31:0] JumpAddress,
  output Hit,
  output EX_Hit,
  output Miss
);

  wire and_1_out, and_2_out, and_3_out, and_4_out, and_5_out, and_6_out, and_7_out, and_8_out, and_9_out,
       and_10_out, and_11_out, and_12_out, and_13_out, and_14_out, and_15_out, and_16_out, and_17_out,
       and_18_out, and_19_out, and_20_out, and_21_out, and_22_out, and_23_out, and_24_out, and_41_out,
       and_42_out, comparator_1_eq, comparator_2_eq, comparator_3_eq, comparator_4_eq, comparator_5_eq,
       comparator_6_eq, comparator_7_eq, comparator_8_eq, comparator_9_eq, comparator_10_eq,
       comparator_11_eq, comparator_12_eq, comparator_13_eq, comparator_14_eq, comparator_15_eq,
       comparator_16_eq, E0, E1, E2, E3, E4, E5, E6, E7, EX_Miss, L0, L1, L2, L3, L4, L5, L6, L7, not_1_out,
       or_1_out, or_2_out, or_3_out, or_4_out, or_5_out, or_6_out, or_7_out, or_8_out, or_9_out, or_10_out,
       or_11_out, or_12_out, or_13_out, or_14_out, or_15_out, or_16_out, priority_encoder_1_en_out, S0, S1,
       S2, S3, S4, S5, S6, S7, Valid0, Valid1, Valid2, Valid3, Valid4, Valid5, Valid6, Valid7, W0, W1, W2,
       W3, W4, W5, W6, W7;
  wire [1:0] multiplexer_1_out, multiplexer_2_out, multiplexer_3_out, multiplexer_4_out, multiplexer_5_out,
       multiplexer_6_out, multiplexer_7_out, multiplexer_8_out, NewState0, NewState1, NewState2, NewState3,
       NewState4, NewState5, NewState6, NewState7, register_25_q, register_26_q, register_27_q,
       register_28_q, register_29_q, register_30_q, register_31_q, register_32_q, State0, State1, State2,
       State3, State4, State5, State6, State7;
  wire [2:0] max2x16_1_max_id, max2x16_2_max_id, max2x16_3_max_id, max2x16_4_max_id, max2x16_5_max_id,
       max2x16_6_max_id, max2x16_7_max_id, priority_encoder_1_out;
  wire [15:0] C0, C1, C2, C3, C4, C5, C6, C7, max2x16_1_max, max2x16_2_max, max2x16_3_max, max2x16_4_max,
       max2x16_5_max, max2x16_6_max;
  wire [31:0] register_17_q, register_18_q, register_19_q, register_20_q, register_21_q, register_22_q,
       register_23_q, register_24_q, Tag0, Tag1, Tag2, Tag3, Tag4, Tag5, Tag6, Tag7;

  Register #(.width(1), .trigger("rising"), .Select("low")) register_1 (
    .D(1'b1), .en(and_1_out), .Q(Valid0), .clk(CLK));  // open: clr
  and and_1 (and_1_out, W0, en);
  Register #(.width(1), .trigger("rising"), .Select("low")) register_2 (
    .D(1'b1), .en(and_2_out), .Q(Valid1), .clk(CLK));  // open: clr
  and and_2 (and_2_out, W1, en);
  Register #(.width(1), .trigger("rising"), .Select("low")) register_3 (
    .D(1'b1), .en(and_3_out), .Q(Valid2), .clk(CLK));  // open: clr
  and and_3 (and_3_out, W2, en);
  Register #(.width(1), .trigger("rising"), .Select("low")) register_4 (
    .D(1'b1), .en(and_4_out), .Q(Valid3), .clk(CLK));  // open: clr
  and and_4 (and_4_out, W3, en);
  Register #(.width(1), .trigger("rising"), .Select("low")) register_5 (
    .D(1'b1), .en(and_5_out), .Q(Valid4), .clk(CLK));  // open: clr
  and and_5 (and_5_out, W4, en);
  Register #(.width(1), .trigger("rising"), .Select("low")) register_6 (
    .D(1'b1), .en(and_6_out), .Q(Valid5), .clk(CLK));  // open: clr
  and and_6 (and_6_out, W5, en);
  Register #(.width(1), .trigger("rising"), .Select("low")) register_7 (
    .D(1'b1), .en(and_7_out), .Q(Valid6), .clk(CLK));  // open: clr
  and and_7 (and_7_out, W6, en);
  Register #(.width(1), .trigger("rising"), .Select("low")) register_8 (
    .D(1'b1), .en(and_8_out), .Q(Valid7), .clk(CLK));  // open: clr
  and and_8 (and_8_out, W7, en);
  Register #(.width(32), .trigger("rising"), .Select("low")) register_9 (
    .D(PC), .en(and_1_out), .Q(Tag0), .clk(CLK));  // open: clr
  Register #(.width(32), .trigger("rising"), .Select("low")) register_10 (
    .D(PC), .en(and_2_out), .Q(Tag1), .clk(CLK));  // open: clr
  Register #(.width(32), .trigger("rising"), .Select("low")) register_11 (
    .D(PC), .en(and_3_out), .Q(Tag2), .clk(CLK));  // open: clr
  Register #(.width(32), .trigger("rising"), .Select("low")) register_12 (
    .D(PC), .en(and_4_out), .Q(Tag3), .clk(CLK));  // open: clr
  Register #(.width(32), .trigger("rising"), .Select("low")) register_13 (
    .D(PC), .en(and_5_out), .Q(Tag4), .clk(CLK));  // open: clr
  Register #(.width(32), .trigger("rising"), .Select("low")) register_14 (
    .D(PC), .en(and_6_out), .Q(Tag5), .clk(CLK));  // open: clr
  Register #(.width(32), .trigger("rising"), .Select("low")) register_15 (
    .D(PC), .en(and_7_out), .Q(Tag6), .clk(CLK));  // open: clr
  Register #(.width(32), .trigger("rising"), .Select("low")) register_16 (
    .D(PC), .en(and_8_out), .Q(Tag7), .clk(CLK));  // open: clr
  Counter #(.width(16), .max('hffff), .ongoal("wrap"), .trigger("rising"), .behavior("new")) counter_1 (
    .load(W0), .D({16{1'b0}}), .Q(C0), .clk(CLK), .clr(and_9_out), .down(or_1_out));  // open: count, carry, preset
  or or_1 (or_1_out, ~Valid0, Hit);  // OR_Gate
  and and_9 (and_9_out, L0, en);
  Counter #(.width(16), .max('hffff), .ongoal("wrap"), .trigger("rising"), .behavior("new")) counter_2 (
    .load(W1), .D({16{1'b0}}), .Q(C1), .clk(CLK), .clr(and_10_out), .down(or_2_out));  // open: count, carry, preset
  or or_2 (or_2_out, ~Valid1, Hit);  // OR_Gate
  and and_10 (and_10_out, L1, en);
  Counter #(.width(16), .max('hffff), .ongoal("wrap"), .trigger("rising"), .behavior("new")) counter_3 (
    .load(W2), .D({16{1'b0}}), .Q(C2), .clk(CLK), .clr(and_11_out), .down(or_3_out));  // open: count, carry, preset
  or or_3 (or_3_out, ~Valid2, Hit);  // OR_Gate
  and and_11 (and_11_out, L2, en);
  Counter #(.width(16), .max('hffff), .ongoal("wrap"), .trigger("rising"), .behavior("new")) counter_4 (
    .load(W3), .D({16{1'b0}}), .Q(C3), .clk(CLK), .clr(and_12_out), .down(or_4_out));  // open: count, carry, preset
  or or_4 (or_4_out, ~Valid3, Hit);  // OR_Gate
  and and_12 (and_12_out, L3, en);
  Counter #(.width(16), .max('hffff), .ongoal("wrap"), .trigger("rising"), .behavior("new")) counter_5 (
    .load(W4), .D({16{1'b0}}), .Q(C4), .clk(CLK), .clr(and_13_out), .down(or_5_out));  // open: count, carry, preset
  or or_5 (or_5_out, ~Valid4, Hit);  // OR_Gate
  and and_13 (and_13_out, L4, en);
  Counter #(.width(16), .max('hffff), .ongoal("wrap"), .trigger("rising"), .behavior("new")) counter_6 (
    .load(W5), .D({16{1'b0}}), .Q(C5), .clk(CLK), .clr(and_14_out), .down(or_6_out));  // open: count, carry, preset
  or or_6 (or_6_out, ~Valid5, Hit);  // OR_Gate
  and and_14 (and_14_out, L5, en);
  Counter #(.width(16), .max('hffff), .ongoal("wrap"), .trigger("rising"), .behavior("new")) counter_7 (
    .load(W6), .D({16{1'b0}}), .Q(C6), .clk(CLK), .clr(and_15_out), .down(or_7_out));  // open: count, carry, preset
  or or_7 (or_7_out, ~Valid6, Hit);  // OR_Gate
  and and_15 (and_15_out, L6, en);
  Counter #(.width(16), .max('hffff), .ongoal("wrap"), .trigger("rising"), .behavior("new")) counter_8 (
    .load(W7), .D({16{1'b0}}), .Q(C7), .clk(CLK), .clr(and_16_out), .down(or_8_out));  // open: count, carry, preset
  or or_8 (or_8_out, ~Valid7, Hit);  // OR_Gate
  and and_16 (and_16_out, L7, en);
  Register #(.width(32), .trigger("rising"), .Select("low")) register_17 (
    .D(BranchAddr), .en(and_1_out), .Q(register_17_q), .clk(CLK));  // open: clr
  assign JumpAddress = L0 ? register_17_q : 32'bz;  // Controlled_Buffer controlled_buffer_1
  assign JumpAddress = L1 ? register_18_q : 32'bz;  // Controlled_Buffer controlled_buffer_2
  Register #(.width(32), .trigger("rising"), .Select("low")) register_18 (
    .D(BranchAddr), .en(and_2_out), .Q(register_18_q), .clk(CLK));  // open: clr
  Register #(.width(32), .trigger("rising"), .Select("low")) register_19 (
    .D(BranchAddr), .en(and_3_out), .Q(register_19_q), .clk(CLK));  // open: clr
  assign JumpAddress = L2 ? register_19_q : 32'bz;  // Controlled_Buffer controlled_buffer_3
  assign JumpAddress = L3 ? register_20_q : 32'bz;  // Controlled_Buffer controlled_buffer_4
  Register #(.width(32), .trigger("rising"), .Select("low")) register_20 (
    .D(BranchAddr), .en(and_4_out), .Q(register_20_q), .clk(CLK));  // open: clr
  Register #(.width(32), .trigger("rising"), .Select("low")) register_21 (
    .D(BranchAddr), .en(and_5_out), .Q(register_21_q), .clk(CLK));  // open: clr
  assign JumpAddress = L4 ? register_21_q : 32'bz;  // Controlled_Buffer controlled_buffer_5
  assign JumpAddress = L5 ? register_22_q : 32'bz;  // Controlled_Buffer controlled_buffer_6
  Register #(.width(32), .trigger("rising"), .Select("low")) register_22 (
    .D(BranchAddr), .en(and_6_out), .Q(register_22_q), .clk(CLK));  // open: clr
  Register #(.width(32), .trigger("rising"), .Select("low")) register_23 (
    .D(BranchAddr), .en(and_7_out), .Q(register_23_q), .clk(CLK));  // open: clr
  assign JumpAddress = L6 ? register_23_q : 32'bz;  // Controlled_Buffer controlled_buffer_7
  Register #(.width(32), .trigger("rising"), .Select("low")) register_24 (
    .D(BranchAddr), .en(and_8_out), .Q(register_24_q), .clk(CLK));  // open: clr
  assign JumpAddress = L7 ? register_24_q : 32'bz;  // Controlled_Buffer controlled_buffer_8
  and and_17 (and_17_out, S0, en);
  and and_18 (and_18_out, S1, en);
  and and_19 (and_19_out, S2, en);
  and and_20 (and_20_out, S3, en);
  and and_21 (and_21_out, S4, en);
  and and_22 (and_22_out, S5, en);
  and and_23 (and_23_out, S6, en);
  and and_24 (and_24_out, S7, en);
  or or_9 (or_9_out, and_17_out, and_1_out);
  or or_10 (or_10_out, and_18_out, and_2_out);
  or or_11 (or_11_out, and_19_out, and_3_out);
  or or_12 (or_12_out, and_20_out, and_4_out);
  or or_13 (or_13_out, and_21_out, and_5_out);
  or or_14 (or_14_out, and_22_out, and_6_out);
  or or_15 (or_15_out, and_23_out, and_7_out);
  or or_16 (or_16_out, and_24_out, and_8_out);
  Multiplexer #(.select(1), .width(2), .disabled("Z"), .enable("false")) multiplexer_1 (
    .in0(NewState0), .in1(State0), .out(multiplexer_1_out), .sel(S0));
  Multiplexer #(.select(1), .width(2), .disabled("Z"), .enable("false")) multiplexer_2 (
    .in0(NewState1), .in1(State1), .out(multiplexer_2_out), .sel(S1));
  Multiplexer #(.select(1), .width(2), .disabled("Z"), .enable("false")) multiplexer_3 (
    .in0(NewState2), .in1(State2), .out(multiplexer_3_out), .sel(S2));
  Multiplexer #(.select(1), .width(2), .disabled("Z"), .enable("false")) multiplexer_4 (
    .in0(NewState3), .in1(State3), .out(multiplexer_4_out), .sel(S3));
  Multiplexer #(.select(1), .width(2), .disabled("Z"), .enable("false")) multiplexer_5 (
    .in0(NewState4), .in1(State4), .out(multiplexer_5_out), .sel(S4));
  Multiplexer #(.select(1), .width(2), .disabled("Z"), .enable("false")) multiplexer_6 (
    .in0(NewState5), .in1(State5), .out(multiplexer_6_out), .sel(S5));
  Multiplexer #(.select(1), .width(2), .disabled("Z"), .enable("false")) multiplexer_7 (
    .in0(NewState6), .in1(State6), .out(multiplexer_7_out), .sel(S6));
  Multiplexer #(.select(1), .width(2), .disabled("Z"), .enable("false")) multiplexer_8 (
    .in0(NewState7), .in1(State7), .out(multiplexer_8_out), .sel(S7));
  Register #(.width(2), .trigger("rising"), .Select("low")) register_25 (
    .D(multiplexer_1_out), .en(or_9_out), .Q(register_25_q), .clk(CLK));  // open: clr
  Register #(.width(2), .trigger("rising"), .Select("low")) register_26 (
    .D(multiplexer_2_out), .en(or_10_out), .Q(register_26_q), .clk(CLK));  // open: clr
  Register #(.width(2), .trigger("rising"), .Select("low")) register_27 (
    .D(multiplexer_3_out), .en(or_11_out), .Q(register_27_q), .clk(CLK));  // open: clr
  Register #(.width(2), .trigger("rising"), .Select("low")) register_28 (
    .D(multiplexer_4_out), .en(or_12_out), .Q(register_28_q), .clk(CLK));  // open: clr
  Register #(.width(2), .trigger("rising"), .Select("low")) register_29 (
    .D(multiplexer_5_out), .en(or_13_out), .Q(register_29_q), .clk(CLK));  // open: clr
  Register #(.width(2), .trigger("rising"), .Select("low")) register_30 (
    .D(multiplexer_6_out), .en(or_14_out), .Q(register_30_q), .clk(CLK));  // open: clr
  Register #(.width(2), .trigger("rising"), .Select("low")) register_31 (
    .D(multiplexer_7_out), .en(or_15_out), .Q(register_31_q), .clk(CLK));  // open: clr
  Register #(.width(2), .trigger("rising"), .Select("low")) register_32 (
    .D(multiplexer_8_out), .en(or_16_out), .Q(register_32_q), .clk(CLK));  // open: clr
  assign PredictJump = L0 ? register_25_q : 2'bz;  // Controlled_Buffer controlled_buffer_9
  assign EX_PredictJump = E0 ? register_25_q : 2'bz;  // Controlled_Buffer controlled_buffer_10
  assign PredictJump = L1 ? register_26_q : 2'bz;  // Controlled_Buffer controlled_buffer_11
  assign EX_PredictJump = E1 ? register_26_q : 2'bz;  // Controlled_Buffer controlled_buffer_12
  assign PredictJump = L2 ? register_27_q : 2'bz;  // Controlled_Buffer controlled_buffer_13
  assign EX_PredictJump = E2 ? register_27_q : 2'bz;  // Controlled_Buffer controlled_buffer_14
  assign PredictJump = L3 ? register_28_q : 2'bz;  // Controlled_Buffer controlled_buffer_15
  assign EX_PredictJump = E3 ? register_28_q : 2'bz;  // Controlled_Buffer controlled_buffer_16
  assign PredictJump = L4 ? register_29_q : 2'bz;  // Controlled_Buffer controlled_buffer_17
  assign EX_PredictJump = E4 ? register_29_q : 2'bz;  // Controlled_Buffer controlled_buffer_18
  assign PredictJump = L5 ? register_30_q : 2'bz;  // Controlled_Buffer controlled_buffer_19
  assign EX_PredictJump = E5 ? register_30_q : 2'bz;  // Controlled_Buffer controlled_buffer_20
  assign PredictJump = L6 ? register_31_q : 2'bz;  // Controlled_Buffer controlled_buffer_21
  assign EX_PredictJump = E6 ? register_31_q : 2'bz;  // Controlled_Buffer controlled_buffer_22
  assign PredictJump = L7 ? register_32_q : 2'bz;  // Controlled_Buffer controlled_buffer_23
  assign EX_PredictJump = E7 ? register_32_q : 2'bz;  // Controlled_Buffer controlled_buffer_24
  MAX2x16 max2x16_1 (.X(C0), .Y(C1), .X_id(3'b000), .Y_id(3'b001), .MAX(max2x16_1_max), .MAX_id(max2x16_1_max_id));
  MAX2x16 max2x16_2 (.X(C2), .Y(C3), .X_id(3'b010), .Y_id(3'b011), .MAX(max2x16_2_max), .MAX_id(max2x16_2_max_id));
  MAX2x16 max2x16_3 (.X(C4), .Y(C5), .X_id(3'b100), .Y_id(3'b101), .MAX(max2x16_3_max), .MAX_id(max2x16_3_max_id));
  MAX2x16 max2x16_4 (.X(C6), .Y(C7), .X_id(3'b110), .Y_id(3'b111), .MAX(max2x16_4_max), .MAX_id(max2x16_4_max_id));
  not not_1 (not_1_out, priority_encoder_1_en_out);
  Priority_Encoder #(.select(3), .disabled("Z")) priority_encoder_1 (
    .in0(E0), .in1(E1), .in2(E2), .in3(E3), .in4(E4), .in5(E5), .in6(E6), .in7(E7),
    .out(priority_encoder_1_out), .en_out(priority_encoder_1_en_out), .en_in(1'b1));  // open: gs
  Comparator #(.width(32), .mode("unsigned")) comparator_1 (.a(PC), .b(Tag0), .eq(comparator_1_eq));  // open: gt, lt
  Comparator #(.width(32), .mode("unsigned")) comparator_2 (.a(PC), .b(Tag1), .eq(comparator_2_eq));  // open: gt, lt
  Comparator #(.width(32), .mode("unsigned")) comparator_3 (.a(PC), .b(Tag2), .eq(comparator_3_eq));  // open: gt, lt
  Comparator #(.width(32), .mode("unsigned")) comparator_4 (.a(PC), .b(Tag3), .eq(comparator_4_eq));  // open: gt, lt
  Comparator #(.width(32), .mode("unsigned")) comparator_5 (.a(PC), .b(Tag4), .eq(comparator_5_eq));  // open: gt, lt
  Comparator #(.width(32), .mode("unsigned")) comparator_6 (.a(PC), .b(Tag5), .eq(comparator_6_eq));  // open: gt, lt
  Comparator #(.width(32), .mode("unsigned")) comparator_7 (.a(PC), .b(Tag6), .eq(comparator_7_eq));  // open: gt, lt
  Comparator #(.width(32), .mode("unsigned")) comparator_8 (.a(PC), .b(Tag7), .eq(comparator_8_eq));  // open: gt, lt
  Comparator #(.width(32), .mode("unsigned")) comparator_9 (.a(EX_PC), .b(Tag0), .eq(comparator_9_eq));  // open: gt, lt
  Comparator #(.width(32), .mode("unsigned")) comparator_10 (
    .a(EX_PC), .b(Tag1), .eq(comparator_10_eq));  // open: gt, lt
  Comparator #(.width(32), .mode("unsigned")) comparator_11 (
    .a(EX_PC), .b(Tag2), .eq(comparator_11_eq));  // open: gt, lt
  Comparator #(.width(32), .mode("unsigned")) comparator_12 (
    .a(EX_PC), .b(Tag3), .eq(comparator_12_eq));  // open: gt, lt
  Comparator #(.width(32), .mode("unsigned")) comparator_13 (
    .a(EX_PC), .b(Tag4), .eq(comparator_13_eq));  // open: gt, lt
  Comparator #(.width(32), .mode("unsigned")) comparator_14 (
    .a(EX_PC), .b(Tag5), .eq(comparator_14_eq));  // open: gt, lt
  Comparator #(.width(32), .mode("unsigned")) comparator_15 (
    .a(EX_PC), .b(Tag6), .eq(comparator_15_eq));  // open: gt, lt
  Comparator #(.width(32), .mode("unsigned")) comparator_16 (
    .a(EX_PC), .b(Tag7), .eq(comparator_16_eq));  // open: gt, lt
  MAX2x16 max2x16_5 (
    .X(max2x16_1_max), .Y(max2x16_2_max), .X_id(max2x16_1_max_id), .Y_id(max2x16_2_max_id),
    .MAX(max2x16_5_max), .MAX_id(max2x16_5_max_id));
  MAX2x16 max2x16_6 (
    .X(max2x16_3_max), .Y(max2x16_4_max), .X_id(max2x16_3_max_id), .Y_id(max2x16_4_max_id),
    .MAX(max2x16_6_max), .MAX_id(max2x16_6_max_id));
  and and_25 (L0, comparator_1_eq, Valid0);
  and and_26 (L1, comparator_2_eq, Valid1);
  and and_27 (L2, comparator_3_eq, Valid2);
  and and_28 (L3, comparator_4_eq, Valid3);
  and and_29 (L4, comparator_5_eq, Valid4);
  and and_30 (L5, comparator_6_eq, Valid5);
  and and_31 (L6, comparator_7_eq, Valid6);
  and and_32 (L7, comparator_8_eq, Valid7);
  and and_33 (E0, comparator_9_eq, Valid0);
  and and_34 (E1, comparator_10_eq, Valid1);
  and and_35 (E2, comparator_11_eq, Valid2);
  and and_36 (E3, comparator_12_eq, Valid3);
  and and_37 (E4, comparator_13_eq, Valid4);
  and and_38 (E5, comparator_14_eq, Valid5);
  and and_39 (E6, comparator_15_eq, Valid6);
  and and_40 (E7, comparator_16_eq, Valid7);
  MAX2x16 max2x16_7 (
    .X(max2x16_5_max), .Y(max2x16_6_max), .X_id(max2x16_5_max_id), .Y_id(max2x16_6_max_id),
    .MAX_id(max2x16_7_max_id));  // open: MAX
  and and_41 (and_41_out, EX_Hit, en, StateReady);
  and and_42 (and_42_out, Miss, en, PCReady);
  Demultiplexer #(.select(3), .width(1), .tristate("false"), .disabled(0), .enable("true")) demultiplexer_1 (
    .out0(S0), .out1(S1), .out2(S2), .out3(S3), .out4(S4), .out5(S5), .out6(S6), .out7(S7), .in(and_41_out),
    .sel(priority_encoder_1_out), .en(not_1_out));
  or or_17 (Hit, L0, L1, L2, L3, L4, L5, L6, L7);
  not not_2 (Miss, Hit);
  or or_18 (EX_Hit, E0, E1, E2, E3, E4, E5, E6, E7);
  not not_3 (EX_Miss, EX_Hit);
  Demultiplexer #(.select(3), .width(1), .tristate("false"), .disabled("Z"), .enable("false")) demultiplexer_2 (
    .out0(W0), .out1(W1), .out2(W2), .out3(W3), .out4(W4), .out5(W5), .out6(W6), .out7(W7), .in(and_42_out),
    .sel(max2x16_7_max_id));
  Demultiplexer #(.select(3), .width(2), .tristate("false"), .disabled("Z"), .enable("false")) demultiplexer_3 (
    .out0(NewState0), .out1(NewState1), .out2(NewState2), .out3(NewState3), .out4(NewState4),
    .out5(NewState5), .out6(NewState6), .out7(NewState7), .in(NewJumpState), .sel(max2x16_7_max_id));
  Demultiplexer #(.select(3), .width(2), .tristate("false"), .disabled(0), .enable("true")) demultiplexer_4 (
    .out0(State0), .out1(State1), .out2(State2), .out3(State3), .out4(State4), .out5(State5), .out6(State6),
    .out7(State7), .in(JumpState), .sel(priority_encoder_1_out), .en(not_1_out));

  // Other names for the same wires on the sheet: JumpAddr[31:0] = JumpAddress; NewState[1:0] = NewJumpState;
  //   State[1:0] = JumpState
endmodule

module MAX2x16 (
  input  [15:0] X,
  input  [15:0] Y,
  input  [2:0] X_id,
  input  [2:0] Y_id,
  output [15:0] MAX,
  output [2:0] MAX_id
);

  wire comparator_1_eq, comparator_1_gt, not_1_out, or_1_out;

  Comparator #(.width(16), .mode("unsigned")) comparator_1 (
    .a(X), .b(Y), .gt(comparator_1_gt), .eq(comparator_1_eq));  // open: lt
  or or_1 (or_1_out, comparator_1_gt, comparator_1_eq);
  not not_1 (not_1_out, or_1_out);
  Multiplexer #(.select(1), .width(16), .disabled("Z"), .enable("false")) multiplexer_1 (
    .in0(X), .in1(Y), .out(MAX), .sel(not_1_out));
  Multiplexer #(.select(1), .width(3), .disabled("Z"), .enable("false")) multiplexer_2 (
    .in0(X_id), .in1(Y_id), .out(MAX_id), .sel(not_1_out));
endmodule

module BHT (
  input  X1,
  input  X0,
  input  JumpSuccess,
  output Y1,
  output Y0
);

  wire and_1_out, and_2_out, and_3_out, and_4_out, not_1_out, not_2_out, not_3_out, not_4_out, not_5_out;

  not not_1 (not_1_out, X0);
  not not_2 (not_2_out, X1);
  not not_3 (not_3_out, X0);
  not not_4 (not_4_out, X0);
  not not_5 (not_5_out, JumpSuccess);
  and and_1 (and_1_out, X0, JumpSuccess);
  and and_2 (and_2_out, X1, not_1_out);
  and and_3 (and_3_out, not_2_out, not_3_out, JumpSuccess);
  and and_4 (and_4_out, X1, not_4_out, not_5_out);
  or or_1 (Y1, and_1_out, and_2_out);
  or or_2 (Y0, and_3_out, and_4_out);
endmodule

module \分支超前  (
  input  [31:0] PC,
  input  [31:0] IR,
  output J,
  output B,
  output [31:0] B_Addr,
  output [31:0] J_Addr
);

  wire BGEU, or_1_out, \单周期硬布线控制器_1_beq , \单周期硬布线控制器_1_bne , \单周期硬布线控制器_1_jal , \单周期硬布线控制器_1_jalr ;
  wire [11:0] shifter_1_out;
  wire [19:0] shifter_2_out;
  wire [31:0] bit_extender_1_out, bit_extender_2_out;

  and and_1 (J, \单周期硬布线控制器_1_jal , ~\单周期硬布线控制器_1_jalr );  // AND_Gate
  \单周期硬布线控制器  \u_单周期硬布线控制器_1  (
    .OP(IR[6:2]), .Funct({IR[30], IR[25], IR[14:12]}), .Beq(\单周期硬布线控制器_1_beq ), .Bne(\单周期硬布线控制器_1_bne ),
    .Jalr(\单周期硬布线控制器_1_jalr ), .JAL(\单周期硬布线控制器_1_jal ), .blt(BGEU));  // open: ALU_OP, in_3, uret, MemToReg, ecall, MemWrite, ALU_SRC, RegWrite, S_type, csrrsi, dasb, U_type, csrrci
  Shifter #(.width(12), .shift("ll")) shifter_1 (
    .in({IR[31], IR[7], IR[30:25], IR[11:8]}), .\dist (4'b0001), .out(shifter_1_out));
  Shifter #(.width(20), .shift("ll")) shifter_2 (
    .in({IR[31], IR[19:12], IR[20], IR[30:21]}), .\dist (5'b00001), .out(shifter_2_out));
  or or_1 (or_1_out, \单周期硬布线控制器_1_beq , \单周期硬布线控制器_1_bne );
  or or_2 (B, or_1_out, BGEU);
  assign bit_extender_1_out = {{20{shifter_1_out[11]}}, shifter_1_out};  // Bit_Extender bit_extender_1
  assign bit_extender_2_out = {{12{shifter_2_out[19]}}, shifter_2_out};  // Bit_Extender bit_extender_2
  Adder #(.width(32)) adder_1 (.a(bit_extender_2_out), .b(PC), .out(J_Addr));  // open: cin, cout
  Adder #(.width(32)) adder_2 (.a(bit_extender_1_out), .b(PC), .out(B_Addr));  // open: cin, cout
endmodule

module \分支预测  (
  input  CLK,
  input  EX_Jalr,
  input  [31:0] PC,
  input  [31:0] EX_PC,
  input  [31:0] EX_jalrAddr,
  input  en,
  input  EX_GuessJ,
  input  [31:0] PC_4,
  input  [31:0] EX_PC_4,
  input  [31:0] EX_JumpAddr,
  input  EX_BranchTaken,
  input  EX_Branch,
  input  [31:0] IR,
  output [31:0] PCout,
  output GuessJ,
  output Ex_PredictErr
);

  wire and_3_out, and_4_out, and_5_out, and_6_out, and_7_out, and_8_out, and_9_out, B, EX_Hit, Hit, J, Miss,
       multiplexer_3_out, or_1_out, or_2_out, or_3_out, or_4_out, or_7_out;
  wire [1:0] and_1_out, bht_1_y0, EX_PredictJump, PredictJump;
  wire [31:0] multiplexer_1_out, multiplexer_4_out, multiplexer_5_out, multiplexer_6_out, multiplexer_7_out,
       PredictAddr, PredictToPC, \分支超前_1_b_addr , \分支超前_1_j_addr ;

  \分支超前  \u_分支超前_1  (.PC(PC), .IR(IR), .J(J), .B(B), .B_Addr(\分支超前_1_b_addr ), .J_Addr(\分支超前_1_j_addr ));
  Multiplexer #(.select(1), .width(32), .disabled("Z"), .enable("false")) multiplexer_1 (
    .in0(PC_4), .in1(\分支超前_1_b_addr ), .out(multiplexer_1_out), .sel(B));
  Multiplexer #(.select(1), .width(32), .disabled("Z"), .enable("false")) multiplexer_2 (
    .in0(multiplexer_1_out), .in1(\分支超前_1_j_addr ), .out(PredictAddr), .sel(J));
  or or_1 (or_1_out, J, B);
  or or_2 (or_2_out, B, J);
  and and_1 (and_1_out[0], or_1_out, Miss);
  and and_2 (and_1_out[1], Miss, or_2_out);
  or or_3 (or_3_out, B, J);
  BHT bht_1 (
    .X1(EX_PredictJump[1]), .X0(EX_PredictJump[0]), .JumpSuccess(EX_BranchTaken), .Y1(bht_1_y0[1]),
    .Y0(bht_1_y0[0]));
  or or_4 (or_4_out, B, J);
  and and_3 (and_3_out, or_3_out, Miss);
  Multiplexer #(.select(1), .width(1), .disabled("Z"), .enable("false")) multiplexer_3 (
    .in0(1'b0), .in1(PredictJump[1]), .out(multiplexer_3_out), .sel(Hit));
  and and_4 (and_4_out, or_4_out, Miss);
  or or_5 (GuessJ, multiplexer_3_out, and_4_out);
  BTB btb_1 (
    .EX_PC(EX_PC), .NewJumpState(and_1_out), .JumpState(bht_1_y0), .PC(PC), .BranchAddr(PredictAddr),
    .CLK(CLK), .en(en), .PCReady(and_3_out), .StateReady(EX_Branch), .PredictJump(PredictJump),
    .EX_PredictJump(EX_PredictJump), .JumpAddress(PredictToPC), .Hit(Hit), .EX_Hit(EX_Hit), .Miss(Miss));
  and and_5 (and_5_out, EX_GuessJ, ~EX_BranchTaken);  // AND_Gate
  or or_6 (Ex_PredictErr, and_5_out, and_6_out);
  and and_6 (and_6_out, EX_BranchTaken, ~EX_GuessJ);  // AND_Gate
  or or_7 (or_7_out, B, J);
  and and_7 (and_7_out, or_7_out, Miss);
  Multiplexer #(.select(1), .width(32), .disabled("Z"), .enable("false")) multiplexer_4 (
    .in0(PC_4), .in1(PredictAddr), .out(multiplexer_4_out), .sel(and_7_out));
  and and_8 (and_8_out, Hit, GuessJ);
  Multiplexer #(.select(1), .width(32), .disabled("Z"), .enable("false")) multiplexer_5 (
    .in0(multiplexer_4_out), .in1(PredictToPC), .out(multiplexer_5_out), .sel(and_8_out));
  Multiplexer #(.select(1), .width(32), .disabled("Z"), .enable("false")) multiplexer_6 (
    .in0(EX_JumpAddr), .in1(EX_PC_4), .out(multiplexer_6_out), .sel(and_9_out));
  and and_9 (and_9_out, EX_GuessJ, ~EX_BranchTaken);  // AND_Gate
  Multiplexer #(.select(1), .width(32), .disabled("Z"), .enable("false")) multiplexer_7 (
    .in0(multiplexer_5_out), .in1(multiplexer_6_out), .out(multiplexer_7_out), .sel(Ex_PredictErr));
  Multiplexer #(.select(1), .width(32), .disabled("Z"), .enable("false")) multiplexer_8 (
    .in0(multiplexer_7_out), .in1(EX_jalrAddr), .out(PCout), .sel(EX_Jalr));
endmodule
